// Digital circuit master loop version Z 19 feb 2022.dig as structural Verilog
module master_loop_version_Z_19_feb_2022 (
  input  FAST,
  input  LOAD__goes_low,
  input  SLOW,
  input  OP_1_disable,
  input  display_ripple_clock,
  input  BUS_PIN__15__IN__HI_TO_PAUSE,
  input  in_22,
  output BUS_PIN__1__OUT__3_A,
  output BUS_PIN__2__OUT__3_B,
  output BUS_PIN__3__OUT__3_C,
  output BUS_PIN__4__OUT__3_D,
  output BUS_PIN__5__OUT__2_A,
  output BUS_PIN__6__OUT__2_B,
  output BUS_PIN__7__OUT__2_C,
  output BUS_PIN__8__OUT__2_D,
  output BUS_PIN__9__OUT__1_A,
  output BUS_PIN__10__OUT__1_B,
  output BUS_PIN__11__OUT__1_C,
  output BUS_PIN__12__OUT__1_D,
  output BUS_PIN__13__OUT__ripple_display,
  output BUS_PIN__14__OUT__low_whilst_reset,
  output BUS_PIN__16__GND,
  output out_23
);

  wire _3_x_10_bit_multiply_version_e_19_feb_2022_1_p0, _3_x_10_bit_multiply_version_e_19_feb_2022_1_p1,
       _3_x_10_bit_multiply_version_e_19_feb_2022_1_p2, _3_x_10_bit_multiply_version_e_19_feb_2022_1_p3,
       _3_x_10_bit_multiply_version_e_19_feb_2022_1_p4, _3_x_10_bit_multiply_version_e_19_feb_2022_1_p5,
       _3_x_10_bit_multiply_version_e_19_feb_2022_1_p6, _3_x_10_bit_multiply_version_e_19_feb_2022_1_p7,
       _3_x_10_bit_multiply_version_e_19_feb_2022_1_p8, _3_x_10_bit_multiply_version_e_19_feb_2022_1_p9,
       _3_x_10_bit_multiply_version_e_19_feb_2022_1_p10, _3_x_10_bit_multiply_version_e_19_feb_2022_1_p11,
       _4_7_pin7, _4_7_pin9, _8_11_pin9, _7400_1_pin2, _7400_1_pin5, _7400_1_pin9, _7400_1_pin12,
       _7400_2_pin9, _7400_2_pin10, _7400_3_pin2, _7400_3_pin3, _7400_3_pin6, _7400_3_pin11, _7400_4_pin3,
       _7400_4_pin8, _7400_4_pin9, _7400_5_pin12, _7400_6_pin6, _7400_6_pin8, _7400_6_pin11, _7400_7_pin8,
       _7400_7_pin12, _7404_1_pin1, _7404_1_pin2, _7404_1_pin3, _7404_1_pin5, _7404_1_pin9, _7404_1_pin11,
       _7404_1_pin13, _7404_2_pin1, _7404_2_pin3, _7404_2_pin5, _7404_2_pin9, _7404_2_pin11, _7404_2_pin13,
       _7404_3_pin2, _7404_3_pin4, _7404_3_pin6, _7404_3_pin8, _7404_3_pin10, _7404_3_pin12, _7404_4_pin11,
       _7404_4_pin12, _7404_5_pin8, _7404_6_pin5, _7404_7_pin12, _7404_8_pin2, _7404_8_pin4, _7404_8_pin6,
       _7404_8_pin8, _7404_8_pin10, _7404_8_pin12, _7404_9_pin2, _7404_10_pin9, _7404_11_pin2, _7404_11_pin4,
       _7404_11_pin6, _7404_11_pin8, _7404_11_pin10, _7404_11_pin12, _7404_12_pin2, _7404_12_pin4,
       _7404_12_pin6, _7404_12_pin8, _7404_12_pin10, _7404_12_pin12, _7404_13_pin2, _7404_13_pin4,
       _7404_13_pin8, _7404_13_pin10, _7407_1_pin1, _7407_1_pin2, _7407_1_pin3, _7407_1_pin4, _7407_1_pin5,
       _7407_1_pin6, _7407_1_pin8, _7407_1_pin9, _7407_1_pin10, _7407_1_pin11, _7407_1_pin12, _7407_1_pin13,
       _7408_1_pin3, _7408_1_pin6, _7408_1_pin8, _7408_1_pin11, _7408_2_pin11, _7408_3_pin13, _7408_4_pin3,
       _7408_4_pin8, _7408_4_pin11, _7408_5_pin3, _7408_6_pin11, _7408_7_pin3, _7408_7_pin6, _7408_7_pin11,
       _7408_8_pin3, _7408_10_pin3, _7408_10_pin6, _7408_10_pin8, _7408_10_pin11, _7408_12_pin6,
       _7408_12_pin11, _7408_12_pin12, _7408_13_pin8, _7408_13_pin11, _7408_14_pin3, _7408_14_pin6,
       _7408_14_pin8, _7408_14_pin11, _7408_15_pin3, _7408_15_pin6, _7408_15_pin8, _7408_15_pin11,
       _7408_16_pin3, _7408_16_pin6, _7408_16_pin8, _7408_16_pin11, _7410_1_pin1, _7410_1_pin8, _7410_2_pin4,
       _7410_2_pin6, _7410_2_pin8, _7410_2_pin10, _7411_1_pin6, _7411_1_pin8, _7411_1_pin11, _7411_2_pin2,
       _7411_2_pin8, _7411_2_pin12, _7411_3_pin2, _7411_3_pin9, _7411_3_pin10, _7411_3_pin11, _7411_4_pin6,
       _7411_4_pin11, _7411_6_pin6, _7411_6_pin8, _7411_6_pin11, _7411_7_pin2, _7411_7_pin8, _7411_7_pin12,
       _7420_1_pin6, _7420_1_pin10, _7420_1_pin12, _7420_1_pin13, _7427_1_pin1, _7427_1_pin2, _7427_1_pin3,
       _7427_1_pin4, _7427_1_pin6, _7427_1_pin8, _7427_1_pin9, _7427_1_pin10, _7427_1_pin12, _7427_2_pin1,
       _7427_2_pin3, _7427_2_pin8, _7427_2_pin13, _7427_3_pin5, _7427_3_pin6, _7427_3_pin8, _7427_3_pin11,
       _7427_3_pin12, _7427_3_pin13, _7427_4_pin5, _7432_1_pin6, _7432_1_pin8, _7432_2_pin3, _7432_2_pin6,
       _7432_2_pin8, _7432_2_pin11, _7432_3_pin3, _7432_3_pin8, _7432_3_pin10, _7432_4_pin3, _7432_4_pin6,
       _7432_4_pin8, _7474_2_pin10, _7474_2_pin12, _7474_2_pin13, _7485_1_pin6, _7485_1_pin11, _74138_1_pin9,
       _74138_1_pin10, _74138_1_pin11, _74138_1_pin12, _74138_1_pin13, _74138_1_pin14, _74154_1_pin14,
       _74154_1_pin15, _74154_1_pin16, _74154_1_pin17, _74154_2_pin2, _74154_2_pin3, _74154_2_pin4,
       _74154_2_pin5, _74154_2_pin6, _74154_2_pin7, _74154_2_pin8, _74154_2_pin9, _74160_1_pin7,
       _74160_1_pin10, _74160_2_pin7, _74160_2_pin10, _74160_3_pin7, _74160_3_pin10, _74160_4_pin7,
       _74161_1_pin7, _74161_1_pin10, _74161_1_pin11, _74161_1_pin12, _74161_1_pin13, _74161_1_pin14,
       _74161_2_pin9, _74161_2_pin11, _74161_2_pin12, _74161_2_pin13, _74161_2_pin14, _74161_3_pin7,
       _74161_3_pin9, _74161_4_pin7, _74161_4_pin9, _74161_5_pin7, _74161_5_pin9, _74161_6_pin9,
       _74161_7_pin7, _74161_7_pin9, _74161_7_pin12, _74161_7_pin13, _74161_7_pin14, _74161_8_pin3,
       _74161_8_pin9, _74161_8_pin12, _74161_8_pin13, _74173_1_pin3, _74173_1_pin7, _74173_1_pin9,
       _74173_1_pin14, _74173_1_pin15, _74173_2_pin14, _74173_2_pin15, _74181_2_pin7, _74181_3_pin7,
       _74181_6_pin7, _74181_7_pin7, _74182_1_pin1, _74182_1_pin2, _74182_1_pin3, _74182_1_pin4,
       _74182_1_pin5, _74182_1_pin6, _74182_1_pin7, _74182_1_pin9, _74182_1_pin10, _74182_1_pin14,
       _74182_1_pin15, _74182_2_pin1, _74182_2_pin2, _74182_2_pin3, _74182_2_pin4, _74182_2_pin7,
       _74182_2_pin9, _74182_2_pin10, _74182_2_pin14, _74182_2_pin15, _74191_1_pin1, _74191_1_pin5,
       _74191_1_pin9, _74191_1_pin10, _74191_1_pin11, _74191_1_pin13, _74191_1_pin15, _74191_2_pin1,
       _74191_2_pin5, _74191_2_pin9, _74191_2_pin10, _74191_2_pin13, _74191_2_pin15, _74191_3_pin1,
       _74191_3_pin5, _74191_3_pin15, _74245_7_pin2, _74245_7_pin3, _74245_7_pin4, _74245_7_pin5,
       _74245_7_pin6, _74245_7_pin7, _74245_7_pin8, _74245_7_pin9, _74245_7_pin19, _74245_8_pin2,
       _74245_8_pin3, _74245_8_pin4, _74245_11_pin11, _74245_11_pin12, _74245_11_pin13, _74245_11_pin14,
       _74245_11_pin15, _74245_11_pin16, _74245_11_pin17, _74245_11_pin18, _74245_11_pin19, _74245_12_pin11,
       _74245_12_pin12, _74245_12_pin13, _74245_12_pin14, _74245_12_pin15, _74245_12_pin16, _74245_12_pin17,
       _74245_12_pin18, _74245_13_pin19, _74245_15_pin19, _74247_1_pin1, _74247_1_pin2, _74247_1_pin3,
       _74247_1_pin6, _74247_1_pin7, _74247_1_pin9, _74247_1_pin10, _74247_1_pin11, _74247_1_pin12,
       _74247_1_pin13, _74247_1_pin14, _74247_1_pin15, _74247_2_pin1, _74247_2_pin2, _74247_2_pin6,
       _74247_2_pin7, _74247_2_pin9, _74247_2_pin10, _74247_2_pin11, _74247_2_pin12, _74247_2_pin13,
       _74247_2_pin14, _74247_2_pin15, _74247_3_pin1, _74247_3_pin2, _74247_3_pin3, _74247_3_pin6,
       _74247_3_pin7, _74247_3_pin9, _74247_3_pin10, _74247_3_pin11, _74247_3_pin12, _74247_3_pin13,
       _74247_3_pin14, _74247_3_pin15, _74247_4_pin1, _74247_4_pin2, _74247_4_pin3, _74247_4_pin6,
       _74247_4_pin7, _74247_4_pin9, _74247_4_pin10, _74247_4_pin11, _74247_4_pin12, _74247_4_pin13,
       _74247_4_pin14, _74247_4_pin15, _74247_5_pin1, _74247_5_pin2, _74247_5_pin3, _74247_5_pin6,
       _74247_5_pin7, _74247_5_pin9, _74247_5_pin10, _74247_5_pin11, _74247_5_pin12, _74247_5_pin13,
       _74247_5_pin14, _74247_5_pin15, _74247_6_pin1, _74247_6_pin2, _74247_6_pin3, _74247_6_pin6,
       _74247_6_pin7, _74247_6_pin9, _74247_6_pin10, _74247_6_pin11, _74247_6_pin12, _74247_6_pin13,
       _74247_6_pin14, _74247_6_pin15, _74247_7_pin1, _74247_7_pin2, _74247_7_pin3, _74247_7_pin6,
       _74247_7_pin7, _74247_7_pin9, _74247_7_pin10, _74247_7_pin11, _74247_7_pin12, _74247_7_pin13,
       _74247_7_pin14, _74247_7_pin15, _74247_8_pin1, _74247_8_pin2, _74247_8_pin3, _74247_8_pin6,
       _74247_8_pin7, _74247_8_pin9, _74247_8_pin10, _74247_8_pin11, _74247_8_pin12, _74247_8_pin13,
       _74247_8_pin14, _74247_8_pin15, _74247_9_pin1, _74247_9_pin2, _74247_9_pin3, _74247_9_pin6,
       _74247_9_pin7, _74247_9_pin9, _74247_9_pin10, _74247_9_pin11, _74247_9_pin12, _74247_9_pin13,
       _74247_9_pin14, _74247_9_pin15, _74247_10_pin1, _74247_10_pin2, _74247_10_pin3, _74247_10_pin6,
       _74247_10_pin7, _74247_10_pin9, _74247_10_pin10, _74247_10_pin11, _74247_10_pin12, _74247_10_pin13,
       _74247_10_pin14, _74247_10_pin15, _74247_11_pin1, _74247_11_pin2, _74247_11_pin3, _74247_11_pin6,
       _74247_11_pin7, _74247_11_pin9, _74247_11_pin10, _74247_11_pin11, _74247_11_pin12, _74247_11_pin13,
       _74247_11_pin14, _74247_11_pin15, _74247_12_pin1, _74247_12_pin2, _74247_12_pin3, _74247_12_pin6,
       _74247_12_pin7, _74247_12_pin9, _74247_12_pin10, _74247_12_pin11, _74247_12_pin12, _74247_12_pin13,
       _74247_12_pin14, _74247_12_pin15, _74247_13_pin1, _74247_13_pin2, _74247_13_pin3, _74247_13_pin6,
       _74247_13_pin7, _74247_13_pin9, _74247_13_pin10, _74247_13_pin11, _74247_13_pin12, _74247_13_pin13,
       _74247_13_pin14, _74247_13_pin15, _74247_14_pin1, _74247_14_pin2, _74247_14_pin3, _74247_14_pin6,
       _74247_14_pin7, _74247_14_pin9, _74247_14_pin10, _74247_14_pin11, _74247_14_pin12, _74247_14_pin13,
       _74247_14_pin14, _74247_14_pin15, _74247_15_pin1, _74247_15_pin2, _74247_15_pin3, _74247_15_pin6,
       _74247_15_pin7, _74247_15_pin9, _74247_15_pin10, _74247_15_pin11, _74247_15_pin12, _74247_15_pin13,
       _74247_15_pin14, _74247_15_pin15, _74247_16_pin1, _74247_16_pin2, _74247_16_pin3, _74247_16_pin6,
       _74247_16_pin7, _74247_16_pin9, _74247_16_pin10, _74247_16_pin11, _74247_16_pin12, _74247_16_pin13,
       _74247_16_pin14, _74247_16_pin15, _74247_17_pin1, _74247_17_pin2, _74247_17_pin3, _74247_17_pin6,
       _74247_17_pin7, _74247_17_pin9, _74247_17_pin10, _74247_17_pin11, _74247_17_pin12, _74247_17_pin13,
       _74247_17_pin14, _74247_17_pin15, _74247_18_pin1, _74247_18_pin2, _74247_18_pin3, _74247_18_pin6,
       _74247_18_pin7, _74247_18_pin9, _74247_18_pin10, _74247_18_pin11, _74247_18_pin12, _74247_18_pin13,
       _74247_18_pin14, _74247_18_pin15, _74247_19_pin1, _74247_19_pin2, _74247_19_pin3, _74247_19_pin6,
       _74247_19_pin7, _74247_19_pin9, _74247_19_pin10, _74247_19_pin11, _74247_19_pin12, _74247_19_pin13,
       _74247_19_pin14, _74247_19_pin15, _74247_20_pin1, _74247_20_pin2, _74247_20_pin3, _74247_20_pin6,
       _74247_20_pin7, _74247_20_pin9, _74247_20_pin10, _74247_20_pin11, _74247_20_pin12, _74247_20_pin13,
       _74247_20_pin14, _74247_20_pin15, _74247_21_pin1, _74247_21_pin2, _74247_21_pin3, _74247_21_pin6,
       _74247_21_pin7, _74247_21_pin9, _74247_21_pin10, _74247_21_pin11, _74247_21_pin12, _74247_21_pin13,
       _74247_21_pin14, _74247_21_pin15, _74247_22_pin1, _74247_22_pin2, _74247_22_pin3, _74247_22_pin6,
       _74247_22_pin7, _74247_22_pin9, _74247_22_pin10, _74247_22_pin11, _74247_22_pin12, _74247_22_pin13,
       _74247_22_pin14, _74247_22_pin15, _74260_1_pin4, _74260_1_pin6, _74283_1_pin1, _74283_1_pin4,
       _74283_1_pin10, _74283_1_pin13, _74367_1_y1, _74367_1_y2, _74367_1_y3, _74541_1_pin2, _74541_1_pin3,
       _74541_1_pin7, _74541_1_pin8, _74541_1_pin9, _74541_1_pin11, _74541_1_pin12, _74541_1_pin13,
       _74541_1_pin14, _74541_1_pin15, _74541_1_pin16, _74541_1_pin17, _74541_1_pin18, _74541_2_pin11,
       _74541_2_pin12, _74541_2_pin13, _74541_2_pin14, _74541_2_pin15, _74541_2_pin16, _74541_2_pin17,
       _74541_2_pin18, _74541_3_pin14, _74541_3_pin15, _74541_3_pin16, _74541_3_pin17, _74541_3_pin18,
       _74541_4_pin11, _74541_4_pin12, _74541_4_pin13, _74541_4_pin14, _74541_4_pin15, _74541_4_pin16,
       _74541_4_pin17, _74541_5_pin11, _74541_5_pin12, _74541_5_pin13, _74541_5_pin14, _74541_5_pin15,
       _74541_5_pin16, _74541_5_pin17, _74541_5_pin18, _74541_6_pin11, _74541_6_pin12, _74541_6_pin13,
       _74541_6_pin14, _74541_6_pin15, _74541_6_pin16, _74541_6_pin17, _74541_6_pin18, _74541_7_pin16,
       _74541_7_pin17, _74541_7_pin18, _74541_8_pin2, _74541_8_pin8, _74541_8_pin9, _74541_8_pin11,
       _74541_8_pin12, _74541_8_pin15, _74541_8_pin16, _74541_8_pin17, _74541_8_pin18, _74541_9_pin17,
       _74541_9_pin18, A1, A2, A3, A4, A5, A6, A7, A8, A9, A10, A11, A12, A13, A14, A15, B1, B2, B3, B4, B5,
       B6, B7, B9, B10, B11, B12, B13, B14, B15, B16, C3, C4, C5, C6, C7, C8, C9, C10, C11, C12, C13, C14,
       C15, C16, C17, C18, C19, C20, C21, C22, C23, C24, Cn__a_b____10_out, Cn__BETA_out, Cn_out, D1, D2, D3,
       D4, D5, D6, D7, D8, D9, D10, D11, D12, D13, D14, D15, D16, D17, D18, D19, D21, D22, debounce__1y,
       debounce__3y, debounce__4y, digit_7_pin10, digit_8_pin10, digit_9_pin10, dipswitch_1_out,
       dipswitch_2_out, dipswitch_3_out, dipswitch_4_out, E1, E2, E3, E4, E5, E6, E7, E8, E9, E10, E11, E12,
       E13, E14, E15, E16, E17, E18, E19, E20, E21, E22, E23, E24, e__0_3_pin3, e__0_3_pin4, e__0_3_pin7,
       e__0_3_pin8, F1, F2, F3, F4, F5, F6, F7, F10, G1, G2, G3, G4, G5, G6, G7, G8, G9, G10, G11, G12, G13,
       G14, G15, G16, G17, G18, G19, G20, G21, H1, H2, H3, H4, H5, H6, H7, H8, H9, H10, H11, H12, H13, H14,
       H15, H16, H17, H18, H19, H20, H21, H22, H23, H24, H25, H26, H27, H28, H29, H30, H31, H32, H33, H34,
       H35, H36, H37, H38, H39, H40, H41, H42, H43, H44, H45, H46, j_digit_pin1, j_digit_pin7, j_digit_pin9,
       j_digit_pin11, j_digit_pin12, j_digit_pin13, j_digit_pin14, M_2_out, M__a_b____10_out, M__BETA_out,
       pulldown_1_out, pullup_4_out, pullup_5_out, pullup_9_out, pullup_10_out, pullup_11_out, pullup_12_out,
       pullup_13_out, pullup_14_out, pullup_15_out, pullup_20_out, pullup_21_out, pullup_27_out,
       pullup_31_out, pullup_33_out, pullup_35_out, pullup_59_out, pullup_60_out, pullup_61_out,
       pullup_62_out, pullup_63_out, pullup_64_out, pullup_65_out, pullup_77_out, pullup_78_out,
       S0__a_b____10_out, S0__BETA_out, S0_out, S1__a_b____10_out, S1__BETA_out, S1_out, S2__a_b____10_out,
       S2__BETA_out, S2_out, S3__a_b____10_out, S3__BETA_out, S3_out, switchdt_4_p2, undriven, undriven_2,
       undriven_3, undriven_4, undriven_5, undriven_6, undriven_7, undriven_8, undriven_9, undriven_10,
       undriven_11, undriven_12, undriven_13, undriven_14, undriven_15;
  wire [0:0] _74181_5_pin9;
  wire [1:0] alpha_8_out;
  wire [2:0] _12_14_and_3_pin1, _74245_10_pin14, beta_14_out, d__0_7_2_pin17, gamma_0_out;
  wire [3:0] _4_7_pin13, _8_11_pin13, _7408_11_pin11, _74161_3_pin11, _74161_4_pin11, _74161_5_pin11,
       _74161_6_pin11, _74181_3_pin11, _74245_9_pin14, _74245_9_pin18, _74245_10_pin18, _74245_11_pin5,
       _74245_11_pin9, _74245_12_pin9, _74273_1_pin2, _74283_1_pin11, alpha_0_out, alpha_4_out, beta_3_out,
       beta_7_out, beta_11_out, d__0_7_2_pin8, d__0_7_pin3, d__0_7_pin13, digit_7_pin14, digit_8_pin14,
       digit_9_pin14;
  wire [3:3] _12_14_and_3_pin10;

  _7404 _7404_1 (
    .pin1(_7404_1_pin1), .pin2(_7404_1_pin2), .pin3(_7404_1_pin3), .pin4(D13), .pin5(_7404_1_pin5),
    .pin6(D12), .pin7(1'b0), .pin8(D11), .pin9(_7404_1_pin9), .pin10(D10), .pin11(_7404_1_pin11), .pin12(D9),
    .pin13(_7404_1_pin13), .pin14(1'b1));
  Seven_Seg_Hex seven_seg_hex_1 (.d({1'b0, E11, E10, E9}), .dp(1'b0));
  Seven_Seg_Hex seven_seg_hex_2 (.d({1'b0, _12_14_and_3_pin1}), .dp(1'b0));
  Seven_Seg_Hex seven_seg_hex_3 (.d({E8, E7, E6, E5}), .dp(1'b0));
  Seven_Seg_Hex seven_seg_hex_4 (.d(_8_11_pin13), .dp(1'b0));
  Seven_Seg_Hex seven_seg_hex_5 (.d({E4, E3, E2, E1}), .dp(1'b0));
  DipSwitch #(.dipDefault("true")) S3__BETA (.out(S3__BETA_out));
  DipSwitch S2__BETA (.out(S2__BETA_out));
  DipSwitch S1__BETA (.out(S1__BETA_out));
  DipSwitch #(.dipDefault("true")) S0__BETA (.out(S0__BETA_out));
  DipSwitch #(.dipDefault("true")) Cn__BETA (.out(Cn__BETA_out));
  DipSwitch M__BETA (.out(M__BETA_out));
  Seven_Seg_Hex seven_seg_hex_6 (.d(_4_7_pin13), .dp(1'b0));
  Seven_Seg_Hex seven_seg_hex_7 (.d({_12_14_and_3_pin10[3], E2, E1, 1'b0}), .dp(1'b0));
  _7427 _7427_1 (
    .pin1(_7427_1_pin1), .pin2(_7427_1_pin2), .pin3(_7427_1_pin3), .pin4(_7427_1_pin4), .pin5(_7427_1_pin4),
    .pin6(_7427_1_pin6), .pin7(1'b0), .pin8(_7427_1_pin8), .pin9(_7427_1_pin9), .pin10(_7427_1_pin10),
    .pin11(_7427_1_pin4), .pin12(_7427_1_pin12), .pin13(_7427_1_pin1), .pin14(1'b1));
  _7427 _7427_2 (
    .pin1(_7427_2_pin1), .pin2(D21), .pin3(_7427_2_pin3), .pin4(_7427_2_pin3), .pin5(_7427_2_pin3),
    .pin6(_7427_1_pin3), .pin7(1'b0), .pin8(_7427_2_pin8), .pin9(_7427_1_pin12), .pin10(_7427_1_pin12),
    .pin11(_7427_1_pin12), .pin12(_7427_2_pin3), .pin13(_7427_2_pin13), .pin14(1'b1));
  DipSwitch dipswitch_1 (.out(dipswitch_1_out));
  DipSwitch dipswitch_2 (.out(dipswitch_2_out));
  DipSwitch dipswitch_3 (.out(dipswitch_3_out));
  DipSwitch dipswitch_4 (.out(dipswitch_4_out));
  _7404 _7404_2 (
    .pin1(_7404_2_pin1), .pin2(D8), .pin3(_7404_2_pin3), .pin4(D7), .pin5(_7404_2_pin5), .pin6(D6),
    .pin7(1'b0), .pin8(D5), .pin9(_7404_2_pin9), .pin10(D4), .pin11(_7404_2_pin11), .pin12(D3),
    .pin13(_7404_2_pin13), .pin14(1'b1));
  PullUp pullup_1 (.out(LOAD__goes_low));
  _7404 _7404_3 (
    .pin1(S0__BETA_out), .pin2(_7404_3_pin2), .pin3(S1__BETA_out), .pin4(_7404_3_pin4), .pin5(S2__BETA_out),
    .pin6(_7404_3_pin6), .pin7(1'b0), .pin8(_7404_3_pin8), .pin9(Cn__BETA_out), .pin10(_7404_3_pin10),
    .pin11(M__BETA_out), .pin12(_7404_3_pin12), .pin13(S3__BETA_out), .pin14(1'b1));
  _74161 _74161_1 (
    .pin1(_7427_1_pin6), .pin2(_7427_1_pin9), .pin3(dipswitch_1_out), .pin4(dipswitch_2_out),
    .pin5(dipswitch_3_out), .pin6(dipswitch_4_out), .pin7(_74161_1_pin7), .pin8(1'b0), .pin9(LOAD__goes_low),
    .pin10(_74161_1_pin10), .pin11(_74161_1_pin11), .pin12(_74161_1_pin12), .pin13(_74161_1_pin13),
    .pin14(_74161_1_pin14), .pin16(1'b1));  // open: pin15
  PullUp pullup_2 (.out(_74161_1_pin7));
  _74154 _74154_1 (
    .pin1(_7404_1_pin1), .pin2(_7404_1_pin3), .pin3(_7404_1_pin5), .pin4(_7404_1_pin9), .pin5(_7404_1_pin11),
    .pin6(_7404_1_pin13), .pin7(_7404_2_pin1), .pin8(_7404_2_pin3), .pin9(_7404_2_pin5),
    .pin10(_7404_2_pin9), .pin11(_7404_2_pin11), .pin12(1'b0), .pin13(_7404_2_pin13), .pin14(_74154_1_pin14),
    .pin15(_74154_1_pin15), .pin16(_74154_1_pin16), .pin17(_74154_1_pin17), .pin18(1'b0), .pin19(1'b0),
    .pin20(_74161_1_pin11), .pin21(_74161_1_pin12), .pin22(_74161_1_pin13), .pin23(_74161_1_pin14),
    .pin24(1'b1));
  Button RESET_SUB_CLOCK (.out(_7427_1_pin10));
  Button RESET_OP_COUNTER (.out(_7427_2_pin13));
  _74132 debounce (
    ._1A(pulldown_1_out), ._1B(pulldown_1_out), ._1Y(debounce__1y), ._2A(debounce__1y), ._2B(debounce__1y),
    ._2Y(_7427_1_pin1), ._3B(debounce__4y), ._3A(pullup_5_out), ._3Y(debounce__3y), ._4A(pullup_4_out),
    ._4B(debounce__3y), ._4Y(debounce__4y), .VCC(1'b1), .GND(1'b0));
  PullUp pullup_3 (.out(_74161_1_pin10));
  _7408 _7408_1 (
    .pin1(_7404_3_pin2), .pin2(S1__BETA_out), .pin3(_7408_1_pin3), .pin4(_7404_3_pin12), .pin5(S2__BETA_out),
    .pin6(_7408_1_pin6), .pin7(1'b0), .pin8(_7408_1_pin8), .pin9(_7404_3_pin10), .pin10(_7404_3_pin8),
    .pin11(_7408_1_pin11), .pin12(_7404_3_pin4), .pin13(S0__BETA_out), .pin14(1'b1));
  _7411 _7411_1 (
    .pin1(_7404_3_pin6), .pin2(S3__BETA_out), .pin3(_7404_3_pin10), .pin4(Cn__BETA_out), .pin5(Cn__BETA_out),
    .pin6(_7411_1_pin6), .pin7(1'b0), .pin8(_7411_1_pin8), .pin9(_7411_1_pin6), .pin10(_7408_1_pin11),
    .pin11(_7411_1_pin11), .pin12(_7411_1_pin11), .pin13(_7404_3_pin6), .pin14(1'b1));
  _7411 _7411_2 (
    .pin1(_7404_3_pin2), .pin2(_7411_2_pin2), .pin3(M__BETA_out), .pin4(S2__BETA_out), .pin5(_7404_3_pin12),
    .pin6(_7411_2_pin2), .pin7(1'b0), .pin8(_7411_2_pin8), .pin9(_7408_1_pin6), .pin10(_7408_1_pin3),
    .pin11(_7408_1_pin8), .pin12(_7411_2_pin12), .pin13(S1__BETA_out), .pin14(1'b1));
  _7404 _7404_4 (
    .pin1(_74154_1_pin14), .pin2(D2), .pin3(_74154_1_pin15), .pin4(_7427_2_pin1), .pin5(_74154_1_pin16),
    .pin7(1'b0), .pin9(_74154_1_pin17), .pin10(_7427_1_pin2), .pin11(_7404_4_pin11), .pin12(_7404_4_pin12),
    .pin13(D22), .pin14(1'b1));  // open: pin6, pin8
  PullUp pullup_4 (.out(pullup_4_out));
  PullUp pullup_5 (.out(pullup_5_out));
  _74161 _74161_2 (
    .pin1(_7427_1_pin8), .pin2(_7427_2_pin8), .pin3(1'b0), .pin4(1'b0), .pin5(1'b0), .pin6(1'b0), .pin7(A15),
    .pin8(1'b0), .pin9(_74161_2_pin9), .pin10(_7404_4_pin12), .pin11(_74161_2_pin11), .pin12(_74161_2_pin12),
    .pin13(_74161_2_pin13), .pin14(_74161_2_pin14), .pin16(1'b1));  // open: pin15
  _74283 _4_7 (
    .pin1(_4_7_pin13[1]), .pin2(E3), .pin3(E5), .pin4(_4_7_pin13[0]), .pin5(E4), .pin6(E2), .pin7(_4_7_pin7),
    .pin8(1'b0), .pin9(_4_7_pin9), .pin10(_4_7_pin13[3]), .pin11(E5), .pin12(E7), .pin13(_4_7_pin13[2]),
    .pin14(E6), .pin15(E4), .pin16(1'b1));
  _74283 _8_11 (
    .pin1(_8_11_pin13[1]), .pin2(E7), .pin3(E9), .pin4(_8_11_pin13[0]), .pin5(E8), .pin6(E6),
    .pin7(_4_7_pin9), .pin8(1'b0), .pin9(_8_11_pin9), .pin10(_8_11_pin13[3]), .pin11(E9), .pin12(E11),
    .pin13(_8_11_pin13[2]), .pin14(E10), .pin15(E8), .pin16(1'b1));
  PullDown pulldown_1 (.out(pulldown_1_out));
  LED led_1 (.in(pullup_5_out));
  // SwitchDT switchdt_1: pin names not known; wires that end beside it: 1'b0, pullup_4_out, pullup_5_out
  LED led_2 (.in(pullup_4_out));
  Button SINGLE_STEP (.out(pulldown_1_out));
  PullUp pullup_6 (.out(_74161_2_pin9));
  LED L2 (.in(_4_7_pin9));
  LED L3 (.in(_8_11_pin9));
  _74154 _74154_2 (
    .pin2(_74154_2_pin2), .pin3(_74154_2_pin3), .pin4(_74154_2_pin4), .pin5(_74154_2_pin5),
    .pin6(_74154_2_pin6), .pin7(_74154_2_pin7), .pin8(_74154_2_pin8), .pin9(_74154_2_pin9), .pin12(1'b0),
    .pin18(1'b0), .pin19(1'b0), .pin20(_74161_2_pin11), .pin21(_74161_2_pin12), .pin22(_74161_2_pin13),
    .pin23(_74161_2_pin14), .pin24(1'b1));  // open: pin1, pin10, pin11, pin13, pin14, pin15, pin16, pin17
  _74283 _12_14_and_3 (
    .pin1(_12_14_and_3_pin1[1]), .pin2(E11), .pin3(1'b0), .pin4(_12_14_and_3_pin1[0]), .pin5(1'b0),
    .pin6(E10), .pin7(_8_11_pin9), .pin8(1'b0), .pin9(_4_7_pin7), .pin10(_12_14_and_3_pin10[3]), .pin11(E1),
    .pin12(E3), .pin13(_12_14_and_3_pin1[2]), .pin14(1'b0), .pin15(1'b0), .pin16(1'b1));
  _74541 _74541_1 (
    .pin1(1'b0), .pin2(_74541_1_pin2), .pin3(_74541_1_pin3), .pin4(_7411_2_pin12), .pin5(_7411_2_pin8),
    .pin6(_7411_1_pin8), .pin7(_74541_1_pin7), .pin8(_74541_1_pin8), .pin9(_74541_1_pin9), .pin10(1'b0),
    .pin11(_74541_1_pin11), .pin12(_74541_1_pin12), .pin13(_74541_1_pin13), .pin14(_74541_1_pin14),
    .pin15(_74541_1_pin15), .pin16(_74541_1_pin16), .pin17(_74541_1_pin17), .pin18(_74541_1_pin18),
    .pin19(1'b0), .pin20(1'b1));
  _7400 _7400_1 (
    .pin1(_74154_2_pin9), .pin2(_7400_1_pin2), .pin3(_7427_1_pin9), .pin4(debounce__4y), .pin5(_7400_1_pin5),
    .pin6(_7404_4_pin11), .pin7(1'b0), .pin8(_7427_1_pin4), .pin9(_7400_1_pin9), .pin10(A15), .pin11(A15),
    .pin12(_7400_1_pin12), .pin13(_7427_1_pin4), .pin14(1'b1));
  // SwitchDT switchdt_2: pin names not known; wires that end beside it: _7400_1_pin5, SLOW, FAST
  _74541 _74541_2 (
    .pin1(1'b0), .pin2(_7404_1_pin2), .pin3(D13), .pin4(D12), .pin5(D11), .pin6(D10), .pin7(D9), .pin8(D8),
    .pin9(D7), .pin10(1'b0), .pin11(_74541_2_pin11), .pin12(_74541_2_pin12), .pin13(_74541_2_pin13),
    .pin14(_74541_2_pin14), .pin15(_74541_2_pin15), .pin16(_74541_2_pin16), .pin17(_74541_2_pin17),
    .pin18(_74541_2_pin18), .pin19(1'b0), .pin20(1'b1));
  _74541 _74541_3 (
    .pin1(1'b0), .pin2(D6), .pin3(D5), .pin4(D4), .pin5(D3), .pin6(D2), .pin7(1'b0), .pin8(1'b0),
    .pin9(1'b0), .pin10(1'b0), .pin14(_74541_3_pin14), .pin15(_74541_3_pin15), .pin16(_74541_3_pin16),
    .pin17(_74541_3_pin17), .pin18(_74541_3_pin18), .pin19(1'b0), .pin20(1'b1));  // open: pin11, pin12, pin13
  LED L_INIT (.in(_74541_1_pin18));
  LED ELSE (.in(_74541_1_pin17));
  LED XOR (.in(_74541_1_pin16));
  LED A_MINUS_B (.in(_74541_1_pin15));
  LED A_PLUS_B (.in(_74541_1_pin14));
  LED XOR_2 (.in(_74541_1_pin13));
  LED A_MINUS_B_2 (.in(_74541_1_pin12));
  LED A_PLUS_B_2 (.in(_74541_1_pin11));
  PullUp pullup_7 (.out(_7400_1_pin12));
  PullUp pullup_8 (.out(_7400_1_pin9));
  LED L1 (.in(_4_7_pin7));
  LED _0 (.in(_74541_2_pin18));
  LED _1 (.in(_74541_2_pin17));
  LED _2 (.in(_74541_2_pin16));
  LED _3 (.in(_74541_2_pin15));
  LED _4 (.in(_74541_2_pin14));
  LED _5 (.in(_74541_2_pin13));
  LED _6 (.in(_74541_2_pin12));
  LED _7 (.in(_74541_2_pin11));
  LED _8 (.in(_74541_3_pin18));
  LED _9 (.in(_74541_3_pin17));
  LED _10 (.in(_74541_3_pin16));
  LED _11 (.in(_74541_3_pin15));
  LED _12 (.in(_74541_3_pin14));
  // SwitchDT switchdt_3: pin names not known; wires that end beside it: 1'b0, _7400_1_pin12, _7400_1_pin9
  DipSwitch beta_0 (.out(beta_3_out[0]));
  DipSwitch beta_1 (.out(beta_3_out[1]));
  DipSwitch #(.dipDefault("true")) beta_2 (.out(beta_3_out[2]));
  DipSwitch beta_3 (.out(beta_3_out[3]));
  DipSwitch #(.dipDefault("true")) beta_4 (.out(beta_7_out[0]));
  DipSwitch beta_5 (.out(beta_7_out[1]));
  DipSwitch beta_6 (.out(beta_7_out[2]));
  DipSwitch beta_7 (.out(beta_7_out[3]));
  DipSwitch beta_8 (.out(beta_11_out[0]));
  DipSwitch beta_9 (.out(beta_11_out[1]));
  DipSwitch beta_10 (.out(beta_11_out[2]));
  DipSwitch beta_11 (.out(beta_11_out[3]));
  DipSwitch beta_12 (.out(beta_14_out[0]));
  DipSwitch beta_13 (.out(beta_14_out[1]));
  DipSwitch beta_14 (.out(beta_14_out[2]));
  LED led_3 (.in(_7400_1_pin9));
  LED led_4 (.in(_7400_1_pin12));
  Seven_Seg_Hex seven_seg_hex_8 (.d({1'b0, beta_14_out}), .dp(1'b0));
  Seven_Seg_Hex seven_seg_hex_9 (.d(beta_11_out), .dp(1'b0));
  DipSwitch #(.dipDefault("true")) S3__a_b____10 (.out(S3__a_b____10_out));
  DipSwitch S2__a_b____10 (.out(S2__a_b____10_out));
  DipSwitch S1__a_b____10 (.out(S1__a_b____10_out));
  DipSwitch #(.dipDefault("true")) S0__a_b____10 (.out(S0__a_b____10_out));
  DipSwitch #(.dipDefault("true")) Cn__a_b____10 (.out(Cn__a_b____10_out));
  DipSwitch M__a_b____10 (.out(M__a_b____10_out));
  _7404 _7404_5 (
    .pin1(_74154_2_pin2), .pin2(D19), .pin3(_74154_2_pin3), .pin4(D18), .pin5(_74154_2_pin4), .pin6(D17),
    .pin7(1'b0), .pin8(_7404_5_pin8), .pin9(_74154_2_pin5), .pin10(D16), .pin11(_74154_2_pin6), .pin12(D15),
    .pin13(_74154_2_pin7), .pin14(1'b1));
  _7404 _7404_6 (
    .pin1(_74154_2_pin8), .pin2(D14), .pin3(1'b0), .pin5(_7404_6_pin5), .pin6(_7400_1_pin2), .pin7(1'b0),
    .pin9(1'b0), .pin11(1'b0), .pin13(1'b0), .pin14(1'b1));  // open: pin4, pin8, pin10, pin12
  Seven_Seg_Hex seven_seg_hex_10 (.d(beta_7_out), .dp(1'b0));
  Seven_Seg_Hex seven_seg_hex_11 (.d(beta_3_out), .dp(1'b0));
  _7404 _7404_7 (
    .pin1(1'b0), .pin3(1'b0), .pin5(1'b0), .pin7(1'b0), .pin8(_74541_1_pin3), .pin9(_74541_1_pin2),
    .pin11(1'b0), .pin12(_7404_7_pin12), .pin13(F10), .pin14(1'b1));  // open: pin2, pin4, pin6, pin10
  PullUp pullup_9 (.out(pullup_9_out));
  _74245 _74245_1 (
    .pin1(pullup_9_out), .pin2(1'b0), .pin3(E1), .pin4(E2), .pin5(_12_14_and_3_pin10[3]),
    .pin6(_4_7_pin13[0]), .pin7(_4_7_pin13[1]), .pin8(_4_7_pin13[2]), .pin9(_4_7_pin13[3]), .pin10(1'b0),
    .pin11(G14), .pin12(G15), .pin13(G16), .pin14(G17), .pin15(G18), .pin16(G19), .pin17(G20), .pin18(G21),
    .pin19(_74541_1_pin2), .pin20(1'b1));
  PullUp pullup_10 (.out(pullup_10_out));
  _74245 _74245_2 (
    .pin1(pullup_10_out), .pin2(_8_11_pin13[0]), .pin3(_8_11_pin13[1]), .pin4(_8_11_pin13[2]),
    .pin5(_8_11_pin13[3]), .pin6(_12_14_and_3_pin1[0]), .pin7(_12_14_and_3_pin1[1]),
    .pin8(_12_14_and_3_pin1[2]), .pin9(1'b0), .pin10(1'b0), .pin12(G7), .pin13(G8), .pin14(G9), .pin15(G10),
    .pin16(G11), .pin17(G12), .pin18(G13), .pin19(_74541_1_pin2), .pin20(1'b1));  // open: pin11
  PullUp pullup_11 (.out(pullup_11_out));
  _74245 _74245_3 (
    .pin1(pullup_11_out), .pin2(beta_3_out[0]), .pin3(beta_3_out[1]), .pin4(beta_3_out[2]),
    .pin5(beta_3_out[3]), .pin6(beta_7_out[0]), .pin7(beta_7_out[1]), .pin8(beta_7_out[2]),
    .pin9(beta_7_out[3]), .pin10(1'b0), .pin11(G14), .pin12(G15), .pin13(G16), .pin14(G17), .pin15(G18),
    .pin16(G19), .pin17(G20), .pin18(G21), .pin19(_74541_1_pin3), .pin20(1'b1));
  PullUp pullup_12 (.out(pullup_12_out));
  _74245 _74245_4 (
    .pin1(pullup_12_out), .pin2(beta_11_out[0]), .pin3(beta_11_out[1]), .pin4(beta_11_out[2]),
    .pin5(beta_11_out[3]), .pin6(beta_14_out[0]), .pin7(beta_14_out[1]), .pin8(beta_14_out[2]), .pin9(1'b0),
    .pin10(1'b0), .pin12(G7), .pin13(G8), .pin14(G9), .pin15(G10), .pin16(G11), .pin17(G12), .pin18(G13),
    .pin19(_74541_1_pin3), .pin20(1'b1));  // open: pin11
  _7404 _7404_8 (
    .pin1(S0__a_b____10_out), .pin2(_7404_8_pin2), .pin3(S1__a_b____10_out), .pin4(_7404_8_pin4),
    .pin5(S2__a_b____10_out), .pin6(_7404_8_pin6), .pin7(1'b0), .pin8(_7404_8_pin8),
    .pin9(Cn__a_b____10_out), .pin10(_7404_8_pin10), .pin11(M__a_b____10_out), .pin12(_7404_8_pin12),
    .pin13(S3__a_b____10_out), .pin14(1'b1));
  LED led_5 (.in(E11));
  _7411 _7411_3 (
    .pin1(_7404_8_pin2), .pin2(_7411_3_pin2), .pin3(M__a_b____10_out), .pin4(S2__a_b____10_out),
    .pin5(_7404_8_pin12), .pin6(_7411_3_pin2), .pin7(1'b0), .pin8(_74541_1_pin8), .pin9(_7411_3_pin9),
    .pin10(_7411_3_pin10), .pin11(_7411_3_pin11), .pin12(_74541_1_pin7), .pin13(S1__a_b____10_out),
    .pin14(1'b1));
  _7408 _7408_2 (
    .pin1(_7404_8_pin2), .pin2(S1__a_b____10_out), .pin3(_7411_3_pin10), .pin4(_7404_8_pin12),
    .pin5(S2__a_b____10_out), .pin6(_7411_3_pin9), .pin7(1'b0), .pin8(_7411_3_pin11), .pin9(_7404_8_pin10),
    .pin10(_7404_8_pin8), .pin11(_7408_2_pin11), .pin12(_7404_8_pin4), .pin13(S0__a_b____10_out), .pin14(1'b1));
  _7411 _7411_4 (
    .pin1(_7404_8_pin6), .pin2(S3__a_b____10_out), .pin3(_7404_8_pin10), .pin4(Cn__a_b____10_out),
    .pin5(Cn__a_b____10_out), .pin6(_7411_4_pin6), .pin7(1'b0), .pin8(_74541_1_pin9), .pin9(_7411_4_pin6),
    .pin10(_7408_2_pin11), .pin11(_7411_4_pin11), .pin12(_7411_4_pin11), .pin13(_7404_8_pin6), .pin14(1'b1));
  LED led_6 (.in(E9));
  LED led_7 (.in(E10));
  LED led_8 (.in(E7));
  LED led_9 (.in(E8));
  _7420 _7420_1 (
    .pin1(D1), .pin2(D1), .pin4(D1), .pin5(D1), .pin6(_7420_1_pin6), .pin7(1'b0), .pin8(_7404_6_pin5),
    .pin9(_7420_1_pin6), .pin10(_7420_1_pin10), .pin12(_7420_1_pin12), .pin13(_7420_1_pin13), .pin14(1'b1));  // open: pin3, pin11
  LED led_10 (.in(E5));
  LED led_11 (.in(E6));
  _74541 _74541_4 (
    .pin1(1'b0), .pin2(1'b0), .pin3(D19), .pin4(D18), .pin5(D17), .pin6(_7404_5_pin8), .pin7(D16),
    .pin8(D15), .pin9(D14), .pin10(1'b0), .pin11(_74541_4_pin11), .pin12(_74541_4_pin12),
    .pin13(_74541_4_pin13), .pin14(_74541_4_pin14), .pin15(_74541_4_pin15), .pin16(_74541_4_pin16),
    .pin17(_74541_4_pin17), .pin19(1'b0), .pin20(1'b1));  // open: pin18
  LED led_12 (.in(E3));
  LED led_13 (.in(E4));
  LED led_14 (.in(E1));
  LED led_15 (.in(E2));
  PullUp pullup_13 (.out(pullup_13_out));
  Seven_Seg_Hex seven_seg_hex_12 (.d({1'b0, E11, E10, E9}), .dp(1'b0));
  LED _1_2 (.in(_74541_4_pin17));
  LED _2_2 (.in(_74541_4_pin16));
  LED _3_2 (.in(_74541_4_pin15));
  LED _4_2 (.in(_74541_4_pin14));
  LED _5_2 (.in(_74541_4_pin13));
  LED _6_2 (.in(_74541_4_pin12));
  LED _7_2 (.in(_74541_4_pin11));
  _7474 _7474_1 (
    .pin1(A15), .pin2(A15), .pin3(F10), .pin4(_7404_7_pin12), .pin6(_74541_1_pin2), .pin7(1'b0),
    .pin10(1'b0), .pin11(1'b0), .pin12(1'b0), .pin13(1'b0), .pin14(1'b1));  // open: pin5, pin8, pin9
  _74245 _74245_5 (
    .pin1(pullup_13_out), .pin2(S3__BETA_out), .pin3(S2__BETA_out), .pin4(S1__BETA_out), .pin5(S0__BETA_out),
    .pin6(Cn__BETA_out), .pin7(M__BETA_out), .pin8(1'b0), .pin9(1'b0), .pin10(1'b0), .pin13(G1), .pin14(G2),
    .pin15(G3), .pin16(G4), .pin17(G5), .pin18(G6), .pin19(_74541_1_pin3), .pin20(1'b1));  // open: pin11, pin12
  PullUp pullup_14 (.out(pullup_14_out));
  _74245 _74245_6 (
    .pin1(pullup_14_out), .pin2(S3__a_b____10_out), .pin3(S2__a_b____10_out), .pin4(S1__a_b____10_out),
    .pin5(S0__a_b____10_out), .pin6(Cn__a_b____10_out), .pin7(M__a_b____10_out), .pin8(1'b0), .pin9(1'b0),
    .pin10(1'b0), .pin13(G1), .pin14(G2), .pin15(G3), .pin16(G4), .pin17(G5), .pin18(G6),
    .pin19(_74541_1_pin2), .pin20(1'b1));  // open: pin11, pin12
  _7454 _7454_1 (
    .pin1(D14), .pin2(D13), .pin3(D14), .pin4(D14), .pin5(D12), .pin6(_7420_1_pin13), .pin7(1'b0),
    .pin9(D11), .pin10(D17), .pin11(D17), .pin12(D10), .pin13(D14), .pin14(1'b1));  // open: pin8
  Seven_Seg_Hex seven_seg_hex_13 (.d({E8, E7, E6, E5}), .dp(1'b0));
  Seven_Seg_Hex seven_seg_hex_14 (.d({E4, E3, E2, E1}), .dp(1'b0));
  Seven_Seg_Hex seven_seg_hex_15 (.d({2'b00, C4, C5}), .dp(1'b0));
  Seven_Seg_Hex seven_seg_hex_16 (.d({C6, C7, C8, C9}), .dp(1'b0));
  _7454 _7454_2 (
    .pin1(D17), .pin2(D9), .pin3(D14), .pin4(D14), .pin5(D10), .pin6(_7420_1_pin12), .pin7(1'b0), .pin9(D7),
    .pin10(D17), .pin11(D17), .pin12(D6), .pin13(_7404_5_pin8), .pin14(1'b1));  // open: pin8
  Seven_Seg_Hex seven_seg_hex_17 (.d({C10, C11, C12, C13}), .dp(1'b0));
  PullUp pullup_15 (.out(pullup_15_out));
  _74214 u_a5 (
    .A0(C13), .A1(C12), .A2(C11), .A3(C10), .A4(C9), .A5(C8), .A6(C7), .A7(C6), .A8(C5), .A9(C4), .nCS(1'b0),
    .nWE(_74245_7_pin19), .Dout(E6), .VCC(1'b1), .GND(1'b0), .Din(_74245_7_pin7));
  _74214 u_a6 (
    .A0(C13), .A1(C12), .A2(C11), .A3(C10), .A4(C9), .A5(C8), .A6(C7), .A7(C6), .A8(C5), .A9(C4), .nCS(1'b0),
    .nWE(_74245_7_pin19), .Dout(E7), .VCC(1'b1), .GND(1'b0), .Din(_74245_7_pin8));
  _74214 u_a7 (
    .A0(C13), .A1(C12), .A2(C11), .A3(C10), .A4(C9), .A5(C8), .A6(C7), .A7(C6), .A8(C5), .A9(C4), .nCS(1'b0),
    .nWE(_74245_7_pin19), .Dout(E8), .VCC(1'b1), .GND(1'b0), .Din(_74245_7_pin9));
  _74214 u_a8 (
    .A0(C13), .A1(C12), .A2(C11), .A3(C10), .A4(C9), .A5(C8), .A6(C7), .A7(C6), .A8(C5), .A9(C4), .nCS(1'b0),
    .nWE(_74245_7_pin19), .Dout(E9), .VCC(1'b1), .GND(1'b0), .Din(_74245_8_pin2));
  _74214 u_a9 (
    .A0(C13), .A1(C12), .A2(C11), .A3(C10), .A4(C9), .A5(C8), .A6(C7), .A7(C6), .A8(C5), .A9(C4), .nCS(1'b0),
    .nWE(_74245_7_pin19), .Dout(E10), .VCC(1'b1), .GND(1'b0), .Din(_74245_8_pin3));
  _74214 u_a10 (
    .A0(C13), .A1(C12), .A2(C11), .A3(C10), .A4(C9), .A5(C8), .A6(C7), .A7(C6), .A8(C5), .A9(C4), .nCS(1'b0),
    .nWE(_74245_7_pin19), .Dout(E11), .VCC(1'b1), .GND(1'b0), .Din(_74245_8_pin4));
  _74161 _74161_3 (
    .pin1(A15), .pin2(D21), .pin3(1'b0), .pin4(1'b0), .pin5(1'b0), .pin6(1'b0), .pin7(_74161_3_pin7),
    .pin8(1'b0), .pin9(_74161_3_pin9), .pin10(_74161_3_pin7), .pin11(_74161_3_pin11[3]),
    .pin12(_74161_3_pin11[2]), .pin13(_74161_3_pin11[1]), .pin14(_74161_3_pin11[0]), .pin16(1'b1));  // open: pin15
  _74161 _74161_4 (
    .pin1(A15), .pin2(D21), .pin3(1'b0), .pin4(1'b0), .pin5(1'b0), .pin6(1'b0), .pin7(_74161_4_pin7),
    .pin8(1'b0), .pin9(_74161_4_pin9), .pin10(_74161_4_pin7), .pin11(_74161_4_pin11[3]),
    .pin12(_74161_4_pin11[2]), .pin13(_74161_4_pin11[1]), .pin14(_74161_4_pin11[0]), .pin15(_74161_3_pin7),
    .pin16(1'b1));
  _74161 _74161_5 (
    .pin1(A15), .pin2(D21), .pin3(1'b0), .pin4(1'b0), .pin5(1'b0), .pin6(1'b0), .pin7(_74161_5_pin7),
    .pin8(1'b0), .pin9(_74161_5_pin9), .pin10(_74161_5_pin7), .pin11(_74161_5_pin11[3]),
    .pin12(_74161_5_pin11[2]), .pin13(_74161_5_pin11[1]), .pin14(_74161_5_pin11[0]), .pin15(_74161_4_pin7),
    .pin16(1'b1));
  _74161 _74161_6 (
    .pin1(A15), .pin2(D21), .pin3(1'b0), .pin4(1'b0), .pin5(1'b0), .pin6(1'b0), .pin7(pullup_15_out),
    .pin8(1'b0), .pin9(_74161_6_pin9), .pin10(pullup_15_out), .pin11(_74161_6_pin11[3]),
    .pin12(_74161_6_pin11[2]), .pin13(_74161_6_pin11[1]), .pin14(_74161_6_pin11[0]), .pin15(_74161_5_pin7),
    .pin16(1'b1));
  _7454 _7454_3 (
    .pin1(D17), .pin2(D4), .pin3(D17), .pin4(D17), .pin5(D5), .pin6(_7420_1_pin10), .pin7(1'b0), .pin9(D3),
    .pin10(_7404_5_pin8), .pin11(_7404_5_pin8), .pin12(D2), .pin13(D17), .pin14(1'b1));  // open: pin8
  PullUp pullup_16 (.out(_74161_3_pin9));
  PullUp pullup_17 (.out(_74161_4_pin9));
  PullUp pullup_18 (.out(_74161_5_pin9));
  PullUp pullup_19 (.out(_74161_6_pin9));
  Seven_Seg_Hex seven_seg_hex_18 (.d(_74161_3_pin11), .dp(1'b0));
  Seven_Seg_Hex seven_seg_hex_19 (.d(_74161_4_pin11), .dp(1'b0));
  Seven_Seg_Hex seven_seg_hex_20 (.d(_74161_5_pin11), .dp(1'b0));
  Seven_Seg_Hex seven_seg_hex_21 (.d(_74161_6_pin11), .dp(1'b0));
  _74214 a0 (
    .A0(C13), .A1(C12), .A2(C11), .A3(C10), .A4(C9), .A5(C8), .A6(C7), .A7(C6), .A8(C5), .A9(C4), .nCS(1'b0),
    .nWE(_74245_7_pin19), .Dout(E1), .VCC(1'b1), .GND(1'b0), .Din(_74245_7_pin2));
  _74214 u_a1 (
    .A0(C13), .A1(C12), .A2(C11), .A3(C10), .A4(C9), .A5(C8), .A6(C7), .A7(C6), .A8(C5), .A9(C4), .nCS(1'b0),
    .nWE(_74245_7_pin19), .Dout(E2), .VCC(1'b1), .GND(1'b0), .Din(_74245_7_pin3));
  _74214 u_a2 (
    .A0(C13), .A1(C12), .A2(C11), .A3(C10), .A4(C9), .A5(C8), .A6(C7), .A7(C6), .A8(C5), .A9(C4), .nCS(1'b0),
    .nWE(_74245_7_pin19), .Dout(E3), .VCC(1'b1), .GND(1'b0), .Din(_74245_7_pin4));
  _74214 u_a3 (
    .A0(C13), .A1(C12), .A2(C11), .A3(C10), .A4(C9), .A5(C8), .A6(C7), .A7(C6), .A8(C5), .A9(C4), .nCS(1'b0),
    .nWE(_74245_7_pin19), .Dout(E4), .VCC(1'b1), .GND(1'b0), .Din(_74245_7_pin5));
  _74214 u_a4 (
    .A0(C13), .A1(C12), .A2(C11), .A3(C10), .A4(C9), .A5(C8), .A6(C7), .A7(C6), .A8(C5), .A9(C4), .nCS(1'b0),
    .nWE(_74245_7_pin19), .Dout(E5), .VCC(1'b1), .GND(1'b0), .Din(_74245_7_pin6));
  LED led_16 (.in(H32));
  LED led_17 (.in(H34));
  LED led_18 (.in(H33));
  LED led_19 (.in(H36));
  LED led_20 (.in(H35));
  _7408 _7408_3 (
    .pin1(D19), .pin2(D2), .pin3(F10), .pin4(D19), .pin5(D2), .pin6(B9), .pin7(1'b0), .pin8(B15), .pin9(D3),
    .pin10(D18), .pin11(B14), .pin12(D3), .pin13(_7408_3_pin13), .pin14(1'b1));
  LED led_21 (.in(H38));
  LED led_22 (.in(H37));
  LED led_23 (.in(H40));
  LED led_24 (.in(H39));
  LED led_25 (.in(H42));
  LED led_26 (.in(H41));
  LED led_27 (.in(H44));
  LED led_28 (.in(H43));
  LED led_29 (.in(H46));
  LED led_30 (.in(H45));
  _74245 _74245_7 (
    .pin1(1'b0), .pin2(_74245_7_pin2), .pin3(_74245_7_pin3), .pin4(_74245_7_pin4), .pin5(_74245_7_pin5),
    .pin6(_74245_7_pin6), .pin7(_74245_7_pin7), .pin8(_74245_7_pin8), .pin9(_74245_7_pin9), .pin10(1'b0),
    .pin11(E17), .pin12(E18), .pin13(E19), .pin14(E20), .pin15(E21), .pin16(E22), .pin17(E23), .pin18(E24),
    .pin19(_74245_7_pin19), .pin20(1'b1));
  _74245 _74245_8 (
    .pin1(1'b0), .pin2(_74245_8_pin2), .pin3(_74245_8_pin3), .pin4(_74245_8_pin4), .pin10(1'b0),
    .pin11(1'b0), .pin12(1'b0), .pin13(1'b0), .pin14(1'b0), .pin15(1'b0), .pin16(E14), .pin17(E15),
    .pin18(E16), .pin19(_74245_7_pin19), .pin20(1'b1));  // open: pin5, pin6, pin7, pin8, pin9
  Seven_Seg_Hex seven_seg_hex_22 (.d({1'b0, H32, H33, H34}), .dp(1'b0));
  _7432 _7432_1 (
    .pin1(D19), .pin2(D18), .pin3(_7408_3_pin13), .pin4(D18), .pin5(D17), .pin6(_7432_1_pin6), .pin7(1'b0),
    .pin8(_7432_1_pin8), .pin9(D16), .pin10(D15), .pin12(1'b0), .pin13(1'b0), .pin14(1'b1));  // open: pin11
  Seven_Seg_Hex seven_seg_hex_23 (.d({H35, H36, H37, H38}), .dp(1'b0));
  Seven_Seg_Hex seven_seg_hex_24 (.d({H39, H40, H41, H42}), .dp(1'b0));
  Seven_Seg_Hex seven_seg_hex_25 (.d({H43, H44, H45, H46}), .dp(1'b0));
  _74181 _74181_1 (
    .pin1(G21), .pin2(H46), .pin3(G6), .pin4(G5), .pin5(G4), .pin6(G3), .pin7(G2), .pin8(G1),
    .pin9(_74245_11_pin5[0]), .pin10(_74245_11_pin5[1]), .pin11(_74245_11_pin5[2]), .pin12(1'b0));  // open: pin13, pin14, pin15, pin16, pin17, pin18, pin19, pin20, pin21, pin22, pin23, pin24
  _7411 _7411_5 (
    .pin1(D19), .pin2(D9), .pin3(1'b0), .pin4(1'b0), .pin5(1'b0), .pin7(1'b0), .pin8(D21), .pin9(D8),
    .pin10(E12), .pin11(D19), .pin12(C3), .pin13(D19), .pin14(1'b1));  // open: pin6
  LED led_31 (.in(undriven_14));
  LED led_32 (.in(undriven_15));
  LED led_33 (.in(E14));
  LED led_34 (.in(E16));
  LED led_35 (.in(E15));
  _74260 _74260_1 (
    .pin1(D19), .pin2(D18), .pin3(D17), .pin4(_74260_1_pin4), .pin5(_74260_1_pin4), .pin6(_74260_1_pin6),
    .pin7(1'b0), .pin8(_74260_1_pin4), .pin9(_74260_1_pin4), .pin10(_74260_1_pin4), .pin11(_74260_1_pin4),
    .pin12(D14), .pin13(D14), .pin14(1'b1));
  LED led_36 (.in(E18));
  LED led_37 (.in(E17));
  LED led_38 (.in(E20));
  LED led_39 (.in(E19));
  _74273 d__0_7 (
    .pin1(A15), .pin2(H46), .pin3(d__0_7_pin3[0]), .pin4(d__0_7_pin3[1]), .pin5(H45), .pin6(H44),
    .pin7(d__0_7_pin3[2]), .pin8(d__0_7_pin3[3]), .pin9(H43), .pin10(1'b0), .pin11(F7), .pin12(H42),
    .pin13(d__0_7_pin13[0]), .pin14(d__0_7_pin13[1]), .pin15(H41), .pin16(H40), .pin17(d__0_7_pin13[2]),
    .pin18(d__0_7_pin13[3]), .pin19(H39), .pin20(1'b1));
  _74273 d__0_7_2 (
    .pin1(A15), .pin2(H38), .pin3(d__0_7_2_pin8[0]), .pin4(d__0_7_2_pin8[1]), .pin5(H37), .pin6(H36),
    .pin7(d__0_7_2_pin8[2]), .pin8(d__0_7_2_pin8[3]), .pin9(H35), .pin10(1'b0), .pin11(F7), .pin12(H34),
    .pin13(d__0_7_2_pin17[0]), .pin14(d__0_7_2_pin17[1]), .pin15(H33), .pin16(H32),
    .pin17(d__0_7_2_pin17[2]), .pin18(1'b0), .pin20(1'b1));  // open: pin19
  _74181 _74181_2 (
    .pin1(G17), .pin2(H42), .pin3(G6), .pin4(G5), .pin5(G4), .pin6(G3), .pin7(_74181_2_pin7), .pin8(G1),
    .pin9(_74245_11_pin9[0]), .pin10(_74245_11_pin9[1]), .pin11(_74245_11_pin9[2]), .pin12(1'b0));  // open: pin13, pin14, pin15, pin16, pin17, pin18, pin19, pin20, pin21, pin22, pin23, pin24
  LED led_40 (.in(E22));
  LED led_41 (.in(E21));
  LED led_42 (.in(E24));
  LED led_43 (.in(E23));
  Seven_Seg_Hex seven_seg_hex_26 (.d({1'b0, E14, E15, E16}), .dp(1'b0));
  LED led_44 (.in(undriven_12));
  LED led_45 (.in(undriven_13));
  _7408 _7408_4 (
    .pin1(_74260_1_pin6), .pin2(D10), .pin3(_7408_4_pin3), .pin4(_7432_1_pin6), .pin5(D10), .pin6(F1),
    .pin7(1'b0), .pin8(_7408_4_pin8), .pin9(_7432_1_pin8), .pin10(D10), .pin11(_7408_4_pin11), .pin12(D17),
    .pin13(D10), .pin14(1'b1));
  Seven_Seg_Hex seven_seg_hex_27 (.d({E17, E18, E19, E20}), .dp(1'b0));
  Seven_Seg_Hex seven_seg_hex_28 (.d({E21, E22, E23, E24}), .dp(1'b0));
  _7408 _7408_5 (
    .pin1(D15), .pin2(D10), .pin3(_7408_5_pin3), .pin4(D19), .pin5(D4), .pin6(B13), .pin7(1'b0), .pin8(B10),
    .pin9(D18), .pin10(D6), .pin11(B11), .pin12(D6), .pin13(_7408_3_pin13), .pin14(1'b1));
  LED led_46 (.in(d__0_7_2_pin17[1]));
  LED led_47 (.in(d__0_7_2_pin17[2]));
  _74181 _74181_3 (
    .pin1(G13), .pin2(H38), .pin3(G6), .pin4(G5), .pin5(G4), .pin6(G3), .pin7(_74181_3_pin7), .pin8(G1),
    .pin9(_74181_3_pin11[0]), .pin10(_74181_3_pin11[1]), .pin11(_74181_3_pin11[2]), .pin12(1'b0));  // open: pin13, pin14, pin15, pin16, pin17, pin18, pin19, pin20, pin21, pin22, pin23, pin24
  LED led_48 (.in(d__0_7_2_pin8[3]));
  LED led_49 (.in(d__0_7_2_pin17[0]));
  _74182 _74182_1 (
    .pin1(_74182_1_pin1), .pin2(_74182_1_pin2), .pin3(_74182_1_pin3), .pin4(_74182_1_pin4),
    .pin5(_74182_1_pin5), .pin6(_74182_1_pin6), .pin7(_74182_1_pin7), .pin8(1'b0), .pin9(_74182_1_pin9),
    .pin10(_74182_1_pin10), .pin11(_74181_3_pin7), .pin12(_74181_2_pin7), .pin13(G2), .pin14(_74182_1_pin14),
    .pin15(_74182_1_pin15), .pin16(1'b1));
  LED led_50 (.in(_74182_1_pin7));
  LED led_51 (.in(d__0_7_2_pin8[1]));
  LED led_52 (.in(d__0_7_2_pin8[2]));
  _7400 _7400_2 (
    .pin1(1'b0), .pin2(1'b0), .pin4(E13), .pin5(E13), .pin6(_74245_7_pin19), .pin7(1'b0), .pin8(E12),
    .pin9(_7400_2_pin9), .pin10(_7400_2_pin10), .pin12(1'b0), .pin13(1'b0), .pin14(1'b1));  // open: pin3, pin11
  LED led_53 (.in(d__0_7_pin13[3]));
  LED led_54 (.in(d__0_7_2_pin8[0]));
  LED led_55 (.in(undriven_10));
  LED led_56 (.in(undriven_11));
  LED led_57 (.in(_74182_1_pin10));
  LED led_58 (.in(d__0_7_pin13[1]));
  LED led_59 (.in(d__0_7_pin13[2]));
  LED led_60 (.in(d__0_7_pin3[3]));
  LED led_61 (.in(d__0_7_pin13[0]));
  LED led_62 (.in(d__0_7_pin3[1]));
  LED led_63 (.in(d__0_7_pin3[2]));
  LED led_64 (.in(d__0_7_pin3[0]));
  _74260 _74260_2 (
    .pin1(C13), .pin2(C12), .pin3(C11), .pin4(C10), .pin5(_7400_2_pin10), .pin6(_7400_2_pin9), .pin7(1'b0),
    .pin8(C4), .pin9(C5), .pin10(C6), .pin11(C7), .pin12(C8), .pin13(C9), .pin14(1'b1));
  Seven_Seg_Hex seven_seg_hex_29 (.d({1'b0, d__0_7_2_pin17}), .dp(1'b0));
  _7408 _7408_6 (
    .pin1(D19), .pin2(D11), .pin3(E13), .pin4(D19), .pin5(D5), .pin6(B12), .pin7(1'b0), .pin8(F5),
    .pin9(_7432_1_pin6), .pin10(D12), .pin11(_7408_6_pin11), .pin12(D12), .pin13(_74260_1_pin6), .pin14(1'b1));
  Seven_Seg_Hex seven_seg_hex_30 (.d(d__0_7_2_pin8), .dp(1'b0));
  Seven_Seg_Hex seven_seg_hex_31 (.d(d__0_7_pin13), .dp(1'b0));
  _74181 _74181_4 (
    .pin1(G9), .pin2(H34), .pin3(G6), .pin4(G5), .pin5(G4), .pin6(G3), .pin7(_74182_1_pin9), .pin8(G1),
    .pin9(_74245_12_pin9[0]), .pin10(_74245_12_pin9[1]), .pin11(_74245_12_pin9[2]), .pin12(1'b0));  // open: pin13, pin14, pin15, pin16, pin17, pin18, pin19, pin20, pin21, pin22, pin23, pin24
  _74541 _74541_5 (
    .pin1(1'b0), .pin2(B15), .pin3(B14), .pin4(B13), .pin5(B12), .pin6(B11), .pin7(B10), .pin8(C3),
    .pin9(F1), .pin10(1'b0), .pin11(_74541_5_pin11), .pin12(_74541_5_pin12), .pin13(_74541_5_pin13),
    .pin14(_74541_5_pin14), .pin15(_74541_5_pin15), .pin16(_74541_5_pin16), .pin17(_74541_5_pin17),
    .pin18(_74541_5_pin18), .pin19(1'b0), .pin20(1'b1));
  Seven_Seg_Hex seven_seg_hex_32 (.d(d__0_7_pin3), .dp(1'b0));
  LED Q (.in(_74541_5_pin18));
  LED P (.in(_74541_5_pin17));
  LED O (.in(_74541_5_pin16));
  LED N (.in(_74541_5_pin15));
  LED L (.in(_74541_5_pin14));
  LED M (.in(_74541_5_pin13));
  LED K (.in(_74541_5_pin12));
  LED J (.in(_74541_5_pin11));
  LED led_65 (.in(undriven_8));
  LED led_66 (.in(undriven_9));
  Seven_Seg_Hex seven_seg_hex_33 (.d(_74245_12_pin9), .dp(1'b0));
  Seven_Seg_Hex seven_seg_hex_34 (.d(_74181_3_pin11), .dp(1'b0));
  _74541 _74541_6 (
    .pin1(1'b0), .pin2(E13), .pin3(B9), .pin4(F10), .pin5(F2), .pin6(F5), .pin7(F3), .pin8(F4), .pin9(F7),
    .pin10(1'b0), .pin11(_74541_6_pin11), .pin12(_74541_6_pin12), .pin13(_74541_6_pin13),
    .pin14(_74541_6_pin14), .pin15(_74541_6_pin15), .pin16(_74541_6_pin16), .pin17(_74541_6_pin17),
    .pin18(_74541_6_pin18), .pin19(1'b0), .pin20(1'b1));
  Seven_Seg_Hex seven_seg_hex_35 (.d(_74245_11_pin9), .dp(1'b0));
  _74245 _74245_9 (
    .pin1(1'b0), .pin2(d__0_7_pin3[0]), .pin3(d__0_7_pin3[1]), .pin4(d__0_7_pin3[2]), .pin5(d__0_7_pin3[3]),
    .pin6(d__0_7_pin13[0]), .pin7(d__0_7_pin13[1]), .pin8(d__0_7_pin13[2]), .pin9(d__0_7_pin13[3]),
    .pin10(1'b0), .pin11(_74245_9_pin14[3]), .pin12(_74245_9_pin14[2]), .pin13(_74245_9_pin14[1]),
    .pin14(_74245_9_pin14[0]), .pin15(_74245_9_pin18[3]), .pin16(_74245_9_pin18[2]),
    .pin17(_74245_9_pin18[1]), .pin18(_74245_9_pin18[0]), .pin19(F6), .pin20(1'b1));
  _74245 _74245_10 (
    .pin1(1'b0), .pin2(d__0_7_2_pin8[0]), .pin3(d__0_7_2_pin8[1]), .pin4(d__0_7_2_pin8[2]),
    .pin5(d__0_7_2_pin8[3]), .pin6(d__0_7_2_pin17[0]), .pin7(d__0_7_2_pin17[1]), .pin8(d__0_7_2_pin17[2]),
    .pin10(1'b0), .pin12(_74245_10_pin14[2]), .pin13(_74245_10_pin14[1]), .pin14(_74245_10_pin14[0]),
    .pin15(_74245_10_pin18[3]), .pin16(_74245_10_pin18[2]), .pin17(_74245_10_pin18[1]),
    .pin18(_74245_10_pin18[0]), .pin19(F6), .pin20(1'b1));  // open: pin9, pin11
  _7408 _7408_7 (
    .pin1(D17), .pin2(D12), .pin3(_7408_7_pin3), .pin4(D12), .pin5(_7432_1_pin8), .pin6(_7408_7_pin6),
    .pin7(1'b0), .pin9(1'b0), .pin10(1'b0), .pin11(_7408_7_pin11), .pin12(D12), .pin13(D15), .pin14(1'b1));  // open: pin8
  Seven_Seg_Hex seven_seg_hex_36 (.d(_74245_11_pin5), .dp(1'b0));
  LED I (.in(_74541_6_pin18));
  LED H (.in(_74541_6_pin17));
  LED G (.in(_74541_6_pin16));
  LED A (.in(_74541_6_pin15));
  LED B (.in(_74541_6_pin14));
  LED C (.in(_74541_6_pin13));
  LED D (.in(_74541_6_pin12));
  LED E (.in(_74541_6_pin11));
  PullUp pullup_20 (.out(pullup_20_out));
  _74245 _74245_11 (
    .pin1(pullup_20_out), .pin2(_74245_11_pin5[0]), .pin3(_74245_11_pin5[1]), .pin4(_74245_11_pin5[2]),
    .pin5(_74245_11_pin5[3]), .pin6(_74245_11_pin9[0]), .pin7(_74245_11_pin9[1]), .pin8(_74245_11_pin9[2]),
    .pin9(_74245_11_pin9[3]), .pin10(1'b0), .pin11(_74245_11_pin11), .pin12(_74245_11_pin12),
    .pin13(_74245_11_pin13), .pin14(_74245_11_pin14), .pin15(_74245_11_pin15), .pin16(_74245_11_pin16),
    .pin17(_74245_11_pin17), .pin18(_74245_11_pin18), .pin19(_74245_11_pin19), .pin20(1'b1));
  PullUp pullup_21 (.out(pullup_21_out));
  _74245 _74245_12 (
    .pin1(pullup_21_out), .pin2(_74181_3_pin11[0]), .pin3(_74181_3_pin11[1]), .pin4(_74181_3_pin11[2]),
    .pin5(_74181_3_pin11[3]), .pin6(_74245_12_pin9[0]), .pin7(_74245_12_pin9[1]), .pin8(_74245_12_pin9[2]),
    .pin9(_74245_12_pin9[3]), .pin10(1'b0), .pin11(_74245_12_pin11), .pin12(_74245_12_pin12),
    .pin13(_74245_12_pin13), .pin14(_74245_12_pin14), .pin15(_74245_12_pin15), .pin16(_74245_12_pin16),
    .pin17(_74245_12_pin17), .pin18(_74245_12_pin18), .pin19(_74245_11_pin19), .pin20(1'b1));
  _74541 _74541_7 (
    .pin1(1'b0), .pin2(F6), .pin3(B16), .pin4(E12), .pin5(1'b0), .pin6(1'b0), .pin7(1'b0), .pin8(1'b0),
    .pin9(1'b0), .pin10(1'b0), .pin16(_74541_7_pin16), .pin17(_74541_7_pin17), .pin18(_74541_7_pin18),
    .pin19(1'b0), .pin20(1'b1));  // open: pin11, pin12, pin13, pin14, pin15
  LED F (.in(_74541_7_pin18));
  LED R (.in(_74541_7_pin17));
  LED b___eq__0 (.in(_74541_7_pin16));
  LED u_OP_1_DISABLE (.in(OP_1_disable));
  LED led_67 (.in(B15));
  LED led_68 (.in(B14));
  LED led_69 (.in(B13));
  LED led_70 (.in(B12));
  LED led_71 (.in(B11));
  LED led_72 (.in(B10));
  LED led_73 (.in(C3));
  LED led_74 (.in(F1));
  LED led_75 (.in(E13));
  LED led_76 (.in(B9));
  LED led_77 (.in(F10));
  LED led_78 (.in(F2));
  LED led_79 (.in(F5));
  LED led_80 (.in(F3));
  LED led_81 (.in(F4));
  LED led_82 (.in(F7));
  LED led_83 (.in(F6));
  _7410 _7410_1 (
    .pin1(_7410_1_pin1), .pin2(_7410_1_pin1), .pin3(D19), .pin4(OP_1_disable), .pin5(D13),
    .pin6(_7410_1_pin1), .pin7(1'b0), .pin8(_7410_1_pin8), .pin9(OP_1_disable), .pin10(OP_1_disable),
    .pin11(OP_1_disable), .pin12(D1), .pin13(_7410_1_pin1), .pin14(1'b1));
  LED led_84 (.in(_74245_10_pin14[1]));
  LED led_85 (.in(_74245_10_pin14[2]));
  LED led_86 (.in(_74245_10_pin18[3]));
  LED led_87 (.in(_74245_10_pin14[0]));
  LED led_88 (.in(_74245_10_pin18[1]));
  LED led_89 (.in(_74245_10_pin18[2]));
  _7427 _7427_3 (
    .pin1(_7408_4_pin3), .pin2(_7408_6_pin11), .pin3(_7408_7_pin3), .pin4(_7408_4_pin11),
    .pin5(_7427_3_pin5), .pin6(_7427_3_pin6), .pin7(1'b0), .pin8(_7427_3_pin8), .pin9(_7408_4_pin8),
    .pin10(_7408_7_pin6), .pin11(_7427_3_pin11), .pin12(_7427_3_pin12), .pin13(_7427_3_pin13), .pin14(1'b1));
  LED led_90 (.in(_74245_9_pin14[3]));
  LED led_91 (.in(_74245_10_pin18[0]));
  LED led_92 (.in(_74245_9_pin14[1]));
  LED led_93 (.in(_74245_9_pin14[2]));
  LED led_94 (.in(_74245_9_pin18[3]));
  LED led_95 (.in(_74245_9_pin14[0]));
  _74245 _74245_13 (
    .pin1(1'b0), .pin2(_74245_11_pin18), .pin3(_74245_11_pin17), .pin4(_74245_11_pin16),
    .pin5(_74245_11_pin15), .pin6(_74245_11_pin14), .pin7(_74245_11_pin13), .pin8(_74245_11_pin12),
    .pin9(_74245_11_pin11), .pin10(1'b0), .pin11(H24), .pin12(H25), .pin13(H26), .pin14(H27), .pin15(H28),
    .pin16(H29), .pin17(H30), .pin18(H31), .pin19(_74245_13_pin19), .pin20(1'b1));
  _74245 _74245_14 (
    .pin1(1'b0), .pin2(_74245_12_pin18), .pin3(_74245_12_pin17), .pin4(_74245_12_pin16),
    .pin5(_74245_12_pin15), .pin6(_74245_12_pin14), .pin7(_74245_12_pin13), .pin8(_74245_12_pin12),
    .pin9(_74245_12_pin11), .pin10(1'b0), .pin11(1'b0), .pin12(H17), .pin13(H18), .pin14(H19), .pin15(H20),
    .pin16(H21), .pin17(H22), .pin18(H23), .pin19(_74245_13_pin19), .pin20(1'b1));
  _74245 _74245_15 (
    .pin1(1'b0), .pin2(_74245_11_pin18), .pin3(_74245_11_pin17), .pin4(_74245_11_pin16),
    .pin5(_74245_11_pin15), .pin6(_74245_11_pin14), .pin7(_74245_11_pin13), .pin8(_74245_11_pin12),
    .pin9(_74245_11_pin11), .pin10(1'b0), .pin11(H9), .pin12(H10), .pin13(H11), .pin14(H12), .pin15(H13),
    .pin16(H14), .pin17(H15), .pin18(H16), .pin19(_74245_15_pin19), .pin20(1'b1));
  _74245 _74245_16 (
    .pin1(1'b0), .pin2(_74245_12_pin18), .pin3(_74245_12_pin17), .pin4(_74245_12_pin16),
    .pin5(_74245_12_pin15), .pin6(_74245_12_pin14), .pin7(_74245_12_pin13), .pin8(_74245_12_pin12),
    .pin9(_74245_12_pin11), .pin10(1'b0), .pin11(H1), .pin12(H2), .pin13(H3), .pin14(H4), .pin15(H5),
    .pin16(H6), .pin17(H7), .pin18(H8), .pin19(_74245_15_pin19), .pin20(1'b1));
  _7404 _7404_9 (
    .pin1(F4), .pin2(_7404_9_pin2), .pin3(F5), .pin4(_74245_11_pin19), .pin5(1'b0), .pin7(1'b0),
    .pin8(_74245_15_pin19), .pin9(F2), .pin10(_74245_13_pin19), .pin11(F1), .pin13(1'b0), .pin14(1'b1));  // open: pin6, pin12
  LED led_96 (.in(_74245_9_pin18[1]));
  LED led_97 (.in(_74245_9_pin18[2]));
  LED led_98 (.in(_74245_9_pin18[0]));
  Seven_Seg_Hex seven_seg_hex_37 (.d({1'b0, _74245_10_pin14}), .dp(1'b0));
  _7408 _7408_8 (
    .pin1(D13), .pin2(_7410_1_pin8), .pin3(_7408_8_pin3), .pin4(_74260_1_pin6), .pin5(_7408_8_pin3),
    .pin6(_7427_3_pin13), .pin7(1'b0), .pin8(F2), .pin9(_7432_1_pin6), .pin10(_7408_8_pin3), .pin12(1'b0),
    .pin13(1'b0), .pin14(1'b1));  // open: pin11
  Seven_Seg_Hex seven_seg_hex_38 (.d(_74245_10_pin18), .dp(1'b0));
  Seven_Seg_Hex seven_seg_hex_39 (.d(_74245_9_pin14), .dp(1'b0));
  Seven_Seg_Hex seven_seg_hex_40 (.d(_74245_9_pin18), .dp(1'b0));
  _7404 _7404_10 (
    .pin1(_7427_3_pin6), .pin2(F3), .pin3(_7427_3_pin12), .pin4(F6), .pin5(_7427_3_pin8), .pin6(F4),
    .pin7(1'b0), .pin8(F7), .pin9(_7404_10_pin9), .pin11(1'b0), .pin13(1'b0), .pin14(1'b1));  // open: pin10, pin12
  _74373 _74373_1 (
    .pin1(_7404_9_pin2), .pin2(_74245_9_pin18[0]), .pin3(_74245_11_pin18), .pin4(_74245_11_pin17),
    .pin5(_74245_9_pin18[1]), .pin6(_74245_9_pin18[2]), .pin7(_74245_11_pin16), .pin8(_74245_11_pin15),
    .pin9(_74245_9_pin18[3]), .pin10(1'b0), .pin11(F3), .pin12(_74245_9_pin14[0]), .pin13(_74245_11_pin14),
    .pin14(_74245_11_pin13), .pin15(_74245_9_pin14[1]), .pin16(_74245_9_pin14[2]), .pin17(_74245_11_pin12),
    .pin18(_74245_11_pin11), .pin19(_74245_9_pin14[3]), .pin20(1'b1));
  _7427 _7427_4 (
    .pin1(1'b0), .pin2(1'b0), .pin3(_7408_7_pin11), .pin4(_7408_5_pin3), .pin5(_7427_4_pin5),
    .pin6(_7404_10_pin9), .pin7(1'b0), .pin9(1'b0), .pin10(1'b0), .pin11(1'b0), .pin13(1'b0), .pin14(1'b1));  // open: pin8, pin12
  _7408 _7408_9 (
    .pin1(D15), .pin2(_7408_8_pin3), .pin3(_7427_4_pin5), .pin4(_7432_1_pin8), .pin5(_7408_8_pin3),
    .pin6(_7427_3_pin11), .pin7(1'b0), .pin8(_7427_3_pin5), .pin9(D17), .pin10(_7408_8_pin3), .pin11(B16),
    .pin12(D7), .pin13(D19), .pin14(1'b1));
  _74373 _74373_2 (
    .pin1(_7404_9_pin2), .pin2(_74245_10_pin18[0]), .pin3(_74245_12_pin18), .pin4(_74245_12_pin17),
    .pin5(_74245_10_pin18[1]), .pin6(_74245_10_pin18[2]), .pin7(_74245_12_pin16), .pin8(_74245_12_pin15),
    .pin9(_74245_10_pin18[3]), .pin10(1'b0), .pin11(F3), .pin12(_74245_10_pin14[0]), .pin13(_74245_12_pin14),
    .pin14(_74245_12_pin13), .pin15(_74245_10_pin14[1]), .pin16(_74245_10_pin14[2]), .pin17(_74245_12_pin12),
    .pin18(_74245_12_pin11), .pin20(1'b1));  // open: pin19
  DipSwitch S3 (.out(S3_out));
  DipSwitch #(.dipDefault("true")) S2 (.out(S2_out));
  DipSwitch #(.dipDefault("true")) S1 (.out(S1_out));
  DipSwitch S0 (.out(S0_out));
  DipSwitch Cn (.out(Cn_out));
  DipSwitch M_2 (.out(M_2_out));
  _7404 _7404_11 (
    .pin1(S0_out), .pin2(_7404_11_pin2), .pin3(S1_out), .pin4(_7404_11_pin4), .pin5(S2_out),
    .pin6(_7404_11_pin6), .pin7(1'b0), .pin8(_7404_11_pin8), .pin9(Cn_out), .pin10(_7404_11_pin10),
    .pin11(M_2_out), .pin12(_7404_11_pin12), .pin13(S3_out), .pin14(1'b1));
  DipSwitch gamma_0 (.out(gamma_0_out[0]));
  DipSwitch #(.dipDefault("true")) gamma_1 (.out(gamma_0_out[1]));
  DipSwitch gamma_2 (.out(gamma_0_out[2]));
  _7408 _7408_10 (
    .pin1(_7404_11_pin2), .pin2(S1_out), .pin3(_7408_10_pin3), .pin4(_7404_11_pin12), .pin5(S2_out),
    .pin6(_7408_10_pin6), .pin7(1'b0), .pin8(_7408_10_pin8), .pin9(_7404_11_pin10), .pin10(_7404_11_pin8),
    .pin11(_7408_10_pin11), .pin12(_7404_11_pin4), .pin13(S0_out), .pin14(1'b1));
  _7411 _7411_6 (
    .pin1(_7404_11_pin6), .pin2(S3_out), .pin3(_7404_11_pin10), .pin4(Cn_out), .pin5(Cn_out),
    .pin6(_7411_6_pin6), .pin7(1'b0), .pin8(_7411_6_pin8), .pin9(_7411_6_pin6), .pin10(_7408_10_pin11),
    .pin11(_7411_6_pin11), .pin12(_7411_6_pin11), .pin13(_7404_11_pin6), .pin14(1'b1));
  Seven_Seg_Hex seven_seg_hex_41 (.d({1'b0, gamma_0_out}), .dp(1'b0));
  _7411 _7411_7 (
    .pin1(_7404_11_pin2), .pin2(_7411_7_pin2), .pin3(M_2_out), .pin4(S2_out), .pin5(_7404_11_pin12),
    .pin6(_7411_7_pin2), .pin7(1'b0), .pin8(_7411_7_pin8), .pin9(_7408_10_pin6), .pin10(_7408_10_pin3),
    .pin11(_7408_10_pin8), .pin12(_7411_7_pin12), .pin13(S1_out), .pin14(1'b1));
  Seven_Seg_Hex seven_seg_hex_42 (.d({2'b00, H41, H42}), .dp(1'b0));
  Seven_Seg_Hex seven_seg_hex_43 (.d({H1, H2, H3, H4}), .dp(1'b0));
  Seven_Seg_Hex seven_seg_hex_44 (.d({H5, H6, H7, H8}), .dp(1'b0));
  Seven_Seg_Hex seven_seg_hex_45 (.d({H43, H44, H45, H46}), .dp(1'b0));
  Seven_Seg_Hex seven_seg_hex_46 (.d({H9, H10, H11, H12}), .dp(1'b0));
  DipSwitch #(.dipDefault("true")) alpha_0 (.out(alpha_0_out[0]));
  DipSwitch alpha_1 (.out(alpha_0_out[1]));
  DipSwitch alpha_2 (.out(alpha_0_out[2]));
  DipSwitch alpha_3 (.out(alpha_0_out[3]));
  DipSwitch alpha_4 (.out(alpha_4_out[0]));
  DipSwitch alpha_5 (.out(alpha_4_out[1]));
  DipSwitch alpha_6 (.out(alpha_4_out[2]));
  DipSwitch alpha_7 (.out(alpha_4_out[3]));
  DipSwitch alpha_8 (.out(alpha_8_out[0]));
  DipSwitch alpha_9 (.out(alpha_8_out[1]));
  _6_x_10_bit_multiply_version_K_19_feb_2022 _6_x_10_bit_multiply_version_k_19_feb_2022_1 (
    .A0(H46), .A1(H45), .A2(H44), .A3(H43), .A4(H42), .A5(H41), .B0(C13), .B1(C12), .B2(C11), .B3(C10),
    .B4(C9), .B5(C8), .B6(C7), .B7(C6), .B8(C5), .B9(C4), .P0(H16), .P1(H15), .P2(H14), .P3(H13), .P4(H12),
    .P5(H11), .P6(H10), .P7(H9), .P8(H8), .P9(H7), .P10(H6), .P11(H5), .P12(H4), .P13(H3), .P14(H2), .P15(H1));
  Seven_Seg_Hex seven_seg_hex_47 (.d({H13, H14, H15, H16}), .dp(1'b0));
  Seven_Seg_Hex seven_seg_hex_48 (.d({2'b00, alpha_8_out}), .dp(1'b0));
  Seven_Seg_Hex seven_seg_hex_49 (.d(alpha_4_out), .dp(1'b0));
  Seven_Seg_Hex seven_seg_hex_50 (.d({2'b00, C4, C5}), .dp(1'b0));
  _74541 _74541_8 (
    .pin1(1'b0), .pin2(_74541_8_pin2), .pin3(_7411_7_pin12), .pin4(_7411_7_pin8), .pin5(_7411_6_pin8),
    .pin6(1'b0), .pin7(1'b0), .pin8(_74541_8_pin8), .pin9(_74541_8_pin9), .pin10(1'b0),
    .pin11(_74541_8_pin11), .pin12(_74541_8_pin12), .pin15(_74541_8_pin15), .pin16(_74541_8_pin16),
    .pin17(_74541_8_pin17), .pin18(_74541_8_pin18), .pin19(1'b0), .pin20(1'b1));  // open: pin13, pin14
  Seven_Seg_Hex seven_seg_hex_51 (.d(alpha_0_out), .dp(1'b0));
  Seven_Seg_Hex seven_seg_hex_52 (.d({C6, C7, C8, C9}), .dp(1'b0));
  _3_x_10_bit_multiply_version_E_19_feb_2022 _3_x_10_bit_multiply_version_e_19_feb_2022_1 (
    .A0(gamma_0_out[0]), .A1(gamma_0_out[1]), .A2(gamma_0_out[2]), .B0(C13), .B1(C12), .B2(C11), .B3(C10),
    .B4(C9), .B5(C8), .B6(C7), .B7(C6), .B8(C5), .B9(C4),
    .P0(_3_x_10_bit_multiply_version_e_19_feb_2022_1_p0),
    .P1(_3_x_10_bit_multiply_version_e_19_feb_2022_1_p1),
    .P2(_3_x_10_bit_multiply_version_e_19_feb_2022_1_p2),
    .P3(_3_x_10_bit_multiply_version_e_19_feb_2022_1_p3),
    .P4(_3_x_10_bit_multiply_version_e_19_feb_2022_1_p4),
    .P5(_3_x_10_bit_multiply_version_e_19_feb_2022_1_p5),
    .P6(_3_x_10_bit_multiply_version_e_19_feb_2022_1_p6),
    .P7(_3_x_10_bit_multiply_version_e_19_feb_2022_1_p7),
    .P8(_3_x_10_bit_multiply_version_e_19_feb_2022_1_p8),
    .P9(_3_x_10_bit_multiply_version_e_19_feb_2022_1_p9),
    .P10(_3_x_10_bit_multiply_version_e_19_feb_2022_1_p10),
    .P11(_3_x_10_bit_multiply_version_e_19_feb_2022_1_p11), .P12(_74541_8_pin2));
  Seven_Seg_Hex seven_seg_hex_53 (.d({C10, C11, C12, C13}), .dp(1'b0));
  LED OVERFLOW (.in(_74541_8_pin18));
  LED XOR_3 (.in(_74541_8_pin17));
  LED A_MINUS_B_3 (.in(_74541_8_pin16));
  LED A_PLUS_B_3 (.in(_74541_8_pin15));
  LED g__eq__0 (.in(_74541_8_pin12));
  LED RESET (.in(_74541_8_pin11));
  _74181 _74181_5 (
    .pin1(alpha_0_out[0]), .pin2(_3_x_10_bit_multiply_version_e_19_feb_2022_1_p0), .pin3(S3_out),
    .pin4(S2_out), .pin5(S1_out), .pin6(S0_out), .pin7(Cn_out), .pin8(M_2_out), .pin9(_74181_5_pin9[0]),
    .pin10(C23), .pin11(C22), .pin12(1'b0));  // open: pin13, pin14, pin15, pin16, pin17, pin18, pin19, pin20, pin21, pin22, pin23, pin24
  LED led_99 (.in(undriven));
  LED led_100 (.in(undriven_2));
  _7432 _7432_2 (
    .pin1(C20), .pin2(C19), .pin3(_7432_2_pin3), .pin4(C18), .pin5(C17), .pin6(_7432_2_pin6), .pin7(1'b0),
    .pin8(_7432_2_pin8), .pin9(C21), .pin10(C22), .pin11(_7432_2_pin11), .pin12(C23),
    .pin13(_74181_5_pin9[0]), .pin14(1'b1));
  _7432 _7432_3 (
    .pin1(_7432_2_pin6), .pin2(_7432_2_pin3), .pin3(_7432_3_pin3), .pin4(1'b0), .pin5(1'b0), .pin7(1'b0),
    .pin8(_7432_3_pin8), .pin9(_7432_3_pin3), .pin10(_7432_3_pin10), .pin11(_7432_3_pin10),
    .pin12(_7432_2_pin11), .pin13(_7432_2_pin8), .pin14(1'b1));  // open: pin6
  _74181 _74181_6 (
    .pin1(alpha_4_out[0]), .pin2(_3_x_10_bit_multiply_version_e_19_feb_2022_1_p4), .pin3(S3_out),
    .pin4(S2_out), .pin5(S1_out), .pin6(S0_out), .pin7(_74181_6_pin7), .pin8(M_2_out), .pin9(C20),
    .pin10(C19), .pin11(C18), .pin12(1'b0));  // open: pin13, pin14, pin15, pin16, pin17, pin18, pin19, pin20, pin21, pin22, pin23, pin24
  _7432 _7432_4 (
    .pin1(C16), .pin2(C15), .pin3(_7432_4_pin3), .pin4(_7432_4_pin3), .pin5(C14), .pin6(_7432_4_pin6),
    .pin7(1'b0), .pin8(_7432_4_pin8), .pin9(_7432_4_pin6), .pin10(_7432_3_pin8), .pin11(C24),
    .pin12(_74541_8_pin8), .pin13(_74181_5_pin9[0]), .pin14(1'b1));
  LED led_101 (.in(undriven_3));
  LED led_102 (.in(undriven_4));
  _15_bit_div_11_bit_blocked_version_E_05_feb_2022 _15_bit_div_11_bit_blocked_version_e_05_feb_2022_1 (
    .N0(H46), .N1(H45), .N2(H44), .N3(H43), .N4(H42), .N5(H41), .N6(H40), .N7(H39), .N8(H38), .N9(H37),
    .N10(H36), .N11(H35), .N12(H34), .N13(H33), .N14(H32), .D0(C24), .D1(C23), .D2(C22), .D3(C21), .D4(C20),
    .D5(C19), .D6(C18), .D7(C17), .D8(C16), .D9(C15), .D10(C14), .Q0(H31), .Q1(H30), .Q2(H29), .Q3(H28),
    .Q4(H27), .Q5(H26), .Q6(H25), .Q7(H24), .Q8(H23), .Q9(H22), .Q10(H21), .Q11(H20), .Q12(H19), .Q13(H18),
    .Q14(H17), .R0(E24), .R1(E23), .R2(E22), .R3(E21), .R4(E20), .R5(E19), .R6(E18), .R7(E17), .R8(E16),
    .R9(E15), .R10(E14));
  _74181 _74181_7 (
    .pin1(alpha_8_out[0]), .pin2(_3_x_10_bit_multiply_version_e_19_feb_2022_1_p8), .pin3(S3_out),
    .pin4(S2_out), .pin5(S1_out), .pin6(S0_out), .pin7(_74181_7_pin7), .pin8(M_2_out), .pin9(C16),
    .pin10(C15), .pin11(C14), .pin12(1'b0));  // open: pin13, pin14, pin15, pin16, pin17, pin18, pin19, pin20, pin21, pin22, pin23, pin24
  Seven_Seg_Hex seven_seg_hex_54 (.d({2'b00, C4, C5}), .dp(1'b0));
  Seven_Seg_Hex seven_seg_hex_55 (.d({C6, C7, C8, C9}), .dp(1'b0));
  _74182 _74182_2 (
    .pin1(_74182_2_pin1), .pin2(_74182_2_pin2), .pin3(_74182_2_pin3), .pin4(_74182_2_pin4), .pin5(1'b0),
    .pin6(1'b0), .pin7(_74182_2_pin7), .pin8(1'b0), .pin9(_74182_2_pin9), .pin10(_74182_2_pin10),
    .pin11(_74181_7_pin7), .pin12(_74181_6_pin7), .pin13(Cn_out), .pin14(_74182_2_pin14),
    .pin15(_74182_2_pin15), .pin16(1'b1));
  LED led_103 (.in(_74182_2_pin7));
  LED led_104 (.in(undriven_5));
  LED led_105 (.in(undriven_6));
  LED led_106 (.in(undriven_7));
  Seven_Seg_Hex seven_seg_hex_56 (.d({C10, C11, C12, C13}), .dp(1'b0));
  LED led_107 (.in(_74182_2_pin10));
  LED led_108 (.in(_74182_2_pin9));
  _74191 _74191_1 (
    .pin1(_74191_1_pin1), .pin2(C12), .pin3(C13), .pin4(1'b0), .pin5(_74191_1_pin5), .pin6(C11), .pin7(C10),
    .pin8(1'b0), .pin9(_74191_1_pin9), .pin10(_74191_1_pin10), .pin11(_74191_1_pin11),
    .pin13(_74191_1_pin13), .pin14(C3), .pin15(_74191_1_pin15), .pin16(1'b1));  // open: pin12
  PullUp pullup_22 (.out(_74191_1_pin5));
  _74191 _74191_2 (
    .pin1(_74191_2_pin1), .pin2(C8), .pin3(C9), .pin4(1'b0), .pin5(_74191_2_pin5), .pin6(C7), .pin7(C6),
    .pin8(1'b0), .pin9(_74191_2_pin9), .pin10(_74191_2_pin10), .pin11(_74191_1_pin11),
    .pin13(_74191_2_pin13), .pin14(_74191_1_pin13), .pin15(_74191_2_pin15), .pin16(1'b1));  // open: pin12
  PullUp pullup_23 (.out(_74191_2_pin5));
  _74191 _74191_3 (
    .pin1(_74191_3_pin1), .pin2(C4), .pin3(C5), .pin4(1'b0), .pin5(_74191_3_pin5), .pin8(1'b0), .pin9(1'b0),
    .pin10(1'b0), .pin11(_74191_1_pin11), .pin14(_74191_2_pin13), .pin15(_74191_3_pin15), .pin16(1'b1));  // open: pin6, pin7, pin12, pin13
  PullUp pullup_24 (.out(_74191_3_pin5));
  Seven_Seg_Hex seven_seg_hex_57 (.d({1'b0, C14, C15, C16}), .dp(1'b0));
  Seven_Seg_Hex seven_seg_hex_58 (.d({C17, C18, C19, C20}), .dp(1'b0));
  Seven_Seg_Hex seven_seg_hex_59 (.d({2'b00, H41, H42}), .dp(1'b0));
  Seven_Seg_Hex seven_seg_hex_60 (.d({C21, C22, C23, _74181_5_pin9[0]}), .dp(1'b0));
  Seven_Seg_Hex seven_seg_hex_61 (.d({H43, H44, H45, H46}), .dp(1'b0));
  DipSwitch #(.dipDefault("true")) b8 (.out(_74191_3_pin15));
  DipSwitch #(.dipDefault("true")) u_b9 (.out(_74191_3_pin1));
  DipSwitch #(.dipDefault("true")) u_b6 (.out(_74191_2_pin10));
  DipSwitch u_b7 (.out(_74191_2_pin9));
  DipSwitch #(.dipDefault("true")) u_b4 (.out(_74191_2_pin15));
  DipSwitch #(.dipDefault("true")) u_b5 (.out(_74191_2_pin1));
  DipSwitch u_b2 (.out(_74191_1_pin10));
  DipSwitch #(.dipDefault("true")) u_b3 (.out(_74191_1_pin9));
  DipSwitch b0 (.out(_74191_1_pin15));
  DipSwitch u_b1 (.out(_74191_1_pin1));
  _7402 _7402_1 (
    .pin2(1'b0), .pin3(1'b0), .pin4(_74541_8_pin8), .pin5(_7432_4_pin8), .pin6(_7432_4_pin8), .pin7(1'b0),
    .pin8(A15), .pin9(A15), .pin10(_74541_8_pin9), .pin11(_74541_8_pin9), .pin12(B9), .pin13(_74191_1_pin11),
    .pin14(1'b1));  // open: pin1
  _6_bit_div_ten_version_I_06_feb_2022 _6_bit_div_ten_version_i_06_feb_2022_1 (
    .A0(H46), .A1(H45), .A2(H44), .A3(H43), .A4(H42), .A5(H41), .Q0(B7), .Q1(B6), .Q2(B5), .R0(B4), .R1(B3),
    .R2(B2), .R3(B1));
  LED led_109 (.in(_74283_1_pin11[2]));
  LED led_110 (.in(_74283_1_pin11[3]));
  LED led_111 (.in(_74283_1_pin11[0]));
  LED led_112 (.in(_74283_1_pin11[1]));
  Seven_Seg_Hex seven_seg_hex_62 (.d(_74283_1_pin11), .dp(1'b0));
  _74247 _74247_1 (
    .pin1(_74247_1_pin1), .pin2(_74247_1_pin2), .pin3(_74247_1_pin3), .pin4(_74247_1_pin3),
    .pin5(_74247_1_pin3), .pin6(_74247_1_pin6), .pin7(_74247_1_pin7), .pin8(1'b0), .pin9(_74247_1_pin9),
    .pin10(_74247_1_pin10), .pin11(_74247_1_pin11), .pin12(_74247_1_pin12), .pin13(_74247_1_pin13),
    .pin14(_74247_1_pin14), .pin15(_74247_1_pin15), .pin16(1'b1));
  PullUp pullup_25 (.out(_74247_1_pin3));
  _74160 _74160_1 (
    .pin1(A15), .pin2(A5), .pin3(1'b0), .pin4(1'b0), .pin5(1'b0), .pin6(1'b0), .pin7(_74160_1_pin7),
    .pin8(1'b0), .pin9(_74247_1_pin3), .pin10(_74160_1_pin10), .pin11(_74247_1_pin6), .pin12(_74247_1_pin2),
    .pin13(_74247_1_pin1), .pin14(_74247_1_pin7), .pin16(1'b1));  // open: pin15
  Seven_Seg #(.commonCathode("true"), .commonConnectionType("anode")) seven_seg_1 (
    .a(_74247_1_pin13), .b(_74247_1_pin12), .c(_74247_1_pin11), .d(_74247_1_pin10), .e(_74247_1_pin9),
    .f(_74247_1_pin15), .g(_74247_1_pin14), .dp(1'b1), .common(1'b1));
  _74283 _74283_1 (
    .pin1(_74283_1_pin1), .pin2(_74283_1_pin11[1]), .pin3(B6), .pin4(_74283_1_pin4), .pin5(B7),
    .pin6(_74283_1_pin11[0]), .pin7(1'b0), .pin8(1'b0), .pin10(_74283_1_pin10), .pin11(_74283_1_pin11[3]),
    .pin12(1'b0), .pin13(_74283_1_pin13), .pin14(B5), .pin15(_74283_1_pin11[2]), .pin16(1'b1));  // open: pin9
  PullUp pullup_26 (.out(_74160_1_pin7));
  Seven_Seg #(.commonCathode("true"), .commonConnectionType("anode")) seven_seg_2 (
    .a(_74247_2_pin13), .b(_74247_2_pin12), .c(_74247_2_pin11), .d(_74247_2_pin10), .e(_74247_2_pin9),
    .f(_74247_2_pin15), .g(_74247_2_pin14), .dp(1'b1), .common(1'b1));
  _74247 _74247_2 (
    .pin1(_74247_2_pin1), .pin2(_74247_2_pin2), .pin3(_74247_1_pin3), .pin4(_74247_1_pin3),
    .pin5(_74247_1_pin3), .pin6(_74247_2_pin6), .pin7(_74247_2_pin7), .pin8(1'b0), .pin9(_74247_2_pin9),
    .pin10(_74247_2_pin10), .pin11(_74247_2_pin11), .pin12(_74247_2_pin12), .pin13(_74247_2_pin13),
    .pin14(_74247_2_pin14), .pin15(_74247_2_pin15), .pin16(1'b1));
  _74160 _74160_2 (
    .pin1(A15), .pin2(A5), .pin3(1'b0), .pin4(1'b0), .pin5(1'b0), .pin6(1'b0), .pin7(_74160_2_pin7),
    .pin8(1'b0), .pin9(_74247_1_pin3), .pin10(_74160_2_pin10), .pin11(_74247_2_pin6), .pin12(_74247_2_pin2),
    .pin13(_74247_2_pin1), .pin14(_74247_2_pin7), .pin15(_74160_1_pin10), .pin16(1'b1));
  LED led_113 (.in(_7400_3_pin2));
  _7400 _7400_3 (
    .pin1(display_ripple_clock), .pin2(_7400_3_pin2), .pin3(_7400_3_pin3), .pin4(_7400_3_pin3),
    .pin5(_7400_3_pin3), .pin6(_7400_3_pin6), .pin7(1'b0), .pin9(1'b0), .pin10(1'b0), .pin11(_7400_3_pin11),
    .pin12(A14), .pin13(A14), .pin14(1'b1));  // open: pin8
  _7474 _7474_2 (
    .pin1(1'b0), .pin2(1'b0), .pin3(1'b0), .pin4(1'b0), .pin7(1'b0), .pin9(_7400_3_pin2),
    .pin10(_7474_2_pin10), .pin11(A5), .pin12(_7474_2_pin12), .pin13(_7474_2_pin13), .pin14(1'b1));  // open: pin5, pin6, pin8
  PullUp pullup_27 (.out(pullup_27_out));
  PullUp pullup_28 (.out(_74160_2_pin7));
  _74273 _74273_1 (
    .pin1(pullup_27_out), .pin2(_74273_1_pin2[0]), .pin3(_74283_1_pin4), .pin4(_74283_1_pin1),
    .pin5(_74273_1_pin2[1]), .pin6(_74273_1_pin2[2]), .pin7(_74283_1_pin13), .pin8(_74283_1_pin10),
    .pin9(_74273_1_pin2[3]), .pin10(1'b0), .pin11(B16), .pin13(1'b0), .pin14(1'b0), .pin17(1'b0),
    .pin18(1'b0), .pin20(1'b1));  // open: pin12, pin15, pin16, pin19
  PullUp pullup_29 (.out(_7474_2_pin12));
  PullUp pullup_30 (.out(_7474_2_pin10));
  Seven_Seg #(.commonCathode("true"), .commonConnectionType("anode")) seven_seg_3 (
    .a(_74247_3_pin13), .b(_74247_3_pin12), .c(_74247_3_pin11), .d(_74247_3_pin10), .e(_74247_3_pin9),
    .f(_74247_3_pin15), .g(_74247_3_pin14), .dp(1'b1), .common(1'b1));
  _74247 _74247_3 (
    .pin1(_74247_3_pin1), .pin2(_74247_3_pin2), .pin3(_74247_3_pin3), .pin4(_74247_3_pin3),
    .pin5(_74247_3_pin3), .pin6(_74247_3_pin6), .pin7(_74247_3_pin7), .pin8(1'b0), .pin9(_74247_3_pin9),
    .pin10(_74247_3_pin10), .pin11(_74247_3_pin11), .pin12(_74247_3_pin12), .pin13(_74247_3_pin13),
    .pin14(_74247_3_pin14), .pin15(_74247_3_pin15), .pin16(1'b1));
  _74160 _74160_3 (
    .pin1(A15), .pin2(A5), .pin3(1'b0), .pin4(1'b0), .pin5(1'b0), .pin6(1'b0), .pin7(_74160_3_pin7),
    .pin8(1'b0), .pin9(_74247_3_pin3), .pin10(_74160_3_pin10), .pin11(_74247_3_pin6), .pin12(_74247_3_pin2),
    .pin13(_74247_3_pin1), .pin14(_74247_3_pin7), .pin15(_74160_2_pin10), .pin16(1'b1));
  PullUp pullup_31 (.out(pullup_31_out));
  LED l__carry (.in(_7485_1_pin6));
  _74161 _74161_7 (
    .pin1(_7400_3_pin11), .pin2(_7400_3_pin6), .pin3(1'b0), .pin4(1'b0), .pin5(1'b0), .pin6(1'b0),
    .pin7(_74161_7_pin7), .pin8(1'b0), .pin9(_74161_7_pin9), .pin10(_74161_7_pin9), .pin12(_74161_7_pin12),
    .pin13(_74161_7_pin13), .pin14(_74161_7_pin14), .pin16(1'b1));  // open: pin11, pin15
  PullUp pullup_32 (.out(_74161_7_pin7));
  _74273 e__0_3 (
    .pin1(A15), .pin2(_74283_1_pin11[0]), .pin3(e__0_3_pin3), .pin4(e__0_3_pin4), .pin5(_74283_1_pin11[1]),
    .pin6(_74283_1_pin11[2]), .pin7(e__0_3_pin7), .pin8(e__0_3_pin8), .pin9(_74283_1_pin11[3]), .pin10(1'b0),
    .pin11(B10), .pin13(1'b0), .pin14(1'b0), .pin17(1'b0), .pin18(1'b0), .pin20(1'b1));  // open: pin12, pin15, pin16, pin19
  PullUp pullup_33 (.out(pullup_33_out));
  _7485 _7485_1 (
    .pin1(pullup_33_out), .pin2(1'b0), .pin3(pullup_31_out), .pin4(1'b0), .pin6(_7485_1_pin6), .pin8(1'b0),
    .pin9(1'b0), .pin10(_74273_1_pin2[0]), .pin11(_7485_1_pin11), .pin12(_74273_1_pin2[1]),
    .pin13(_74273_1_pin2[2]), .pin14(1'b0), .pin15(_74273_1_pin2[3]), .pin16(1'b1));  // open: pin5, pin7
  _7407 _7407_1 (
    .pin1(_7407_1_pin1), .pin2(_7407_1_pin2), .pin3(_7407_1_pin3), .pin4(_7407_1_pin4), .pin5(_7407_1_pin5),
    .pin6(_7407_1_pin6), .pin7(1'b0), .pin8(_7407_1_pin8), .pin9(_7407_1_pin9), .pin10(_7407_1_pin10),
    .pin11(_7407_1_pin11), .pin12(_7407_1_pin12), .pin13(_7407_1_pin13), .pin14(1'b1));
  PullUp pullup_34 (.out(_74160_3_pin7));
  Seven_Seg #(.commonCathode("true"), .commonConnectionType("anode")) seven_seg_4 (
    .a(_74247_4_pin13), .b(_74247_4_pin12), .c(_74247_4_pin11), .d(_74247_4_pin10), .e(_74247_4_pin9),
    .f(_74247_4_pin15), .g(_74247_4_pin14), .dp(1'b1), .common(1'b1));
  _74247 _74247_4 (
    .pin1(_74247_4_pin1), .pin2(_74247_4_pin2), .pin3(_74247_4_pin3), .pin4(_74247_4_pin3),
    .pin5(_74247_4_pin3), .pin6(_74247_4_pin6), .pin7(_74247_4_pin7), .pin8(1'b0), .pin9(_74247_4_pin9),
    .pin10(_74247_4_pin10), .pin11(_74247_4_pin11), .pin12(_74247_4_pin12), .pin13(_74247_4_pin13),
    .pin14(_74247_4_pin14), .pin15(_74247_4_pin15), .pin16(1'b1));
  _74160 _74160_4 (
    .pin1(A15), .pin2(A5), .pin3(1'b0), .pin4(1'b0), .pin5(1'b0), .pin6(1'b0), .pin7(_74160_4_pin7),
    .pin8(1'b0), .pin9(_74247_4_pin3), .pin10(_74247_4_pin3), .pin11(_74247_4_pin6), .pin12(_74247_4_pin2),
    .pin13(_74247_4_pin1), .pin14(_74247_4_pin7), .pin15(_74160_3_pin10), .pin16(1'b1));
  PullUp pullup_35 (.out(pullup_35_out));
  PullUp pullup_36 (.out(_74161_7_pin9));
  _74138 _74138_1 (
    .pin1(_74161_7_pin14), .pin2(_74161_7_pin13), .pin3(_74161_7_pin12), .pin4(1'b0), .pin5(1'b0),
    .pin6(pullup_35_out), .pin7(_7474_2_pin13), .pin8(1'b0), .pin9(_74138_1_pin9), .pin10(_74138_1_pin10),
    .pin11(_74138_1_pin11), .pin12(_74138_1_pin12), .pin13(_74138_1_pin13), .pin14(_74138_1_pin14),
    .pin16(1'b1));  // open: pin15
  PullUp pullup_37 (.out(_7485_1_pin11));
  _7442 _7442_1 (
    .pin2(_7407_1_pin1), .pin3(_7407_1_pin3), .pin4(_7407_1_pin5), .pin5(_7407_1_pin9), .pin6(_7407_1_pin11),
    .pin7(_7407_1_pin13), .pin8(1'b0), .pin12(_74247_4_pin6), .pin13(_74247_4_pin2), .pin14(_74247_4_pin1),
    .pin15(_74247_4_pin7), .pin16(1'b1));  // open: pin1, pin9, pin10, pin11
  PullUp pullup_38 (.out(_74160_4_pin7));
  Seven_Seg_Hex seven_seg_hex_63 (.d(_74273_1_pin2), .dp(1'b0));
  PullUp pullup_39 (.out(_7407_1_pin12));
  PullUp pullup_40 (.out(_7407_1_pin10));
  PullUp pullup_41 (.out(_7407_1_pin8));
  PullUp pullup_42 (.out(_7407_1_pin6));
  PullUp pullup_43 (.out(_7407_1_pin4));
  PullUp pullup_44 (.out(_7407_1_pin2));
  _7404 _7404_12 (
    .pin1(_74138_1_pin14), .pin2(_7404_12_pin2), .pin3(_74138_1_pin13), .pin4(_7404_12_pin4),
    .pin5(_74138_1_pin12), .pin6(_7404_12_pin6), .pin7(1'b0), .pin8(_7404_12_pin8), .pin9(_74138_1_pin11),
    .pin10(_7404_12_pin10), .pin11(_74138_1_pin10), .pin12(_7404_12_pin12), .pin13(_74138_1_pin9),
    .pin14(1'b1));
  _74373 _74373_3 (
    .pin1(1'b0), .pin2(e__0_3_pin3), .pin3(B4), .pin4(B3), .pin5(e__0_3_pin4), .pin6(e__0_3_pin7), .pin7(B2),
    .pin8(B1), .pin9(e__0_3_pin8), .pin10(1'b0), .pin11(B11), .pin13(1'b0), .pin14(1'b0), .pin17(1'b0),
    .pin18(1'b0), .pin20(1'b1));  // open: pin12, pin15, pin16, pin19
  Seven_Seg #(.commonCathode("true"), .commonConnectionType("anode")) seven_seg_5 (
    .a(_74247_5_pin13), .b(_74247_5_pin12), .c(_74247_5_pin11), .d(_74247_5_pin10), .e(_74247_5_pin9),
    .f(_74247_5_pin15), .g(_74247_5_pin14), .dp(_7407_1_pin12), .common(1'b1));
  _74247 _74247_5 (
    .pin1(_74247_5_pin1), .pin2(_74247_5_pin2), .pin3(_74247_5_pin3), .pin4(_74247_5_pin3),
    .pin5(_74247_5_pin3), .pin6(_74247_5_pin6), .pin7(_74247_5_pin7), .pin8(1'b0), .pin9(_74247_5_pin9),
    .pin10(_74247_5_pin10), .pin11(_74247_5_pin11), .pin12(_74247_5_pin12), .pin13(_74247_5_pin13),
    .pin14(_74247_5_pin14), .pin15(_74247_5_pin15), .pin16(1'b1));
  _7477 _7477_1 (
    .Q_0(_74247_5_pin7), .D_0(_74247_8_pin7), .E_0_E_1(_7404_12_pin2), .VCC(1'b1), .GND(1'b0),
    .Q_1(_74247_5_pin1), .D_1(_74247_8_pin1), .Q_2(_74247_5_pin2), .D_2(_74247_8_pin2),
    .E_2_E_3(_7404_12_pin2), .Q_3(_74247_5_pin6), .D_3(_74247_8_pin6));
  PullUp pullup_45 (.out(_74247_5_pin3));
  Seven_Seg #(.commonCathode("true"), .commonConnectionType("anode")) seven_seg_6 (
    .a(_74247_6_pin13), .b(_74247_6_pin12), .c(_74247_6_pin11), .d(_74247_6_pin10), .e(_74247_6_pin9),
    .f(_74247_6_pin15), .g(_74247_6_pin14), .dp(1'b1), .common(1'b1));
  _74247 _74247_6 (
    .pin1(_74247_6_pin1), .pin2(_74247_6_pin2), .pin3(_74247_6_pin3), .pin4(_74247_6_pin3),
    .pin5(_74247_6_pin3), .pin6(_74247_6_pin6), .pin7(_74247_6_pin7), .pin8(1'b0), .pin9(_74247_6_pin9),
    .pin10(_74247_6_pin10), .pin11(_74247_6_pin11), .pin12(_74247_6_pin12), .pin13(_74247_6_pin13),
    .pin14(_74247_6_pin14), .pin15(_74247_6_pin15), .pin16(1'b1));
  _7477 _7477_2 (
    .Q_0(_74247_6_pin7), .D_0(_74247_9_pin7), .E_0_E_1(_7404_12_pin2), .VCC(1'b1), .GND(1'b0),
    .Q_1(_74247_6_pin1), .D_1(_74247_9_pin1), .Q_2(_74247_6_pin2), .D_2(_74247_9_pin2),
    .E_2_E_3(_7404_12_pin2), .Q_3(_74247_6_pin6), .D_3(_74247_9_pin6));
  PullUp pullup_46 (.out(_74247_6_pin3));
  _7400 _7400_4 (
    .pin1(_7485_1_pin6), .pin2(_7485_1_pin6), .pin3(_7400_4_pin3), .pin4(1'b0), .pin5(1'b0), .pin7(1'b0),
    .pin8(_7400_4_pin8), .pin9(_7400_4_pin9), .pin10(_7400_4_pin9), .pin11(_7400_4_pin9), .pin12(B12),
    .pin13(_7485_1_pin6), .pin14(1'b1));  // open: pin6
  _7408 _7408_11 (
    .pin1(_7400_4_pin3), .pin2(_74273_1_pin2[0]), .pin3(_7408_11_pin11[0]), .pin4(_7400_4_pin3),
    .pin5(_74273_1_pin2[1]), .pin6(_7408_11_pin11[1]), .pin7(1'b0), .pin8(_7408_11_pin11[2]),
    .pin9(_74273_1_pin2[2]), .pin10(_7400_4_pin3), .pin11(_7408_11_pin11[3]), .pin12(_74273_1_pin2[3]),
    .pin13(_7400_4_pin3), .pin14(1'b1));
  Seven_Seg #(.commonCathode("true"), .commonConnectionType("anode")) seven_seg_7 (
    .a(_74247_7_pin13), .b(_74247_7_pin12), .c(_74247_7_pin11), .d(_74247_7_pin10), .e(_74247_7_pin9),
    .f(_74247_7_pin15), .g(_74247_7_pin14), .dp(1'b1), .common(1'b1));
  _74247 _74247_7 (
    .pin1(_74247_7_pin1), .pin2(_74247_7_pin2), .pin3(_74247_7_pin3), .pin4(_74247_7_pin3),
    .pin5(_74247_7_pin3), .pin6(_74247_7_pin6), .pin7(_74247_7_pin7), .pin8(1'b0), .pin9(_74247_7_pin9),
    .pin10(_74247_7_pin10), .pin11(_74247_7_pin11), .pin12(_74247_7_pin12), .pin13(_74247_7_pin13),
    .pin14(_74247_7_pin14), .pin15(_74247_7_pin15), .pin16(1'b1));
  _7477 _7477_3 (
    .Q_0(_74247_7_pin7), .D_0(_74247_10_pin7), .E_0_E_1(_7404_12_pin2), .VCC(1'b1), .GND(1'b0),
    .Q_1(_74247_7_pin1), .D_1(_74247_10_pin1), .Q_2(_74247_7_pin2), .D_2(_74247_10_pin2),
    .E_2_E_3(_7404_12_pin2), .Q_3(_74247_7_pin6), .D_3(_74247_10_pin6));
  PullUp pullup_47 (.out(_74247_7_pin3));
  Seven_Seg_Hex seven_seg_hex_64 (.d(_7408_11_pin11), .dp(1'b0));
  Seven_Seg #(.commonCathode("true"), .commonConnectionType("anode")) seven_seg_8 (
    .a(_74247_8_pin13), .b(_74247_8_pin12), .c(_74247_8_pin11), .d(_74247_8_pin10), .e(_74247_8_pin9),
    .f(_74247_8_pin15), .g(_74247_8_pin14), .dp(_7407_1_pin10), .common(1'b1));
  _74247 _74247_8 (
    .pin1(_74247_8_pin1), .pin2(_74247_8_pin2), .pin3(_74247_8_pin3), .pin4(_74247_8_pin3),
    .pin5(_74247_8_pin3), .pin6(_74247_8_pin6), .pin7(_74247_8_pin7), .pin8(1'b0), .pin9(_74247_8_pin9),
    .pin10(_74247_8_pin10), .pin11(_74247_8_pin11), .pin12(_74247_8_pin12), .pin13(_74247_8_pin13),
    .pin14(_74247_8_pin14), .pin15(_74247_8_pin15), .pin16(1'b1));
  _7477 _7477_4 (
    .Q_0(_74247_8_pin7), .D_0(_74247_11_pin7), .E_0_E_1(_7404_12_pin4), .VCC(1'b1), .GND(1'b0),
    .Q_1(_74247_8_pin1), .D_1(_74247_11_pin1), .Q_2(_74247_8_pin2), .D_2(_74247_11_pin2),
    .E_2_E_3(_7404_12_pin4), .Q_3(_74247_8_pin6), .D_3(_74247_11_pin6));
  PullUp pullup_48 (.out(_74247_8_pin3));
  _74247 _74247_9 (
    .pin1(_74247_9_pin1), .pin2(_74247_9_pin2), .pin3(_74247_9_pin3), .pin4(_74247_9_pin3),
    .pin5(_74247_9_pin3), .pin6(_74247_9_pin6), .pin7(_74247_9_pin7), .pin8(1'b0), .pin9(_74247_9_pin9),
    .pin10(_74247_9_pin10), .pin11(_74247_9_pin11), .pin12(_74247_9_pin12), .pin13(_74247_9_pin13),
    .pin14(_74247_9_pin14), .pin15(_74247_9_pin15), .pin16(1'b1));
  Seven_Seg #(.commonCathode("true"), .commonConnectionType("anode")) seven_seg_9 (
    .a(_74247_9_pin13), .b(_74247_9_pin12), .c(_74247_9_pin11), .d(_74247_9_pin10), .e(_74247_9_pin9),
    .f(_74247_9_pin15), .g(_74247_9_pin14), .dp(1'b1), .common(1'b1));
  _7477 _7477_5 (
    .Q_0(_74247_9_pin7), .D_0(_74247_12_pin7), .E_0_E_1(_7404_12_pin4), .VCC(1'b1), .GND(1'b0),
    .Q_1(_74247_9_pin1), .D_1(_74247_12_pin1), .Q_2(_74247_9_pin2), .D_2(_74247_12_pin2),
    .E_2_E_3(_7404_12_pin4), .Q_3(_74247_9_pin6), .D_3(_74247_12_pin6));
  _74160 j_digit (
    .pin1(j_digit_pin1), .pin2(B13), .pin3(1'b0), .pin4(1'b0), .pin5(1'b0), .pin6(1'b0), .pin7(j_digit_pin7),
    .pin8(1'b0), .pin9(j_digit_pin9), .pin10(j_digit_pin9), .pin11(j_digit_pin11), .pin12(j_digit_pin12),
    .pin13(j_digit_pin13), .pin14(j_digit_pin14), .pin16(1'b1));  // open: pin15
  PullUp pullup_49 (.out(j_digit_pin7));
  PullUp pullup_50 (.out(_74247_9_pin3));
  PullUp pullup_51 (.out(j_digit_pin9));
  Seven_Seg #(.commonCathode("true"), .commonConnectionType("anode")) seven_seg_10 (
    .a(_74247_10_pin13), .b(_74247_10_pin12), .c(_74247_10_pin11), .d(_74247_10_pin10), .e(_74247_10_pin9),
    .f(_74247_10_pin15), .g(_74247_10_pin14), .dp(1'b1), .common(1'b1));
  _74247 _74247_10 (
    .pin1(_74247_10_pin1), .pin2(_74247_10_pin2), .pin3(_74247_10_pin3), .pin4(_74247_10_pin3),
    .pin5(_74247_10_pin3), .pin6(_74247_10_pin6), .pin7(_74247_10_pin7), .pin8(1'b0), .pin9(_74247_10_pin9),
    .pin10(_74247_10_pin10), .pin11(_74247_10_pin11), .pin12(_74247_10_pin12), .pin13(_74247_10_pin13),
    .pin14(_74247_10_pin14), .pin15(_74247_10_pin15), .pin16(1'b1));
  _7477 _7477_6 (
    .Q_0(_74247_10_pin7), .D_0(_74247_13_pin7), .E_0_E_1(_7404_12_pin4), .VCC(1'b1), .GND(1'b0),
    .Q_1(_74247_10_pin1), .D_1(_74247_13_pin1), .Q_2(_74247_10_pin2), .D_2(_74247_13_pin2),
    .E_2_E_3(_7404_12_pin4), .Q_3(_74247_10_pin6), .D_3(_74247_13_pin6));
  _7410 _7410_2 (
    .pin1(j_digit_pin14), .pin2(j_digit_pin13), .pin3(j_digit_pin12), .pin4(_7410_2_pin4),
    .pin5(_7410_2_pin4), .pin6(_7410_2_pin6), .pin7(1'b0), .pin8(_7410_2_pin8), .pin9(_7410_2_pin6),
    .pin10(_7410_2_pin10), .pin11(A15), .pin12(_7410_2_pin4), .pin13(j_digit_pin11), .pin14(1'b1));
  _7400 _7400_5 (
    .pin1(1'b0), .pin2(1'b0), .pin4(1'b0), .pin5(1'b0), .pin7(1'b0), .pin8(A5), .pin9(_7410_2_pin10),
    .pin10(_7410_2_pin10), .pin11(_7410_2_pin10), .pin12(_7400_5_pin12), .pin13(B9), .pin14(1'b1));  // open: pin3, pin6
  PullUp pullup_52 (.out(_74247_10_pin3));
  Seven_Seg #(.commonCathode("true"), .commonConnectionType("anode")) seven_seg_11 (
    .a(_74247_11_pin13), .b(_74247_11_pin12), .c(_74247_11_pin11), .d(_74247_11_pin10), .e(_74247_11_pin9),
    .f(_74247_11_pin15), .g(_74247_11_pin14), .dp(_7407_1_pin8), .common(1'b1));
  _74247 _74247_11 (
    .pin1(_74247_11_pin1), .pin2(_74247_11_pin2), .pin3(_74247_11_pin3), .pin4(_74247_11_pin3),
    .pin5(_74247_11_pin3), .pin6(_74247_11_pin6), .pin7(_74247_11_pin7), .pin8(1'b0), .pin9(_74247_11_pin9),
    .pin10(_74247_11_pin10), .pin11(_74247_11_pin11), .pin12(_74247_11_pin12), .pin13(_74247_11_pin13),
    .pin14(_74247_11_pin14), .pin15(_74247_11_pin15), .pin16(1'b1));
  _7477 _7477_7 (
    .Q_0(_74247_11_pin7), .D_0(_74247_14_pin7), .E_0_E_1(_7404_12_pin6), .VCC(1'b1), .GND(1'b0),
    .Q_1(_74247_11_pin1), .D_1(_74247_14_pin1), .Q_2(_74247_11_pin2), .D_2(_74247_14_pin2),
    .E_2_E_3(_7404_12_pin6), .Q_3(_74247_11_pin6), .D_3(_74247_14_pin6));
  _7404 _7404_13 (
    .pin1(j_digit_pin13), .pin2(_7404_13_pin2), .pin3(j_digit_pin14), .pin4(_7404_13_pin4),
    .pin5(_7410_2_pin8), .pin6(j_digit_pin1), .pin7(1'b0), .pin8(_7404_13_pin8), .pin9(_7400_4_pin8),
    .pin10(_7404_13_pin10), .pin11(B15), .pin13(1'b0), .pin14(1'b1));  // open: pin12
  PullUp pullup_53 (.out(_74247_11_pin3));
  _7408 _7408_12 (
    .pin1(j_digit_pin14), .pin2(_7404_13_pin2), .pin3(A14), .pin4(j_digit_pin13), .pin5(_7404_13_pin4),
    .pin6(_7408_12_pin6), .pin7(1'b0), .pin9(1'b0), .pin10(1'b0), .pin11(_7408_12_pin11),
    .pin12(_7408_12_pin12), .pin13(A14), .pin14(1'b1));  // open: pin8
  Seven_Seg #(.commonCathode("true"), .commonConnectionType("anode")) seven_seg_12 (
    .a(_74247_12_pin13), .b(_74247_12_pin12), .c(_74247_12_pin11), .d(_74247_12_pin10), .e(_74247_12_pin9),
    .f(_74247_12_pin15), .g(_74247_12_pin14), .dp(1'b1), .common(1'b1));
  _74247 _74247_12 (
    .pin1(_74247_12_pin1), .pin2(_74247_12_pin2), .pin3(_74247_12_pin3), .pin4(_74247_12_pin3),
    .pin5(_74247_12_pin3), .pin6(_74247_12_pin6), .pin7(_74247_12_pin7), .pin8(1'b0), .pin9(_74247_12_pin9),
    .pin10(_74247_12_pin10), .pin11(_74247_12_pin11), .pin12(_74247_12_pin12), .pin13(_74247_12_pin13),
    .pin14(_74247_12_pin14), .pin15(_74247_12_pin15), .pin16(1'b1));
  _7477 _7477_8 (
    .Q_0(_74247_12_pin7), .D_0(_74247_15_pin7), .E_0_E_1(_7404_12_pin6), .VCC(1'b1), .GND(1'b0),
    .Q_1(_74247_12_pin1), .D_1(_74247_15_pin1), .Q_2(_74247_12_pin2), .D_2(_74247_15_pin2),
    .E_2_E_3(_7404_12_pin6), .Q_3(_74247_12_pin6), .D_3(_74247_15_pin6));
  PullUp pullup_54 (.out(_74247_12_pin3));
  Seven_Seg #(.commonCathode("true"), .commonConnectionType("anode")) seven_seg_13 (
    .a(_74247_13_pin13), .b(_74247_13_pin12), .c(_74247_13_pin11), .d(_74247_13_pin10), .e(_74247_13_pin9),
    .f(_74247_13_pin15), .g(_74247_13_pin14), .dp(1'b1), .common(1'b1));
  _74247 _74247_13 (
    .pin1(_74247_13_pin1), .pin2(_74247_13_pin2), .pin3(_74247_13_pin3), .pin4(_74247_13_pin3),
    .pin5(_74247_13_pin3), .pin6(_74247_13_pin6), .pin7(_74247_13_pin7), .pin8(1'b0), .pin9(_74247_13_pin9),
    .pin10(_74247_13_pin10), .pin11(_74247_13_pin11), .pin12(_74247_13_pin12), .pin13(_74247_13_pin13),
    .pin14(_74247_13_pin14), .pin15(_74247_13_pin15), .pin16(1'b1));
  _7477 _7477_9 (
    .Q_0(_74247_13_pin7), .D_0(_74247_16_pin7), .E_0_E_1(_7404_12_pin6), .VCC(1'b1), .GND(1'b0),
    .Q_1(_74247_13_pin1), .D_1(_74247_16_pin1), .Q_2(_74247_13_pin2), .D_2(_74247_16_pin2),
    .E_2_E_3(_7404_12_pin6), .Q_3(_74247_13_pin6), .D_3(_74247_16_pin6));
  PullUp pullup_55 (.out(_74247_13_pin3));
  _74367 _74367_1 (
    .nG1(1'b0), .nG2(1'b0), .A1(A14), .Y1(_74367_1_y1), .A2(_7408_12_pin6), .Y2(_74367_1_y2),
    .A3(_7400_5_pin12), .Y3(_74367_1_y3), .A4(1'b0), .A5(1'b0), .A6(1'b0), .VCC(1'b1), .GND(1'b0));  // open: Y4, Y5, Y6
  LED j_digit__eq__1 (.in(_74367_1_y1));
  LED j_digit__eq__2 (.in(_74367_1_y2));
  LED j_digit__eq__3 (.in(_74367_1_y3));
  _7400 _7400_6 (
    .pin1(_7404_13_pin10), .pin2(_7404_13_pin8), .pin3(_7408_12_pin12), .pin4(_7408_12_pin6), .pin5(B14),
    .pin6(_7400_6_pin6), .pin7(1'b0), .pin8(_7400_6_pin8), .pin9(_7400_5_pin12), .pin10(B14),
    .pin11(_7400_6_pin11), .pin12(B14), .pin13(A14), .pin14(1'b1));
  _7408 _7408_13 (
    .pin1(j_digit_pin14), .pin2(j_digit_pin13), .pin3(_7400_5_pin12), .pin4(1'b0), .pin5(1'b0), .pin7(1'b0),
    .pin8(_7408_13_pin8), .pin9(_7400_5_pin12), .pin10(_7408_12_pin12), .pin11(_7408_13_pin11),
    .pin12(_7408_12_pin6), .pin13(_7408_12_pin12), .pin14(1'b1));  // open: pin6
  _74247 _74247_14 (
    .pin1(_74247_14_pin1), .pin2(_74247_14_pin2), .pin3(_74247_14_pin3), .pin4(_74247_14_pin3),
    .pin5(_74247_14_pin3), .pin6(_74247_14_pin6), .pin7(_74247_14_pin7), .pin8(1'b0), .pin9(_74247_14_pin9),
    .pin10(_74247_14_pin10), .pin11(_74247_14_pin11), .pin12(_74247_14_pin12), .pin13(_74247_14_pin13),
    .pin14(_74247_14_pin14), .pin15(_74247_14_pin15), .pin16(1'b1));
  Seven_Seg #(.commonCathode("true"), .commonConnectionType("anode")) seven_seg_14 (
    .a(_74247_14_pin13), .b(_74247_14_pin12), .c(_74247_14_pin11), .d(_74247_14_pin10), .e(_74247_14_pin9),
    .f(_74247_14_pin15), .g(_74247_14_pin14), .dp(_7407_1_pin6), .common(1'b1));
  _7477 _7477_10 (
    .Q_0(_74247_14_pin7), .D_0(_74247_17_pin7), .E_0_E_1(_7404_12_pin8), .VCC(1'b1), .GND(1'b0),
    .Q_1(_74247_14_pin1), .D_1(_74247_17_pin1), .Q_2(_74247_14_pin2), .D_2(_74247_17_pin2),
    .E_2_E_3(_7404_12_pin8), .Q_3(_74247_14_pin6), .D_3(_74247_17_pin6));
  PullUp pullup_56 (.out(_74247_14_pin3));
  Seven_Seg #(.commonCathode("true"), .commonConnectionType("anode")) seven_seg_15 (
    .a(_74247_15_pin13), .b(_74247_15_pin12), .c(_74247_15_pin11), .d(_74247_15_pin10), .e(_74247_15_pin9),
    .f(_74247_15_pin15), .g(_74247_15_pin14), .dp(1'b1), .common(1'b1));
  _74247 _74247_15 (
    .pin1(_74247_15_pin1), .pin2(_74247_15_pin2), .pin3(_74247_15_pin3), .pin4(_74247_15_pin3),
    .pin5(_74247_15_pin3), .pin6(_74247_15_pin6), .pin7(_74247_15_pin7), .pin8(1'b0), .pin9(_74247_15_pin9),
    .pin10(_74247_15_pin10), .pin11(_74247_15_pin11), .pin12(_74247_15_pin12), .pin13(_74247_15_pin13),
    .pin14(_74247_15_pin14), .pin15(_74247_15_pin15), .pin16(1'b1));
  _7477 _7477_11 (
    .Q_0(_74247_15_pin7), .D_0(_74247_18_pin7), .E_0_E_1(_7404_12_pin8), .VCC(1'b1), .GND(1'b0),
    .Q_1(_74247_15_pin1), .D_1(_74247_18_pin1), .Q_2(_74247_15_pin2), .D_2(_74247_18_pin2),
    .E_2_E_3(_7404_12_pin8), .Q_3(_74247_15_pin6), .D_3(_74247_18_pin6));
  _7408 _7408_14 (
    .pin1(_7408_11_pin11[0]), .pin2(A14), .pin3(_7408_14_pin3), .pin4(_7408_11_pin11[1]), .pin5(A14),
    .pin6(_7408_14_pin6), .pin7(1'b0), .pin8(_7408_14_pin8), .pin9(_7408_11_pin11[2]), .pin10(A14),
    .pin11(_7408_14_pin11), .pin12(_7408_11_pin11[3]), .pin13(A14), .pin14(1'b1));
  _7408 _7408_15 (
    .pin1(_7408_11_pin11[0]), .pin2(_7408_12_pin6), .pin3(_7408_15_pin3), .pin4(_7408_11_pin11[1]),
    .pin5(_7408_12_pin6), .pin6(_7408_15_pin6), .pin7(1'b0), .pin8(_7408_15_pin8), .pin9(_7408_11_pin11[2]),
    .pin10(_7408_12_pin6), .pin11(_7408_15_pin11), .pin12(_7408_11_pin11[3]), .pin13(_7408_12_pin6),
    .pin14(1'b1));
  _7408 _7408_16 (
    .pin1(_7408_11_pin11[0]), .pin2(_7400_5_pin12), .pin3(_7408_16_pin3), .pin4(_7408_11_pin11[1]),
    .pin5(_7400_5_pin12), .pin6(_7408_16_pin6), .pin7(1'b0), .pin8(_7408_16_pin8), .pin9(_7408_11_pin11[2]),
    .pin10(_7400_5_pin12), .pin11(_7408_16_pin11), .pin12(_7408_11_pin11[3]), .pin13(_7400_5_pin12),
    .pin14(1'b1));
  PullUp pullup_57 (.out(_74247_15_pin3));
  _74247 _74247_16 (
    .pin1(_74247_16_pin1), .pin2(_74247_16_pin2), .pin3(_74247_16_pin3), .pin4(_74247_16_pin3),
    .pin5(_74247_16_pin3), .pin6(_74247_16_pin6), .pin7(_74247_16_pin7), .pin8(1'b0), .pin9(_74247_16_pin9),
    .pin10(_74247_16_pin10), .pin11(_74247_16_pin11), .pin12(_74247_16_pin12), .pin13(_74247_16_pin13),
    .pin14(_74247_16_pin14), .pin15(_74247_16_pin15), .pin16(1'b1));
  Seven_Seg #(.commonCathode("true"), .commonConnectionType("anode")) seven_seg_16 (
    .a(_74247_16_pin13), .b(_74247_16_pin12), .c(_74247_16_pin11), .d(_74247_16_pin10), .e(_74247_16_pin9),
    .f(_74247_16_pin15), .g(_74247_16_pin14), .dp(1'b1), .common(1'b1));
  _7477 _7477_12 (
    .Q_0(_74247_16_pin7), .D_0(_74247_19_pin7), .E_0_E_1(_7404_12_pin8), .VCC(1'b1), .GND(1'b0),
    .Q_1(_74247_16_pin1), .D_1(_74247_19_pin1), .Q_2(_74247_16_pin2), .D_2(_74247_19_pin2),
    .E_2_E_3(_7404_12_pin8), .Q_3(_74247_16_pin6), .D_3(_74247_19_pin6));
  PullUp pullup_58 (.out(_74247_16_pin3));
  PullUp pullup_59 (.out(pullup_59_out));
  PullUp pullup_60 (.out(pullup_60_out));
  PullUp pullup_61 (.out(pullup_61_out));
  PullUp pullup_62 (.out(pullup_62_out));
  PullUp pullup_63 (.out(pullup_63_out));
  PullUp pullup_64 (.out(pullup_64_out));
  PullUp pullup_65 (.out(pullup_65_out));
  _74161 _74161_8 (
    .pin1(A15), .pin2(A5), .pin3(_74161_8_pin3), .pin4(1'b0), .pin5(1'b0), .pin6(1'b0), .pin7(pullup_59_out),
    .pin8(1'b0), .pin9(_74161_8_pin9), .pin10(pullup_59_out), .pin12(_74161_8_pin12), .pin13(_74161_8_pin13),
    .pin16(1'b1));  // open: pin11, pin14, pin15
  PullUp pullup_66 (.out(_74161_8_pin3));
  _74160 digit_7 (
    .pin1(pullup_60_out), .pin2(_7408_12_pin11), .pin3(_7408_14_pin3), .pin4(_7408_14_pin6),
    .pin5(_7408_14_pin8), .pin6(_7408_14_pin11), .pin7(pullup_61_out), .pin8(1'b0), .pin9(_7400_6_pin11),
    .pin10(digit_7_pin10), .pin11(digit_7_pin14[3]), .pin12(digit_7_pin14[2]), .pin13(digit_7_pin14[1]),
    .pin14(digit_7_pin14[0]), .pin16(1'b1));  // open: pin15
  _74160 digit_8 (
    .pin1(pullup_62_out), .pin2(_7408_13_pin11), .pin3(_7408_15_pin3), .pin4(_7408_15_pin6),
    .pin5(_7408_15_pin8), .pin6(_7408_15_pin11), .pin7(pullup_63_out), .pin8(1'b0), .pin9(_7400_6_pin6),
    .pin10(digit_8_pin10), .pin11(digit_8_pin14[3]), .pin12(digit_8_pin14[2]), .pin13(digit_8_pin14[1]),
    .pin14(digit_8_pin14[0]), .pin16(1'b1));  // open: pin15
  _74160 digit_9 (
    .pin1(pullup_64_out), .pin2(_7408_13_pin8), .pin3(_7408_16_pin3), .pin4(_7408_16_pin6),
    .pin5(_7408_16_pin8), .pin6(_7408_16_pin11), .pin7(pullup_65_out), .pin8(1'b0), .pin9(_7400_6_pin8),
    .pin10(digit_9_pin10), .pin11(digit_9_pin14[3]), .pin12(digit_9_pin14[2]), .pin13(digit_9_pin14[1]),
    .pin14(digit_9_pin14[0]), .pin16(1'b1));  // open: pin15
  Seven_Seg #(.commonCathode("true"), .commonConnectionType("anode")) seven_seg_17 (
    .a(_74247_17_pin13), .b(_74247_17_pin12), .c(_74247_17_pin11), .d(_74247_17_pin10), .e(_74247_17_pin9),
    .f(_74247_17_pin15), .g(_74247_17_pin14), .dp(_7407_1_pin4), .common(1'b1));
  _74247 _74247_17 (
    .pin1(_74247_17_pin1), .pin2(_74247_17_pin2), .pin3(_74247_17_pin3), .pin4(_74247_17_pin3),
    .pin5(_74247_17_pin3), .pin6(_74247_17_pin6), .pin7(_74247_17_pin7), .pin8(1'b0), .pin9(_74247_17_pin9),
    .pin10(_74247_17_pin10), .pin11(_74247_17_pin11), .pin12(_74247_17_pin12), .pin13(_74247_17_pin13),
    .pin14(_74247_17_pin14), .pin15(_74247_17_pin15), .pin16(1'b1));
  _7477 _7477_13 (
    .Q_0(_74247_17_pin7), .D_0(_74247_20_pin7), .E_0_E_1(_7404_12_pin10), .VCC(1'b1), .GND(1'b0),
    .Q_1(_74247_17_pin1), .D_1(_74247_20_pin1), .Q_2(_74247_17_pin2), .D_2(_74247_20_pin2),
    .E_2_E_3(_7404_12_pin10), .Q_3(_74247_17_pin6), .D_3(_74247_20_pin6));
  PullUp pullup_67 (.out(digit_7_pin10));
  PullUp pullup_68 (.out(digit_8_pin10));
  PullUp pullup_69 (.out(digit_9_pin10));
  PullUp pullup_70 (.out(_74247_17_pin3));
  Seven_Seg_Hex seven_seg_hex_65 (.d(digit_7_pin14), .dp(1'b0));
  _74173 _74173_1 (
    .pin1(1'b0), .pin2(1'b0), .pin3(_74173_1_pin3), .pin7(_74173_1_pin7), .pin8(1'b0), .pin9(_74173_1_pin9),
    .pin10(1'b0), .pin11(1'b0), .pin12(1'b0), .pin13(1'b0), .pin14(_74173_1_pin14), .pin15(_74173_1_pin15),
    .pin16(1'b1));  // open: pin4, pin5, pin6
  Seven_Seg #(.commonCathode("true"), .commonConnectionType("anode")) seven_seg_18 (
    .a(_74247_18_pin13), .b(_74247_18_pin12), .c(_74247_18_pin11), .d(_74247_18_pin10), .e(_74247_18_pin9),
    .f(_74247_18_pin15), .g(_74247_18_pin14), .dp(1'b1), .common(1'b1));
  _74247 _74247_18 (
    .pin1(_74247_18_pin1), .pin2(_74247_18_pin2), .pin3(_74247_18_pin3), .pin4(_74247_18_pin3),
    .pin5(_74247_18_pin3), .pin6(_74247_18_pin6), .pin7(_74247_18_pin7), .pin8(1'b0), .pin9(_74247_18_pin9),
    .pin10(_74247_18_pin10), .pin11(_74247_18_pin11), .pin12(_74247_18_pin12), .pin13(_74247_18_pin13),
    .pin14(_74247_18_pin14), .pin15(_74247_18_pin15), .pin16(1'b1));
  Seven_Seg_Hex seven_seg_hex_66 (.d(digit_8_pin14), .dp(1'b0));
  _7477 _7477_14 (
    .Q_0(_74247_18_pin7), .D_0(_74247_21_pin7), .E_0_E_1(_7404_12_pin10), .VCC(1'b1), .GND(1'b0),
    .Q_1(_74247_18_pin1), .D_1(_74247_21_pin1), .Q_2(_74247_18_pin2), .D_2(_74247_21_pin2),
    .E_2_E_3(_7404_12_pin10), .Q_3(_74247_18_pin6), .D_3(_74247_21_pin6));
  _7400 _7400_7 (
    .pin1(_74161_8_pin13), .pin2(_74161_8_pin12), .pin3(_74161_8_pin9), .pin4(_74161_8_pin9),
    .pin5(_74161_8_pin9), .pin6(_74173_1_pin7), .pin7(1'b0), .pin8(_7400_7_pin8), .pin9(_74173_1_pin3),
    .pin10(_74173_1_pin3), .pin11(D22), .pin12(_7400_7_pin12), .pin13(_7400_7_pin8), .pin14(1'b1));
  PullUp pullup_71 (.out(_74173_1_pin14));
  // SwitchDT switchdt_4: pin names not known; wires that end beside it: _74173_1_pin9, switchdt_4_p2, 1'b0
  Seven_Seg_Hex seven_seg_hex_67 (.d(digit_9_pin14), .dp(1'b0));
  PullUp pullup_72 (.out(_74247_18_pin3));
  Button RESUME (.out(_74173_1_pin15));
  PullUp pullup_73 (.out(switchdt_4_p2));
  LED PRINT (.in(out_23));
  Seven_Seg #(.commonCathode("true"), .commonConnectionType("anode")) seven_seg_19 (
    .a(_74247_19_pin13), .b(_74247_19_pin12), .c(_74247_19_pin11), .d(_74247_19_pin10), .e(_74247_19_pin9),
    .f(_74247_19_pin15), .g(_74247_19_pin14), .dp(1'b1), .common(1'b1));
  _74247 _74247_19 (
    .pin1(_74247_19_pin1), .pin2(_74247_19_pin2), .pin3(_74247_19_pin3), .pin4(_74247_19_pin3),
    .pin5(_74247_19_pin3), .pin6(_74247_19_pin6), .pin7(_74247_19_pin7), .pin8(1'b0), .pin9(_74247_19_pin9),
    .pin10(_74247_19_pin10), .pin11(_74247_19_pin11), .pin12(_74247_19_pin12), .pin13(_74247_19_pin13),
    .pin14(_74247_19_pin14), .pin15(_74247_19_pin15), .pin16(1'b1));
  _7477 _7477_15 (
    .Q_0(_74247_19_pin7), .D_0(_74247_22_pin7), .E_0_E_1(_7404_12_pin10), .VCC(1'b1), .GND(1'b0),
    .Q_1(_74247_19_pin1), .D_1(_74247_22_pin1), .Q_2(_74247_19_pin2), .D_2(_74247_22_pin2),
    .E_2_E_3(_7404_12_pin10), .Q_3(_74247_19_pin6), .D_3(_74247_22_pin6));
  _74173 _74173_2 (
    .pin1(1'b0), .pin2(1'b0), .pin3(out_23), .pin7(in_22), .pin8(1'b0), .pin9(1'b0), .pin10(1'b0),
    .pin11(1'b0), .pin12(1'b0), .pin13(1'b0), .pin14(_74173_2_pin14), .pin15(_74173_2_pin15), .pin16(1'b1));  // open: pin4, pin5, pin6
  PullUp pullup_74 (.out(_7400_7_pin12));
  Switch switch_1 (.A(_7400_7_pin12), .B(1'b0));
  PullUp pullup_75 (.out(_74247_19_pin3));
  Button PRINT_COMPLETE (.out(_74173_2_pin15));
  PullUp pullup_76 (.out(_74173_2_pin14));
  PullUp pullup_77 (.out(pullup_77_out));
  _74273 _74273_2 (
    .pin1(pullup_77_out), .pin2(A13), .pin3(digit_7_pin14[0]), .pin4(digit_7_pin14[1]), .pin5(A12),
    .pin6(A11), .pin7(digit_7_pin14[2]), .pin8(digit_7_pin14[3]), .pin9(A10), .pin10(1'b0), .pin11(A5),
    .pin12(A9), .pin13(digit_8_pin14[0]), .pin14(digit_8_pin14[1]), .pin15(A8), .pin16(A7),
    .pin17(digit_8_pin14[2]), .pin18(digit_8_pin14[3]), .pin19(A6), .pin20(1'b1));
  PullUp pullup_78 (.out(pullup_78_out));
  _74273 _74273_3 (
    .pin1(pullup_78_out), .pin2(A4), .pin3(digit_9_pin14[0]), .pin4(digit_9_pin14[1]), .pin5(A3), .pin6(A2),
    .pin7(digit_9_pin14[2]), .pin8(digit_9_pin14[3]), .pin9(A1), .pin10(1'b0), .pin11(A5), .pin13(1'b0),
    .pin14(1'b0), .pin17(1'b0), .pin18(1'b0), .pin20(1'b1));  // open: pin12, pin15, pin16, pin19
  Seven_Seg_Hex seven_seg_hex_68 (.d({A10, A11, A12, A13}), .dp(1'b0));
  Seven_Seg_Hex seven_seg_hex_69 (.d({A6, A7, A8, A9}), .dp(1'b0));
  Seven_Seg #(.commonCathode("true"), .commonConnectionType("anode")) seven_seg_20 (
    .a(_74247_20_pin13), .b(_74247_20_pin12), .c(_74247_20_pin11), .d(_74247_20_pin10), .e(_74247_20_pin9),
    .f(_74247_20_pin15), .g(_74247_20_pin14), .dp(_7407_1_pin2), .common(1'b1));
  _74247 _74247_20 (
    .pin1(_74247_20_pin1), .pin2(_74247_20_pin2), .pin3(_74247_20_pin3), .pin4(_74247_20_pin3),
    .pin5(_74247_20_pin3), .pin6(_74247_20_pin6), .pin7(_74247_20_pin7), .pin8(1'b0), .pin9(_74247_20_pin9),
    .pin10(_74247_20_pin10), .pin11(_74247_20_pin11), .pin12(_74247_20_pin12), .pin13(_74247_20_pin13),
    .pin14(_74247_20_pin14), .pin15(_74247_20_pin15), .pin16(1'b1));
  _7477 _7477_16 (
    .Q_0(_74247_20_pin7), .D_0(A13), .E_0_E_1(_7404_12_pin12), .VCC(1'b1), .GND(1'b0), .Q_1(_74247_20_pin1),
    .D_1(A12), .Q_2(_74247_20_pin2), .D_2(A11), .E_2_E_3(_7404_12_pin12), .Q_3(_74247_20_pin6), .D_3(A10));
  Seven_Seg_Hex seven_seg_hex_70 (.d({A1, A2, A3, A4}), .dp(1'b0));
  PullUp pullup_79 (.out(_74247_20_pin3));
  _74541 _74541_9 (
    .pin1(1'b0), .pin2(D22), .pin3(_74173_1_pin3), .pin4(A15), .pin5(A5), .pin6(A10), .pin7(A11), .pin8(A12),
    .pin9(A13), .pin10(1'b0), .pin11(BUS_PIN__9__OUT__1_A), .pin12(BUS_PIN__10__OUT__1_B),
    .pin13(BUS_PIN__11__OUT__1_C), .pin14(BUS_PIN__12__OUT__1_D), .pin15(BUS_PIN__13__OUT__ripple_display),
    .pin16(BUS_PIN__14__OUT__low_whilst_reset), .pin17(_74541_9_pin17), .pin18(_74541_9_pin18), .pin19(1'b0),
    .pin20(1'b1));
  _74541 _74541_10 (
    .pin1(1'b0), .pin2(A6), .pin3(A7), .pin4(A8), .pin5(A9), .pin6(A1), .pin7(A2), .pin8(A3), .pin9(A4),
    .pin10(1'b0), .pin11(BUS_PIN__1__OUT__3_A), .pin12(BUS_PIN__2__OUT__3_B), .pin13(BUS_PIN__3__OUT__3_C),
    .pin14(BUS_PIN__4__OUT__3_D), .pin15(BUS_PIN__5__OUT__2_A), .pin16(BUS_PIN__6__OUT__2_B),
    .pin17(BUS_PIN__7__OUT__2_C), .pin18(BUS_PIN__8__OUT__2_D), .pin19(1'b0), .pin20(1'b1));
  _7405 _7405_1 (
    .pin1(1'b0), .pin3(1'b0), .pin5(1'b0), .pin7(1'b0), .pin9(1'b0), .pin11(1'b0), .pin12(_7400_7_pin12),
    .pin13(BUS_PIN__15__IN__HI_TO_PAUSE), .pin14(1'b1));  // open: pin2, pin4, pin6, pin8, pin10
  _74247 _74247_21 (
    .pin1(_74247_21_pin1), .pin2(_74247_21_pin2), .pin3(_74247_21_pin3), .pin4(_74247_21_pin3),
    .pin5(_74247_21_pin3), .pin6(_74247_21_pin6), .pin7(_74247_21_pin7), .pin8(1'b0), .pin9(_74247_21_pin9),
    .pin10(_74247_21_pin10), .pin11(_74247_21_pin11), .pin12(_74247_21_pin12), .pin13(_74247_21_pin13),
    .pin14(_74247_21_pin14), .pin15(_74247_21_pin15), .pin16(1'b1));
  LED WAITING (.in(_74541_9_pin17));
  LED PAUSED (.in(_74541_9_pin18));
  Seven_Seg #(.commonCathode("true"), .commonConnectionType("anode")) seven_seg_21 (
    .a(_74247_21_pin13), .b(_74247_21_pin12), .c(_74247_21_pin11), .d(_74247_21_pin10), .e(_74247_21_pin9),
    .f(_74247_21_pin15), .g(_74247_21_pin14), .dp(1'b1), .common(1'b1));
  _7477 _7477_17 (
    .Q_0(_74247_21_pin7), .D_0(A9), .E_0_E_1(_7404_12_pin12), .VCC(1'b1), .GND(1'b0), .Q_1(_74247_21_pin1),
    .D_1(A8), .Q_2(_74247_21_pin2), .D_2(A7), .E_2_E_3(_7404_12_pin12), .Q_3(_74247_21_pin6), .D_3(A6));
  PullUp pullup_80 (.out(_74247_21_pin3));
  Seven_Seg #(.commonCathode("true"), .commonConnectionType("anode")) seven_seg_22 (
    .a(_74247_22_pin13), .b(_74247_22_pin12), .c(_74247_22_pin11), .d(_74247_22_pin10), .e(_74247_22_pin9),
    .f(_74247_22_pin15), .g(_74247_22_pin14), .dp(1'b1), .common(1'b1));
  _74247 _74247_22 (
    .pin1(_74247_22_pin1), .pin2(_74247_22_pin2), .pin3(_74247_22_pin3), .pin4(_74247_22_pin3),
    .pin5(_74247_22_pin3), .pin6(_74247_22_pin6), .pin7(_74247_22_pin7), .pin8(1'b0), .pin9(_74247_22_pin9),
    .pin10(_74247_22_pin10), .pin11(_74247_22_pin11), .pin12(_74247_22_pin12), .pin13(_74247_22_pin13),
    .pin14(_74247_22_pin14), .pin15(_74247_22_pin15), .pin16(1'b1));
  _7477 _7477_18 (
    .Q_0(_74247_22_pin7), .D_0(A4), .E_0_E_1(_7404_12_pin12), .VCC(1'b1), .GND(1'b0), .Q_1(_74247_22_pin1),
    .D_1(A3), .Q_2(_74247_22_pin2), .D_2(A2), .E_2_E_3(_7404_12_pin12), .Q_3(_74247_22_pin6), .D_3(A1));
  PullUp pullup_81 (.out(_74247_22_pin3));

  assign BUS_PIN__16__GND = 1'b0;

  // Other names for the same wires on the sheet: C2 = B9; B8 = A15; C1 = A15; D20 = A15; F8 = A15; F9 = A15; E25 = C4;
  //   I1 = C4; E26 = C5; I2 = C5; E27 = C6; I3 = C6; E28 = C7; I4 = C7; E29 = C8; I5 = C8; E30 = C9; I6 = C9;
  //   E31 = C10; I7 = C10; E32 = C11; I8 = C11; E33 = C12; I9 = C12; E34 = C13; I10 = C13

  // Notes on the sheet:
  //   FAST: Hz: 2147483647
  //   LOAD__goes_low: default 1
  //   SLOW: Hz: 150
  //   display_ripple_clock: Hz: 50000
  //   B
  //   B x ten
  //   NOTE 4
  //   OP count resets on count #13
  //   NOTE 2
  //   11 bit mult ten version I 03 oct 2021.dig
  //   LSB
  //   NOTE 3
  //   HI to clear counters
  //   A PLUS B
  //   A MINUS B
  //   CONTINUOUS
  //   SINGLE STEP
  //   (pulls line high)
  //   XOR
  //   Y0 is deliberate dead cycle
  //   low whilst reset
  //   BETA
  //   pull line high to pause
  //   a(b)
  //   operation
  //   RUN
  //   STOP/RESET
  //   BETA (HEX)
  //   RESET OP COUNTER
  //   a out
  //   op lines
  //   NOTE 5
  //   NOTE 6
  //   G: L\_INIT = FALSE
  //   sub-clock
  //   NOTE 1
  //   b (10 bit)
  //   number of cycles (hex)
  //   sub clock
  //   op #1
  //   op #2
  //   op #3
  //   op #4
  //   op#12* logic
  //   d out
  //   op#11* logic
  //   a in
  //   b != 0
  //   a 11 bit x 1024 SRAM
  //   op#5 logic
  //   op#6: if (b != 0) cycle
  //   NOTE 15
  //   NOTE 11
  //   op#4 logic
  //   register d
  //   d in
  //   op#10* logic
  //   op#8* logic
  //   op#3 logic
  //   i.e. selects IF ELSE ENDIF
  //   sub clock 1
  //   sub clock 2
  //   sub clock 3
  //   sub clock 4
  //   sub clock 5
  //   sub clock 6
  //   HI to reset sub-clock
  //   d + BETA or d + a(b) * 10
  //   NOTE 12
  //   op#9* logic
  //   op#2 logic
  //   #F: reg d READ/~WRITE
  //   NOTE 13
  //   NOTE 17
  //   d = d % g
  //   d = d * b
  //   #Q: assign kpi to j\_pi(j\_digit) step TWO
  //   #P: assign kpi to j\_pi(j\_digit) step ONE
  //   #O: j\_digit = j\_digit + 1
  //   #N: j\_pi(j\_digit) = j\_pi(j\_digit) + 1
  //   #L: latch e value
  //   #M: LOAD e value
  //   #K: b = b - 1
  //   #J: put d % g onto bus
  //   #I: a(b) WRITE
  //   #H: set b = 888
  //   #G: L\_INIT = F
  //   #A: put d * b onto bus
  //   #B: put d + BETA or d + a(b) * 10 onto bus
  //   #C: LATCH temp reg d
  //   #D: reg d OUTPUT ENABLE
  //   #E: LATCH reg d
  //   d in/out
  //   op#1 logic
  //   #D: latch d onto d input
  //   d is 15 bits only
  //   only 15 bits used for d
  //   op#7 logic
  //   #R: latch kpi value
  //   #O: j\_digit = j\_digit + 2
  //   #H: set b = 888;
  //   #C: latch temp reg d
  //   b = b - 1
  //   NOTE 23
  //   B0
  //   B1
  //   B2
  //   B3
  //   B4
  //   B5
  //   B6
  //   B7
  //   B8
  //   B9
  //   A0
  //   A1
  //   A2
  //   A3
  //   A4
  //   A5
  //   GAMMA
  //   6 bits of d only used here
  //   P16
  //   P17
  //   P18
  //   P19
  //   P20
  //   P21
  //   P22
  //   P23
  //   P24
  //   P25
  //   P26
  //   P27
  //   P28
  //   P29
  //   P30
  //   P31
  //   ALPHA
  //   master loop version Z 19 feb 2022.dig
  //   A
  //   ALPHA (HEX)
  //   NOTE 16
  //   NOTE 22
  //   2 * b +/- alpha = g
  //   NOTE 10
  //   b (375 hex = 888)
  //   a in = d % g
  //   2 * b +/- alpha = g etc
  //   a0
  //   a1
  //   a2
  //   a3
  //   a4
  //   a5
  //   a6
  //   a7
  //   a8
  //   a9
  //   a10
  //   d % g
  //   NOTE 9
  //   lowest six bits of d only
  //   0
  //   1
  //   b = b -1
  //   e out
  //   ripple display
  //   DISPLAYS ARE COMMON ANODE
  //   kpi = e + d / 10
  //   number of triplets
  //   arm display ripple
  //   NOTE 14
  //   #O: j\_digit = j\_digit + 3
  //   latch KPI
  //   NOTE 19
  //   d % 10
  //   NOTE 20
  //   kpi
  //   #P: assign kpi to j\_pi(j\_digit)
  //   if (l\_carry) kpi = 0
  //   counts 0,1,2,3; resets on 4
  //   kpi 0
  //   kpi 1
  //   kpi 2
  //   kpi 3
  //   assign new kpi to jpi
  //   if (l\_carry) jpi(jdigit) = jpi(jdigit) + 1
  //   NOTE 7
  //   j\_pi(j\_digit) = kpi
  //   set j\_digit = 0 when print j\_pi
  //   NOTE 21
  //   pi digit [1]
  //   pi digit [2]
  //   pi digit [3]
  //   NOTE 8
  //   GOES HIGH DURING PRINT
  //   ripple display in (HI when triplet ready for print)
  //   WAITING
  //   [1]
  //   NOTE 24
  //   [2]
  //   [3]
  //   NOTE 26
  //   NON-STOP
  //   WAIT
  //   NOTE 18
  //   PAUSE
  //   final triplet
  //   one
  //   two
  //   three
  //   NOTE 25
  //   EXTERNAL
  //   BUS
  //   INTERFACE
endmodule
