// Digital circuit 74214.dig as structural Verilog
// Static RAM 1024 x 1 bit
module _74214 (
  input  A0,
  input  A1,
  input  A2,
  input  A3,
  input  A4,
  input  A5,
  input  A6,
  input  A7,
  input  A8,
  input  A9,
  input  nCS,
  input  nWE,
  input  VCC,
  input  GND,
  input  Din,
  output Dout
);

  wire driverinvsel_1_out, ramasync_q;

  PowerSupply powersupply_1 (.VDD(VCC), .GND(GND));
  assign driverinvsel_1_out = ~nCS ? nWE : 1'bz;  // DriverInvSel driverinvsel_1
  RAMAsync #(.AddrBits(10)) ramasync (
    .A({A9, A8, A7, A6, A5, A4, A3, A2, A1, A0}), .D(Din), .we(~driverinvsel_1_out), .Q(ramasync_q));
  assign Dout = ~nCS ? ramasync_q : 1'bz;  // DriverInvSel driverinvsel_2

  // Notes on the sheet:
  //   A0: pin 2
  //   A1: pin 3
  //   A2: pin 4
  //   A3: pin 5
  //   A4: pin 6
  //   A5: pin 9
  //   A6: pin 10
  //   A7: pin 11
  //   A8: pin 12
  //   A9: pin 13
  //   nCS: pin 1, default 1
  //   nWE: pin 14, default 1
  //   Dout: pin 7
  //   VCC: pin 16, default 1
  //   GND: pin 8
  //   Din: pin 15, default 1
endmodule
