// Digital circuit 7433.dig as structural Verilog
// quad 2-input NOR gate with open-collector outputs
module _7433 (
  input  _2A,
  input  _2B,
  input  VCC,
  input  GND,
  input  _3A,
  input  _3B,
  input  _4A,
  input  _4B,
  input  _1A,
  input  _1B,
  output _2Y,
  output _3Y,
  output _4Y,
  output _1Y
);

  wire or_1_out, or_2_out, or_3_out, or_4_out;

  or or_1 (or_1_out, _1A, _1B);
  or or_2 (or_2_out, _2A, _2B);
  or or_3 (or_3_out, _3A, _3B);
  or or_4 (or_4_out, _4A, _4B);
  PowerSupply powersupply_1 (.VDD(VCC), .GND(GND));
  NFET nfet_1 (.G(or_1_out), .D(_1Y), .S(1'b0));
  NFET nfet_2 (.G(or_2_out), .D(_2Y), .S(1'b0));
  NFET nfet_3 (.G(or_3_out), .D(_3Y), .S(1'b0));
  NFET nfet_4 (.G(or_4_out), .D(_4Y), .S(1'b0));

  // Notes on the sheet:
  //   _2A: pin 5
  //   _2B: pin 6
  //   _2Y: pin 4
  //   VCC: pin 14, default 1
  //   GND: pin 7
  //   _3A: pin 8
  //   _3B: pin 9
  //   _3Y: pin 10
  //   _4A: pin 11
  //   _4B: pin 12
  //   _4Y: pin 13
  //   _1A: pin 2
  //   _1B: pin 3
  //   _1Y: pin 1
endmodule
