// Digital circuit 74367.dig as structural Verilog
// hex bus driver
module _74367 (
  input  nG1,
  input  nG2,
  input  A1,
  input  A2,
  input  A3,
  input  A4,
  input  A5,
  input  A6,
  input  VCC,
  input  GND,
  output Y1,
  output Y2,
  output Y3,
  output Y4,
  output Y5,
  output Y6
);

  wire not_1_out, not_2_out;

  not not_1 (not_1_out, nG1);
  not not_2 (not_2_out, nG2);
  PowerSupply powersupply_1 (.VDD(VCC), .GND(GND));
  assign Y1 = not_1_out ? A1 : 1'bz;  // Driver driver_1
  assign Y2 = not_1_out ? A2 : 1'bz;  // Driver driver_2
  assign Y3 = not_1_out ? A3 : 1'bz;  // Driver driver_3
  assign Y4 = not_1_out ? A4 : 1'bz;  // Driver driver_4
  assign Y5 = not_2_out ? A5 : 1'bz;  // Driver driver_5
  assign Y6 = not_2_out ? A6 : 1'bz;  // Driver driver_6

  // Notes on the sheet:
  //   nG1: pin 1
  //   nG2: pin 15
  //   A1: pin 2
  //   Y1: pin 3
  //   A2: pin 4
  //   Y2: pin 5
  //   A3: pin 6
  //   Y3: pin 7
  //   A4: pin 10
  //   Y4: pin 9
  //   A5: pin 12
  //   Y5: pin 11
  //   A6: pin 14
  //   Y6: pin 13
  //   VCC: pin 16, default 1
  //   GND: pin 8
endmodule
