// Digital circuit 7477.dig as structural Verilog
// 4-bit D latch
module _7477 (
  input  D_0,
  input  E_0_E_1,
  input  VCC,
  input  GND,
  input  D_1,
  input  D_2,
  input  E_2_E_3,
  input  D_3,
  output Q_0,
  output Q_1,
  output Q_2,
  output Q_3
);

  PowerSupply powersupply_1 (.VDD(VCC), .GND(GND));
  D_FF d_ff_1 (.D(D_0), .C(E_0_E_1), .Q(Q_0));  // open: nQ
  D_FF d_ff_2 (.D(D_1), .C(E_0_E_1), .Q(Q_1));  // open: nQ
  D_FF d_ff_3 (.D(D_2), .C(E_2_E_3), .Q(Q_2));  // open: nQ
  D_FF d_ff_4 (.D(D_3), .C(E_2_E_3), .Q(Q_3));  // open: nQ

  // Notes on the sheet:
  //   Q_0: pin 14
  //   D_0: pin 1
  //   E_0_E_1: pin 12
  //   VCC: pin 4, default 1
  //   GND: pin 11
  //   Q_1: pin 13
  //   D_1: pin 2
  //   Q_2: pin 9
  //   D_2: pin 5
  //   E_2_E_3: pin 3
  //   Q_3: pin 8
  //   D_3: pin 6
endmodule
