// Digital circuit 7492.dig as structural Verilog
// Divide by twelve counter
module _7492 (
  input  IN_A,
  input  R0_1,
  input  VCC,
  input  GND,
  input  R0_2,
  input  IN_B,
  output Q_D,
  output Q_C,
  output Q_B,
  output Q_A
);

  wire jk_ff_as_3_nq, nand_1_out;

  nand nand_1 (nand_1_out, R0_1, R0_2);
  PowerSupply powersupply_1 (.VDD(VCC), .GND(GND));
  JK_FF_AS jk_ff_as_1 (.Set(1'b0), .J(1'b1), .C(IN_A), .K(1'b1), .Clr(nand_1_out), .Q(Q_A));  // open: nQ
  JK_FF_AS jk_ff_as_2 (.Set(1'b0), .J(jk_ff_as_3_nq), .C(IN_B), .K(1'b1), .Clr(nand_1_out), .Q(Q_B));  // open: nQ
  JK_FF_AS jk_ff_as_3 (.Set(1'b0), .J(Q_B), .C(IN_B), .K(1'b1), .Clr(nand_1_out), .Q(Q_C), .nQ(jk_ff_as_3_nq));
  JK_FF_AS jk_ff_as_4 (.Set(1'b0), .J(1'b1), .C(Q_C), .K(1'b1), .Clr(nand_1_out), .Q(Q_D));  // open: nQ

  // Notes on the sheet:
  //   Q_D: pin 8
  //   IN_A: pin 14
  //   R0_1: pin 6
  //   VCC: pin 5, default 1
  //   GND: pin 10
  //   R0_2: pin 7
  //   Q_C: pin 9
  //   Q_B: pin 11
  //   Q_A: pin 12
  //   IN_B: pin 1
endmodule
