// Digital circuit 15 bit div 11 bit blocked version E 05 feb 2022.dig as structural Verilog
// 15 bit div 11 bit blocked version E 05 feb 2022
module _15_bit_div_11_bit_blocked_version_E_05_feb_2022 (
  input  N0,
  input  N1,
  input  N2,
  input  N3,
  input  N4,
  input  N5,
  input  N6,
  input  N7,
  input  N8,
  input  N9,
  input  N10,
  input  N11,
  input  N12,
  input  N13,
  input  N14,
  input  D0,
  input  D1,
  input  D2,
  input  D3,
  input  D4,
  input  D5,
  input  D6,
  input  D7,
  input  D8,
  input  D9,
  input  D10,
  output Q0,
  output Q1,
  output Q2,
  output Q3,
  output Q4,
  output Q5,
  output Q6,
  output Q7,
  output Q8,
  output Q9,
  output Q10,
  output Q11,
  output Q12,
  output Q13,
  output Q14,
  output R0,
  output R1,
  output R2,
  output R3,
  output R4,
  output R5,
  output R6,
  output R7,
  output R8,
  output R9,
  output R10
);

  wire _15_bit_div_11_bit_triple_block_version_b_05_feb_2022_1_f,
       _15_bit_div_11_bit_triple_block_version_b_05_feb_2022_1_y0,
       _15_bit_div_11_bit_triple_block_version_b_05_feb_2022_1_y1,
       _15_bit_div_11_bit_triple_block_version_b_05_feb_2022_1_y2,
       _15_bit_div_11_bit_triple_block_version_b_05_feb_2022_1_y3,
       _15_bit_div_11_bit_triple_block_version_b_05_feb_2022_1_y4,
       _15_bit_div_11_bit_triple_block_version_b_05_feb_2022_1_y5,
       _15_bit_div_11_bit_triple_block_version_b_05_feb_2022_1_y6,
       _15_bit_div_11_bit_triple_block_version_b_05_feb_2022_1_y7,
       _15_bit_div_11_bit_triple_block_version_b_05_feb_2022_1_y8,
       _15_bit_div_11_bit_triple_block_version_b_05_feb_2022_1_y9,
       _15_bit_div_11_bit_triple_block_version_b_05_feb_2022_1_y10,
       _15_bit_div_11_bit_triple_block_version_b_05_feb_2022_1_z0,
       _15_bit_div_11_bit_triple_block_version_b_05_feb_2022_1_z1,
       _15_bit_div_11_bit_triple_block_version_b_05_feb_2022_1_z2,
       _15_bit_div_11_bit_triple_block_version_b_05_feb_2022_1_z3,
       _15_bit_div_11_bit_triple_block_version_b_05_feb_2022_1_z4,
       _15_bit_div_11_bit_triple_block_version_b_05_feb_2022_1_z5,
       _15_bit_div_11_bit_triple_block_version_b_05_feb_2022_1_z6,
       _15_bit_div_11_bit_triple_block_version_b_05_feb_2022_1_z7,
       _15_bit_div_11_bit_triple_block_version_b_05_feb_2022_1_z8,
       _15_bit_div_11_bit_triple_block_version_b_05_feb_2022_1_z9,
       _15_bit_div_11_bit_triple_block_version_b_05_feb_2022_1_z10,
       _15_bit_div_11_bit_triple_block_version_b_05_feb_2022_1_z11,
       _15_bit_div_11_bit_triple_block_version_b_05_feb_2022_1_z12,
       _15_bit_div_11_bit_triple_block_version_b_05_feb_2022_1_z13,
       _15_bit_div_11_bit_triple_block_version_b_05_feb_2022_1_z14,
       _15_bit_div_11_bit_triple_block_version_b_05_feb_2022_2_f,
       _15_bit_div_11_bit_triple_block_version_b_05_feb_2022_2_y0,
       _15_bit_div_11_bit_triple_block_version_b_05_feb_2022_2_y1,
       _15_bit_div_11_bit_triple_block_version_b_05_feb_2022_2_y2,
       _15_bit_div_11_bit_triple_block_version_b_05_feb_2022_2_y3,
       _15_bit_div_11_bit_triple_block_version_b_05_feb_2022_2_y4,
       _15_bit_div_11_bit_triple_block_version_b_05_feb_2022_2_y5,
       _15_bit_div_11_bit_triple_block_version_b_05_feb_2022_2_y6,
       _15_bit_div_11_bit_triple_block_version_b_05_feb_2022_2_y7,
       _15_bit_div_11_bit_triple_block_version_b_05_feb_2022_2_y8,
       _15_bit_div_11_bit_triple_block_version_b_05_feb_2022_2_y9,
       _15_bit_div_11_bit_triple_block_version_b_05_feb_2022_2_y10,
       _15_bit_div_11_bit_triple_block_version_b_05_feb_2022_2_z0,
       _15_bit_div_11_bit_triple_block_version_b_05_feb_2022_2_z1,
       _15_bit_div_11_bit_triple_block_version_b_05_feb_2022_2_z2,
       _15_bit_div_11_bit_triple_block_version_b_05_feb_2022_2_z3,
       _15_bit_div_11_bit_triple_block_version_b_05_feb_2022_2_z4,
       _15_bit_div_11_bit_triple_block_version_b_05_feb_2022_2_z5,
       _15_bit_div_11_bit_triple_block_version_b_05_feb_2022_2_z6,
       _15_bit_div_11_bit_triple_block_version_b_05_feb_2022_2_z7,
       _15_bit_div_11_bit_triple_block_version_b_05_feb_2022_2_z8,
       _15_bit_div_11_bit_triple_block_version_b_05_feb_2022_2_z9,
       _15_bit_div_11_bit_triple_block_version_b_05_feb_2022_2_z10,
       _15_bit_div_11_bit_triple_block_version_b_05_feb_2022_2_z11,
       _15_bit_div_11_bit_triple_block_version_b_05_feb_2022_2_z12,
       _15_bit_div_11_bit_triple_block_version_b_05_feb_2022_2_z13,
       _15_bit_div_11_bit_triple_block_version_b_05_feb_2022_2_z14,
       _15_bit_div_11_bit_triple_block_version_b_05_feb_2022_3_f,
       _15_bit_div_11_bit_triple_block_version_b_05_feb_2022_3_y0,
       _15_bit_div_11_bit_triple_block_version_b_05_feb_2022_3_y1,
       _15_bit_div_11_bit_triple_block_version_b_05_feb_2022_3_y2,
       _15_bit_div_11_bit_triple_block_version_b_05_feb_2022_3_y3,
       _15_bit_div_11_bit_triple_block_version_b_05_feb_2022_3_y4,
       _15_bit_div_11_bit_triple_block_version_b_05_feb_2022_3_y5,
       _15_bit_div_11_bit_triple_block_version_b_05_feb_2022_3_y6,
       _15_bit_div_11_bit_triple_block_version_b_05_feb_2022_3_y7,
       _15_bit_div_11_bit_triple_block_version_b_05_feb_2022_3_y8,
       _15_bit_div_11_bit_triple_block_version_b_05_feb_2022_3_y9,
       _15_bit_div_11_bit_triple_block_version_b_05_feb_2022_3_y10,
       _15_bit_div_11_bit_triple_block_version_b_05_feb_2022_3_z0,
       _15_bit_div_11_bit_triple_block_version_b_05_feb_2022_3_z1,
       _15_bit_div_11_bit_triple_block_version_b_05_feb_2022_3_z2,
       _15_bit_div_11_bit_triple_block_version_b_05_feb_2022_3_z3,
       _15_bit_div_11_bit_triple_block_version_b_05_feb_2022_3_z4,
       _15_bit_div_11_bit_triple_block_version_b_05_feb_2022_3_z5,
       _15_bit_div_11_bit_triple_block_version_b_05_feb_2022_3_z6,
       _15_bit_div_11_bit_triple_block_version_b_05_feb_2022_3_z7,
       _15_bit_div_11_bit_triple_block_version_b_05_feb_2022_3_z8,
       _15_bit_div_11_bit_triple_block_version_b_05_feb_2022_3_z9,
       _15_bit_div_11_bit_triple_block_version_b_05_feb_2022_3_z10,
       _15_bit_div_11_bit_triple_block_version_b_05_feb_2022_3_z11,
       _15_bit_div_11_bit_triple_block_version_b_05_feb_2022_3_z12,
       _15_bit_div_11_bit_triple_block_version_b_05_feb_2022_3_z13,
       _15_bit_div_11_bit_triple_block_version_b_05_feb_2022_3_z14,
       _15_bit_div_11_bit_triple_block_version_b_05_feb_2022_4_f,
       _15_bit_div_11_bit_triple_block_version_b_05_feb_2022_4_y0,
       _15_bit_div_11_bit_triple_block_version_b_05_feb_2022_4_y1,
       _15_bit_div_11_bit_triple_block_version_b_05_feb_2022_4_y2,
       _15_bit_div_11_bit_triple_block_version_b_05_feb_2022_4_y3,
       _15_bit_div_11_bit_triple_block_version_b_05_feb_2022_4_y4,
       _15_bit_div_11_bit_triple_block_version_b_05_feb_2022_4_y5,
       _15_bit_div_11_bit_triple_block_version_b_05_feb_2022_4_y6,
       _15_bit_div_11_bit_triple_block_version_b_05_feb_2022_4_y7,
       _15_bit_div_11_bit_triple_block_version_b_05_feb_2022_4_y8,
       _15_bit_div_11_bit_triple_block_version_b_05_feb_2022_4_y9,
       _15_bit_div_11_bit_triple_block_version_b_05_feb_2022_4_y10,
       _15_bit_div_11_bit_triple_block_version_b_05_feb_2022_4_z0,
       _15_bit_div_11_bit_triple_block_version_b_05_feb_2022_4_z1,
       _15_bit_div_11_bit_triple_block_version_b_05_feb_2022_4_z2,
       _15_bit_div_11_bit_triple_block_version_b_05_feb_2022_4_z3,
       _15_bit_div_11_bit_triple_block_version_b_05_feb_2022_4_z4,
       _15_bit_div_11_bit_triple_block_version_b_05_feb_2022_4_z5,
       _15_bit_div_11_bit_triple_block_version_b_05_feb_2022_4_z6,
       _15_bit_div_11_bit_triple_block_version_b_05_feb_2022_4_z7,
       _15_bit_div_11_bit_triple_block_version_b_05_feb_2022_4_z8,
       _15_bit_div_11_bit_triple_block_version_b_05_feb_2022_4_z9,
       _15_bit_div_11_bit_triple_block_version_b_05_feb_2022_4_z10,
       _15_bit_div_11_bit_triple_block_version_b_05_feb_2022_4_z11,
       _15_bit_div_11_bit_triple_block_version_b_05_feb_2022_4_z12,
       _15_bit_div_11_bit_triple_block_version_b_05_feb_2022_4_z13,
       _15_bit_div_11_bit_triple_block_version_b_05_feb_2022_4_z14,
       _15_bit_div_11_bit_triple_block_version_b_05_feb_2022_5_y1,
       _15_bit_div_11_bit_triple_block_version_b_05_feb_2022_5_y2,
       _15_bit_div_11_bit_triple_block_version_b_05_feb_2022_5_y3,
       _15_bit_div_11_bit_triple_block_version_b_05_feb_2022_5_y5,
       _15_bit_div_11_bit_triple_block_version_b_05_feb_2022_5_y6,
       _15_bit_div_11_bit_triple_block_version_b_05_feb_2022_5_y7,
       _15_bit_div_11_bit_triple_block_version_b_05_feb_2022_5_y9,
       _15_bit_div_11_bit_triple_block_version_b_05_feb_2022_5_y10, _74181_1_pin2, _74181_1_pin3,
       _74181_1_pin7, _74181_2_pin2, _74181_2_pin7, _74181_3_pin2, _74181_3_pin7, _74182_1_pin1,
       _74182_1_pin2, _74182_1_pin3, _74182_1_pin4, _74182_1_pin7, _74182_1_pin9, _74182_1_pin10,
       _74182_1_pin13, _74182_1_pin14, _74182_1_pin15, undriven, undriven_2, undriven_3, undriven_4,
       undriven_5, undriven_6;

  LED led_1 (.in(N14));
  LED led_2 (.in(N12));
  LED led_3 (.in(N13));
  LED led_4 (.in(N10));
  LED led_5 (.in(N11));
  LED led_6 (.in(N8));
  LED led_7 (.in(N9));
  LED led_8 (.in(D9));
  LED led_9 (.in(D10));
  LED led_10 (.in(N6));
  LED led_11 (.in(N7));
  LED led_12 (.in(D7));
  LED led_13 (.in(D8));
  LED led_14 (.in(N4));
  LED led_15 (.in(N5));
  LED led_16 (.in(D5));
  LED led_17 (.in(D6));
  LED led_18 (.in(N2));
  LED led_19 (.in(N3));
  LED led_20 (.in(D3));
  LED led_21 (.in(D4));
  LED led_22 (.in(N0));
  LED led_23 (.in(N1));
  LED led_24 (.in(D1));
  LED led_25 (.in(D2));
  LED led_26 (.in(D0));
  Seven_Seg_Hex seven_seg_hex_1 (.d({1'b0, N14, N13, N12}), .dp(1'b0));
  Seven_Seg_Hex seven_seg_hex_2 (.d({1'b0, D10, D9, D8}), .dp(1'b0));
  Seven_Seg_Hex seven_seg_hex_3 (.d({N11, N10, N9, N8}), .dp(1'b0));
  Seven_Seg_Hex seven_seg_hex_4 (.d({D7, D6, D5, D4}), .dp(1'b0));
  Seven_Seg_Hex seven_seg_hex_5 (.d({N7, N6, N5, N4}), .dp(1'b0));
  Seven_Seg_Hex seven_seg_hex_6 (.d({D3, D2, D1, D0}), .dp(1'b0));
  Seven_Seg_Hex seven_seg_hex_7 (.d({N3, N2, N1, N0}), .dp(1'b0));
  _15_bit_div_11_bit_triple_block_version_B_05_feb_2022 _15_bit_div_11_bit_triple_block_version_b_05_feb_2022_1 (
    .D0(D0), .D1(D1), .D2(D2), .D3(D3), .D4(D4), .D5(D5), .D6(D6), .D7(D7), .D8(D8), .D9(D9), .D10(D10),
    .N0(N0), .N1(N1), .N2(N2), .N3(N3), .N4(N4), .N5(N5), .N6(N6), .N7(N7), .N8(N8), .N9(N9), .N10(N10),
    .N11(N11), .N12(N12), .N13(N13), .N14(N14), .S(1'b0), .A0(1'b0), .A1(1'b0), .A2(1'b0), .A3(1'b0),
    .A4(1'b0), .A5(1'b0), .A6(1'b0), .A7(1'b0), .A8(1'b0), .A9(1'b0), .A10(1'b0),
    .Z0(_15_bit_div_11_bit_triple_block_version_b_05_feb_2022_1_z0),
    .Z1(_15_bit_div_11_bit_triple_block_version_b_05_feb_2022_1_z1),
    .Z2(_15_bit_div_11_bit_triple_block_version_b_05_feb_2022_1_z2),
    .Z3(_15_bit_div_11_bit_triple_block_version_b_05_feb_2022_1_z3),
    .Z4(_15_bit_div_11_bit_triple_block_version_b_05_feb_2022_1_z4),
    .Z5(_15_bit_div_11_bit_triple_block_version_b_05_feb_2022_1_z5),
    .Z6(_15_bit_div_11_bit_triple_block_version_b_05_feb_2022_1_z6),
    .Z7(_15_bit_div_11_bit_triple_block_version_b_05_feb_2022_1_z7),
    .Z8(_15_bit_div_11_bit_triple_block_version_b_05_feb_2022_1_z8),
    .Z9(_15_bit_div_11_bit_triple_block_version_b_05_feb_2022_1_z9),
    .Z10(_15_bit_div_11_bit_triple_block_version_b_05_feb_2022_1_z10),
    .Z11(_15_bit_div_11_bit_triple_block_version_b_05_feb_2022_1_z11),
    .Z12(_15_bit_div_11_bit_triple_block_version_b_05_feb_2022_1_z12),
    .Z13(_15_bit_div_11_bit_triple_block_version_b_05_feb_2022_1_z13),
    .Z14(_15_bit_div_11_bit_triple_block_version_b_05_feb_2022_1_z14),
    .F(_15_bit_div_11_bit_triple_block_version_b_05_feb_2022_1_f),
    .Y0(_15_bit_div_11_bit_triple_block_version_b_05_feb_2022_1_y0),
    .Y1(_15_bit_div_11_bit_triple_block_version_b_05_feb_2022_1_y1),
    .Y2(_15_bit_div_11_bit_triple_block_version_b_05_feb_2022_1_y2),
    .Y3(_15_bit_div_11_bit_triple_block_version_b_05_feb_2022_1_y3),
    .Y4(_15_bit_div_11_bit_triple_block_version_b_05_feb_2022_1_y4),
    .Y5(_15_bit_div_11_bit_triple_block_version_b_05_feb_2022_1_y5),
    .Y6(_15_bit_div_11_bit_triple_block_version_b_05_feb_2022_1_y6),
    .Y7(_15_bit_div_11_bit_triple_block_version_b_05_feb_2022_1_y7),
    .Y8(_15_bit_div_11_bit_triple_block_version_b_05_feb_2022_1_y8),
    .Y9(_15_bit_div_11_bit_triple_block_version_b_05_feb_2022_1_y9),
    .Y10(_15_bit_div_11_bit_triple_block_version_b_05_feb_2022_1_y10));
  LED led_27 (.in(_15_bit_div_11_bit_triple_block_version_b_05_feb_2022_1_y10));
  LED led_28 (.in(_15_bit_div_11_bit_triple_block_version_b_05_feb_2022_1_f));
  LED led_29 (.in(_15_bit_div_11_bit_triple_block_version_b_05_feb_2022_1_y8));
  LED led_30 (.in(_15_bit_div_11_bit_triple_block_version_b_05_feb_2022_1_y9));
  LED led_31 (.in(_15_bit_div_11_bit_triple_block_version_b_05_feb_2022_1_y6));
  LED led_32 (.in(_15_bit_div_11_bit_triple_block_version_b_05_feb_2022_1_y7));
  LED led_33 (.in(_15_bit_div_11_bit_triple_block_version_b_05_feb_2022_1_y4));
  LED led_34 (.in(_15_bit_div_11_bit_triple_block_version_b_05_feb_2022_1_y5));
  LED led_35 (.in(_15_bit_div_11_bit_triple_block_version_b_05_feb_2022_1_y2));
  LED led_36 (.in(_15_bit_div_11_bit_triple_block_version_b_05_feb_2022_1_y3));
  LED led_37 (.in(_15_bit_div_11_bit_triple_block_version_b_05_feb_2022_1_y0));
  LED led_38 (.in(_15_bit_div_11_bit_triple_block_version_b_05_feb_2022_1_y1));
  _15_bit_div_11_bit_triple_block_version_B_05_feb_2022 _15_bit_div_11_bit_triple_block_version_b_05_feb_2022_2 (
    .D0(D0), .D1(D1), .D2(D2), .D3(D3), .D4(D4), .D5(D5), .D6(D6), .D7(D7), .D8(D8), .D9(D9), .D10(D10),
    .N0(_15_bit_div_11_bit_triple_block_version_b_05_feb_2022_1_z0),
    .N1(_15_bit_div_11_bit_triple_block_version_b_05_feb_2022_1_z1),
    .N2(_15_bit_div_11_bit_triple_block_version_b_05_feb_2022_1_z2),
    .N3(_15_bit_div_11_bit_triple_block_version_b_05_feb_2022_1_z3),
    .N4(_15_bit_div_11_bit_triple_block_version_b_05_feb_2022_1_z4),
    .N5(_15_bit_div_11_bit_triple_block_version_b_05_feb_2022_1_z5),
    .N6(_15_bit_div_11_bit_triple_block_version_b_05_feb_2022_1_z6),
    .N7(_15_bit_div_11_bit_triple_block_version_b_05_feb_2022_1_z7),
    .N8(_15_bit_div_11_bit_triple_block_version_b_05_feb_2022_1_z8),
    .N9(_15_bit_div_11_bit_triple_block_version_b_05_feb_2022_1_z9),
    .N10(_15_bit_div_11_bit_triple_block_version_b_05_feb_2022_1_z10),
    .N11(_15_bit_div_11_bit_triple_block_version_b_05_feb_2022_1_z11),
    .N12(_15_bit_div_11_bit_triple_block_version_b_05_feb_2022_1_z12),
    .N13(_15_bit_div_11_bit_triple_block_version_b_05_feb_2022_1_z13),
    .N14(_15_bit_div_11_bit_triple_block_version_b_05_feb_2022_1_z14),
    .S(_15_bit_div_11_bit_triple_block_version_b_05_feb_2022_1_f),
    .A0(_15_bit_div_11_bit_triple_block_version_b_05_feb_2022_1_y0),
    .A1(_15_bit_div_11_bit_triple_block_version_b_05_feb_2022_1_y1),
    .A2(_15_bit_div_11_bit_triple_block_version_b_05_feb_2022_1_y2),
    .A3(_15_bit_div_11_bit_triple_block_version_b_05_feb_2022_1_y3),
    .A4(_15_bit_div_11_bit_triple_block_version_b_05_feb_2022_1_y4),
    .A5(_15_bit_div_11_bit_triple_block_version_b_05_feb_2022_1_y5),
    .A6(_15_bit_div_11_bit_triple_block_version_b_05_feb_2022_1_y6),
    .A7(_15_bit_div_11_bit_triple_block_version_b_05_feb_2022_1_y7),
    .A8(_15_bit_div_11_bit_triple_block_version_b_05_feb_2022_1_y8),
    .A9(_15_bit_div_11_bit_triple_block_version_b_05_feb_2022_1_y9),
    .A10(_15_bit_div_11_bit_triple_block_version_b_05_feb_2022_1_y10),
    .Z0(_15_bit_div_11_bit_triple_block_version_b_05_feb_2022_2_z0),
    .Z1(_15_bit_div_11_bit_triple_block_version_b_05_feb_2022_2_z1),
    .Z2(_15_bit_div_11_bit_triple_block_version_b_05_feb_2022_2_z2),
    .Z3(_15_bit_div_11_bit_triple_block_version_b_05_feb_2022_2_z3),
    .Z4(_15_bit_div_11_bit_triple_block_version_b_05_feb_2022_2_z4),
    .Z5(_15_bit_div_11_bit_triple_block_version_b_05_feb_2022_2_z5),
    .Z6(_15_bit_div_11_bit_triple_block_version_b_05_feb_2022_2_z6),
    .Z7(_15_bit_div_11_bit_triple_block_version_b_05_feb_2022_2_z7),
    .Z8(_15_bit_div_11_bit_triple_block_version_b_05_feb_2022_2_z8),
    .Z9(_15_bit_div_11_bit_triple_block_version_b_05_feb_2022_2_z9),
    .Z10(_15_bit_div_11_bit_triple_block_version_b_05_feb_2022_2_z10),
    .Z11(_15_bit_div_11_bit_triple_block_version_b_05_feb_2022_2_z11),
    .Z12(_15_bit_div_11_bit_triple_block_version_b_05_feb_2022_2_z12),
    .Z13(_15_bit_div_11_bit_triple_block_version_b_05_feb_2022_2_z13),
    .Z14(_15_bit_div_11_bit_triple_block_version_b_05_feb_2022_2_z14),
    .F(_15_bit_div_11_bit_triple_block_version_b_05_feb_2022_2_f),
    .Y0(_15_bit_div_11_bit_triple_block_version_b_05_feb_2022_2_y0),
    .Y1(_15_bit_div_11_bit_triple_block_version_b_05_feb_2022_2_y1),
    .Y2(_15_bit_div_11_bit_triple_block_version_b_05_feb_2022_2_y2),
    .Y3(_15_bit_div_11_bit_triple_block_version_b_05_feb_2022_2_y3),
    .Y4(_15_bit_div_11_bit_triple_block_version_b_05_feb_2022_2_y4),
    .Y5(_15_bit_div_11_bit_triple_block_version_b_05_feb_2022_2_y5),
    .Y6(_15_bit_div_11_bit_triple_block_version_b_05_feb_2022_2_y6),
    .Y7(_15_bit_div_11_bit_triple_block_version_b_05_feb_2022_2_y7),
    .Y8(_15_bit_div_11_bit_triple_block_version_b_05_feb_2022_2_y8),
    .Y9(_15_bit_div_11_bit_triple_block_version_b_05_feb_2022_2_y9),
    .Y10(_15_bit_div_11_bit_triple_block_version_b_05_feb_2022_2_y10));
  LED led_39 (.in(_15_bit_div_11_bit_triple_block_version_b_05_feb_2022_2_f));
  LED led_40 (.in(_15_bit_div_11_bit_triple_block_version_b_05_feb_2022_2_y9));
  LED led_41 (.in(_15_bit_div_11_bit_triple_block_version_b_05_feb_2022_2_y10));
  _74181 _74181_1 (
    .pin1(D0), .pin2(_74181_1_pin2), .pin3(_74181_1_pin3), .pin4(1'b0), .pin5(1'b0), .pin6(_74181_1_pin3),
    .pin7(_74181_1_pin7), .pin8(1'b0), .pin9(R0), .pin10(R1), .pin11(R2), .pin12(1'b0));  // open: pin13, pin14, pin15, pin16, pin17, pin18, pin19, pin20, pin21, pin22, pin23, pin24
  PullUp pullup_1 (.out(_74181_1_pin7));
  LED led_42 (.in(_15_bit_div_11_bit_triple_block_version_b_05_feb_2022_2_y7));
  LED led_43 (.in(_15_bit_div_11_bit_triple_block_version_b_05_feb_2022_2_y8));
  LED led_44 (.in(_15_bit_div_11_bit_triple_block_version_b_05_feb_2022_2_y5));
  LED led_45 (.in(_15_bit_div_11_bit_triple_block_version_b_05_feb_2022_2_y6));
  LED led_46 (.in(_15_bit_div_11_bit_triple_block_version_b_05_feb_2022_2_y3));
  LED led_47 (.in(_15_bit_div_11_bit_triple_block_version_b_05_feb_2022_2_y4));
  LED led_48 (.in(_15_bit_div_11_bit_triple_block_version_b_05_feb_2022_2_y1));
  LED led_49 (.in(_15_bit_div_11_bit_triple_block_version_b_05_feb_2022_2_y2));
  LED led_50 (.in(undriven_2));
  LED led_51 (.in(undriven));
  LED led_52 (.in(_15_bit_div_11_bit_triple_block_version_b_05_feb_2022_2_y0));
  _15_bit_div_11_bit_triple_block_version_B_05_feb_2022 _15_bit_div_11_bit_triple_block_version_b_05_feb_2022_3 (
    .D0(D0), .D1(D1), .D2(D2), .D3(D3), .D4(D4), .D5(D5), .D6(D6), .D7(D7), .D8(D8), .D9(D9), .D10(D10),
    .N0(_15_bit_div_11_bit_triple_block_version_b_05_feb_2022_2_z0),
    .N1(_15_bit_div_11_bit_triple_block_version_b_05_feb_2022_2_z1),
    .N2(_15_bit_div_11_bit_triple_block_version_b_05_feb_2022_2_z2),
    .N3(_15_bit_div_11_bit_triple_block_version_b_05_feb_2022_2_z3),
    .N4(_15_bit_div_11_bit_triple_block_version_b_05_feb_2022_2_z4),
    .N5(_15_bit_div_11_bit_triple_block_version_b_05_feb_2022_2_z5),
    .N6(_15_bit_div_11_bit_triple_block_version_b_05_feb_2022_2_z6),
    .N7(_15_bit_div_11_bit_triple_block_version_b_05_feb_2022_2_z7),
    .N8(_15_bit_div_11_bit_triple_block_version_b_05_feb_2022_2_z8),
    .N9(_15_bit_div_11_bit_triple_block_version_b_05_feb_2022_2_z9),
    .N10(_15_bit_div_11_bit_triple_block_version_b_05_feb_2022_2_z10),
    .N11(_15_bit_div_11_bit_triple_block_version_b_05_feb_2022_2_z11),
    .N12(_15_bit_div_11_bit_triple_block_version_b_05_feb_2022_2_z12),
    .N13(_15_bit_div_11_bit_triple_block_version_b_05_feb_2022_2_z13),
    .N14(_15_bit_div_11_bit_triple_block_version_b_05_feb_2022_2_z14),
    .S(_15_bit_div_11_bit_triple_block_version_b_05_feb_2022_2_f),
    .A0(_15_bit_div_11_bit_triple_block_version_b_05_feb_2022_2_y0),
    .A1(_15_bit_div_11_bit_triple_block_version_b_05_feb_2022_2_y1),
    .A2(_15_bit_div_11_bit_triple_block_version_b_05_feb_2022_2_y2),
    .A3(_15_bit_div_11_bit_triple_block_version_b_05_feb_2022_2_y3),
    .A4(_15_bit_div_11_bit_triple_block_version_b_05_feb_2022_2_y4),
    .A5(_15_bit_div_11_bit_triple_block_version_b_05_feb_2022_2_y5),
    .A6(_15_bit_div_11_bit_triple_block_version_b_05_feb_2022_2_y6),
    .A7(_15_bit_div_11_bit_triple_block_version_b_05_feb_2022_2_y7),
    .A8(_15_bit_div_11_bit_triple_block_version_b_05_feb_2022_2_y8),
    .A9(_15_bit_div_11_bit_triple_block_version_b_05_feb_2022_2_y9),
    .A10(_15_bit_div_11_bit_triple_block_version_b_05_feb_2022_2_y10),
    .Z0(_15_bit_div_11_bit_triple_block_version_b_05_feb_2022_3_z0),
    .Z1(_15_bit_div_11_bit_triple_block_version_b_05_feb_2022_3_z1),
    .Z2(_15_bit_div_11_bit_triple_block_version_b_05_feb_2022_3_z2),
    .Z3(_15_bit_div_11_bit_triple_block_version_b_05_feb_2022_3_z3),
    .Z4(_15_bit_div_11_bit_triple_block_version_b_05_feb_2022_3_z4),
    .Z5(_15_bit_div_11_bit_triple_block_version_b_05_feb_2022_3_z5),
    .Z6(_15_bit_div_11_bit_triple_block_version_b_05_feb_2022_3_z6),
    .Z7(_15_bit_div_11_bit_triple_block_version_b_05_feb_2022_3_z7),
    .Z8(_15_bit_div_11_bit_triple_block_version_b_05_feb_2022_3_z8),
    .Z9(_15_bit_div_11_bit_triple_block_version_b_05_feb_2022_3_z9),
    .Z10(_15_bit_div_11_bit_triple_block_version_b_05_feb_2022_3_z10),
    .Z11(_15_bit_div_11_bit_triple_block_version_b_05_feb_2022_3_z11),
    .Z12(_15_bit_div_11_bit_triple_block_version_b_05_feb_2022_3_z12),
    .Z13(_15_bit_div_11_bit_triple_block_version_b_05_feb_2022_3_z13),
    .Z14(_15_bit_div_11_bit_triple_block_version_b_05_feb_2022_3_z14),
    .F(_15_bit_div_11_bit_triple_block_version_b_05_feb_2022_3_f),
    .Y0(_15_bit_div_11_bit_triple_block_version_b_05_feb_2022_3_y0),
    .Y1(_15_bit_div_11_bit_triple_block_version_b_05_feb_2022_3_y1),
    .Y2(_15_bit_div_11_bit_triple_block_version_b_05_feb_2022_3_y2),
    .Y3(_15_bit_div_11_bit_triple_block_version_b_05_feb_2022_3_y3),
    .Y4(_15_bit_div_11_bit_triple_block_version_b_05_feb_2022_3_y4),
    .Y5(_15_bit_div_11_bit_triple_block_version_b_05_feb_2022_3_y5),
    .Y6(_15_bit_div_11_bit_triple_block_version_b_05_feb_2022_3_y6),
    .Y7(_15_bit_div_11_bit_triple_block_version_b_05_feb_2022_3_y7),
    .Y8(_15_bit_div_11_bit_triple_block_version_b_05_feb_2022_3_y8),
    .Y9(_15_bit_div_11_bit_triple_block_version_b_05_feb_2022_3_y9),
    .Y10(_15_bit_div_11_bit_triple_block_version_b_05_feb_2022_3_y10));
  _74181 _74181_2 (
    .pin1(D4), .pin2(_74181_2_pin2), .pin3(_74181_1_pin3), .pin4(1'b0), .pin5(1'b0), .pin6(_74181_1_pin3),
    .pin7(_74181_2_pin7), .pin8(1'b0), .pin9(R4), .pin10(R5), .pin11(R6), .pin12(1'b0));  // open: pin13, pin14, pin15, pin16, pin17, pin18, pin19, pin20, pin21, pin22, pin23, pin24
  LED led_53 (.in(_15_bit_div_11_bit_triple_block_version_b_05_feb_2022_3_f));
  LED led_54 (.in(undriven_4));
  LED led_55 (.in(undriven_3));
  LED led_56 (.in(_15_bit_div_11_bit_triple_block_version_b_05_feb_2022_3_y9));
  LED led_57 (.in(_15_bit_div_11_bit_triple_block_version_b_05_feb_2022_3_y10));
  LED led_58 (.in(_15_bit_div_11_bit_triple_block_version_b_05_feb_2022_3_y7));
  LED led_59 (.in(_15_bit_div_11_bit_triple_block_version_b_05_feb_2022_3_y8));
  LED led_60 (.in(_15_bit_div_11_bit_triple_block_version_b_05_feb_2022_3_y5));
  LED led_61 (.in(_15_bit_div_11_bit_triple_block_version_b_05_feb_2022_3_y6));
  LED led_62 (.in(_15_bit_div_11_bit_triple_block_version_b_05_feb_2022_3_y3));
  LED led_63 (.in(_15_bit_div_11_bit_triple_block_version_b_05_feb_2022_3_y4));
  LED led_64 (.in(_15_bit_div_11_bit_triple_block_version_b_05_feb_2022_3_y1));
  LED led_65 (.in(_15_bit_div_11_bit_triple_block_version_b_05_feb_2022_3_y2));
  LED led_66 (.in(_15_bit_div_11_bit_triple_block_version_b_05_feb_2022_3_y0));
  _74181 _74181_3 (
    .pin1(D8), .pin2(_74181_3_pin2), .pin3(_74181_1_pin3), .pin4(1'b0), .pin5(1'b0), .pin6(_74181_1_pin3),
    .pin7(_74181_3_pin7), .pin8(1'b0), .pin9(R8), .pin10(R9), .pin11(R10), .pin12(1'b0));  // open: pin13, pin14, pin15, pin16, pin17, pin18, pin19, pin20, pin21, pin22, pin23, pin24
  _7404 _7404_1 (
    .pin1(1'b0), .pin3(1'b0), .pin5(_74181_1_pin3), .pin6(Q0), .pin7(1'b0), .pin9(1'b0), .pin11(1'b0),
    .pin13(1'b0), .pin14(1'b1));  // open: pin2, pin4, pin8, pin10, pin12
  _15_bit_div_11_bit_triple_block_version_B_05_feb_2022 _15_bit_div_11_bit_triple_block_version_b_05_feb_2022_4 (
    .D0(D0), .D1(D1), .D2(D2), .D3(D3), .D4(D4), .D5(D5), .D6(D6), .D7(D7), .D8(D8), .D9(D9), .D10(D10),
    .N0(_15_bit_div_11_bit_triple_block_version_b_05_feb_2022_3_z0),
    .N1(_15_bit_div_11_bit_triple_block_version_b_05_feb_2022_3_z1),
    .N2(_15_bit_div_11_bit_triple_block_version_b_05_feb_2022_3_z2),
    .N3(_15_bit_div_11_bit_triple_block_version_b_05_feb_2022_3_z3),
    .N4(_15_bit_div_11_bit_triple_block_version_b_05_feb_2022_3_z4),
    .N5(_15_bit_div_11_bit_triple_block_version_b_05_feb_2022_3_z5),
    .N6(_15_bit_div_11_bit_triple_block_version_b_05_feb_2022_3_z6),
    .N7(_15_bit_div_11_bit_triple_block_version_b_05_feb_2022_3_z7),
    .N8(_15_bit_div_11_bit_triple_block_version_b_05_feb_2022_3_z8),
    .N9(_15_bit_div_11_bit_triple_block_version_b_05_feb_2022_3_z9),
    .N10(_15_bit_div_11_bit_triple_block_version_b_05_feb_2022_3_z10),
    .N11(_15_bit_div_11_bit_triple_block_version_b_05_feb_2022_3_z11),
    .N12(_15_bit_div_11_bit_triple_block_version_b_05_feb_2022_3_z12),
    .N13(_15_bit_div_11_bit_triple_block_version_b_05_feb_2022_3_z13),
    .N14(_15_bit_div_11_bit_triple_block_version_b_05_feb_2022_3_z14),
    .S(_15_bit_div_11_bit_triple_block_version_b_05_feb_2022_3_f),
    .A0(_15_bit_div_11_bit_triple_block_version_b_05_feb_2022_3_y0),
    .A1(_15_bit_div_11_bit_triple_block_version_b_05_feb_2022_3_y1),
    .A2(_15_bit_div_11_bit_triple_block_version_b_05_feb_2022_3_y2),
    .A3(_15_bit_div_11_bit_triple_block_version_b_05_feb_2022_3_y3),
    .A4(_15_bit_div_11_bit_triple_block_version_b_05_feb_2022_3_y4),
    .A5(_15_bit_div_11_bit_triple_block_version_b_05_feb_2022_3_y5),
    .A6(_15_bit_div_11_bit_triple_block_version_b_05_feb_2022_3_y6),
    .A7(_15_bit_div_11_bit_triple_block_version_b_05_feb_2022_3_y7),
    .A8(_15_bit_div_11_bit_triple_block_version_b_05_feb_2022_3_y8),
    .A9(_15_bit_div_11_bit_triple_block_version_b_05_feb_2022_3_y9),
    .A10(_15_bit_div_11_bit_triple_block_version_b_05_feb_2022_3_y10),
    .Z0(_15_bit_div_11_bit_triple_block_version_b_05_feb_2022_4_z0),
    .Z1(_15_bit_div_11_bit_triple_block_version_b_05_feb_2022_4_z1),
    .Z2(_15_bit_div_11_bit_triple_block_version_b_05_feb_2022_4_z2),
    .Z3(_15_bit_div_11_bit_triple_block_version_b_05_feb_2022_4_z3),
    .Z4(_15_bit_div_11_bit_triple_block_version_b_05_feb_2022_4_z4),
    .Z5(_15_bit_div_11_bit_triple_block_version_b_05_feb_2022_4_z5),
    .Z6(_15_bit_div_11_bit_triple_block_version_b_05_feb_2022_4_z6),
    .Z7(_15_bit_div_11_bit_triple_block_version_b_05_feb_2022_4_z7),
    .Z8(_15_bit_div_11_bit_triple_block_version_b_05_feb_2022_4_z8),
    .Z9(_15_bit_div_11_bit_triple_block_version_b_05_feb_2022_4_z9),
    .Z10(_15_bit_div_11_bit_triple_block_version_b_05_feb_2022_4_z10),
    .Z11(_15_bit_div_11_bit_triple_block_version_b_05_feb_2022_4_z11),
    .Z12(_15_bit_div_11_bit_triple_block_version_b_05_feb_2022_4_z12),
    .Z13(_15_bit_div_11_bit_triple_block_version_b_05_feb_2022_4_z13),
    .Z14(_15_bit_div_11_bit_triple_block_version_b_05_feb_2022_4_z14),
    .F(_15_bit_div_11_bit_triple_block_version_b_05_feb_2022_4_f),
    .Y0(_15_bit_div_11_bit_triple_block_version_b_05_feb_2022_4_y0),
    .Y1(_15_bit_div_11_bit_triple_block_version_b_05_feb_2022_4_y1),
    .Y2(_15_bit_div_11_bit_triple_block_version_b_05_feb_2022_4_y2),
    .Y3(_15_bit_div_11_bit_triple_block_version_b_05_feb_2022_4_y3),
    .Y4(_15_bit_div_11_bit_triple_block_version_b_05_feb_2022_4_y4),
    .Y5(_15_bit_div_11_bit_triple_block_version_b_05_feb_2022_4_y5),
    .Y6(_15_bit_div_11_bit_triple_block_version_b_05_feb_2022_4_y6),
    .Y7(_15_bit_div_11_bit_triple_block_version_b_05_feb_2022_4_y7),
    .Y8(_15_bit_div_11_bit_triple_block_version_b_05_feb_2022_4_y8),
    .Y9(_15_bit_div_11_bit_triple_block_version_b_05_feb_2022_4_y9),
    .Y10(_15_bit_div_11_bit_triple_block_version_b_05_feb_2022_4_y10));
  LED led_67 (.in(undriven_6));
  LED led_68 (.in(undriven_5));
  _74182 _74182_1 (
    .pin1(_74182_1_pin1), .pin2(_74182_1_pin2), .pin3(_74182_1_pin3), .pin4(_74182_1_pin4), .pin5(1'b0),
    .pin6(1'b0), .pin7(_74182_1_pin7), .pin8(1'b0), .pin9(_74182_1_pin9), .pin10(_74182_1_pin10),
    .pin11(_74181_3_pin7), .pin12(_74181_2_pin7), .pin13(_74182_1_pin13), .pin14(_74182_1_pin14),
    .pin15(_74182_1_pin15), .pin16(1'b1));
  LED led_69 (.in(_74182_1_pin7));
  LED led_70 (.in(_15_bit_div_11_bit_triple_block_version_b_05_feb_2022_4_y10));
  LED led_71 (.in(_15_bit_div_11_bit_triple_block_version_b_05_feb_2022_4_f));
  LED led_72 (.in(_74182_1_pin10));
  LED led_73 (.in(_74182_1_pin9));
  LED led_74 (.in(_15_bit_div_11_bit_triple_block_version_b_05_feb_2022_4_y8));
  LED led_75 (.in(_15_bit_div_11_bit_triple_block_version_b_05_feb_2022_4_y9));
  PullUp pullup_2 (.out(_74182_1_pin13));
  LED led_76 (.in(_15_bit_div_11_bit_triple_block_version_b_05_feb_2022_4_y6));
  LED led_77 (.in(_15_bit_div_11_bit_triple_block_version_b_05_feb_2022_4_y7));
  LED led_78 (.in(R9));
  LED led_79 (.in(R10));
  LED led_80 (.in(_15_bit_div_11_bit_triple_block_version_b_05_feb_2022_4_y4));
  LED led_81 (.in(_15_bit_div_11_bit_triple_block_version_b_05_feb_2022_4_y5));
  LED led_82 (.in(R7));
  LED led_83 (.in(R8));
  LED led_84 (.in(_15_bit_div_11_bit_triple_block_version_b_05_feb_2022_4_y2));
  LED led_85 (.in(_15_bit_div_11_bit_triple_block_version_b_05_feb_2022_4_y3));
  LED led_86 (.in(R5));
  LED led_87 (.in(R6));
  LED led_88 (.in(_15_bit_div_11_bit_triple_block_version_b_05_feb_2022_4_y0));
  LED led_89 (.in(_15_bit_div_11_bit_triple_block_version_b_05_feb_2022_4_y1));
  LED led_90 (.in(R3));
  LED led_91 (.in(R4));
  LED led_92 (.in(R1));
  LED led_93 (.in(R2));
  LED led_94 (.in(R0));
  Seven_Seg_Hex seven_seg_hex_8 (.d({1'b0, R10, R9, R8}), .dp(1'b0));
  _15_bit_div_11_bit_triple_block_version_B_05_feb_2022 _15_bit_div_11_bit_triple_block_version_b_05_feb_2022_5 (
    .D0(D0), .D1(D1), .D2(D2), .D3(D3), .D4(D4), .D5(D5), .D6(D6), .D7(D7), .D8(D8), .D9(D9), .D10(D10),
    .N0(_15_bit_div_11_bit_triple_block_version_b_05_feb_2022_4_z0),
    .N1(_15_bit_div_11_bit_triple_block_version_b_05_feb_2022_4_z1),
    .N2(_15_bit_div_11_bit_triple_block_version_b_05_feb_2022_4_z2),
    .N3(_15_bit_div_11_bit_triple_block_version_b_05_feb_2022_4_z3),
    .N4(_15_bit_div_11_bit_triple_block_version_b_05_feb_2022_4_z4),
    .N5(_15_bit_div_11_bit_triple_block_version_b_05_feb_2022_4_z5),
    .N6(_15_bit_div_11_bit_triple_block_version_b_05_feb_2022_4_z6),
    .N7(_15_bit_div_11_bit_triple_block_version_b_05_feb_2022_4_z7),
    .N8(_15_bit_div_11_bit_triple_block_version_b_05_feb_2022_4_z8),
    .N9(_15_bit_div_11_bit_triple_block_version_b_05_feb_2022_4_z9),
    .N10(_15_bit_div_11_bit_triple_block_version_b_05_feb_2022_4_z10),
    .N11(_15_bit_div_11_bit_triple_block_version_b_05_feb_2022_4_z11),
    .N12(_15_bit_div_11_bit_triple_block_version_b_05_feb_2022_4_z12),
    .N13(_15_bit_div_11_bit_triple_block_version_b_05_feb_2022_4_z13),
    .N14(_15_bit_div_11_bit_triple_block_version_b_05_feb_2022_4_z14),
    .S(_15_bit_div_11_bit_triple_block_version_b_05_feb_2022_4_f),
    .A0(_15_bit_div_11_bit_triple_block_version_b_05_feb_2022_4_y0),
    .A1(_15_bit_div_11_bit_triple_block_version_b_05_feb_2022_4_y1),
    .A2(_15_bit_div_11_bit_triple_block_version_b_05_feb_2022_4_y2),
    .A3(_15_bit_div_11_bit_triple_block_version_b_05_feb_2022_4_y3),
    .A4(_15_bit_div_11_bit_triple_block_version_b_05_feb_2022_4_y4),
    .A5(_15_bit_div_11_bit_triple_block_version_b_05_feb_2022_4_y5),
    .A6(_15_bit_div_11_bit_triple_block_version_b_05_feb_2022_4_y6),
    .A7(_15_bit_div_11_bit_triple_block_version_b_05_feb_2022_4_y7),
    .A8(_15_bit_div_11_bit_triple_block_version_b_05_feb_2022_4_y8),
    .A9(_15_bit_div_11_bit_triple_block_version_b_05_feb_2022_4_y9),
    .A10(_15_bit_div_11_bit_triple_block_version_b_05_feb_2022_4_y10), .Z1(Q1), .Z2(Q2), .Z3(Q3), .Z4(Q4),
    .Z5(Q5), .Z6(Q6), .Z7(Q7), .Z8(Q8), .Z9(Q9), .Z10(Q10), .Z11(Q11), .Z12(Q12), .Z13(Q13), .Z14(Q14),
    .F(_74181_1_pin3), .Y0(_74181_1_pin2), .Y1(_15_bit_div_11_bit_triple_block_version_b_05_feb_2022_5_y1),
    .Y2(_15_bit_div_11_bit_triple_block_version_b_05_feb_2022_5_y2),
    .Y3(_15_bit_div_11_bit_triple_block_version_b_05_feb_2022_5_y3), .Y4(_74181_2_pin2),
    .Y5(_15_bit_div_11_bit_triple_block_version_b_05_feb_2022_5_y5),
    .Y6(_15_bit_div_11_bit_triple_block_version_b_05_feb_2022_5_y6),
    .Y7(_15_bit_div_11_bit_triple_block_version_b_05_feb_2022_5_y7), .Y8(_74181_3_pin2),
    .Y9(_15_bit_div_11_bit_triple_block_version_b_05_feb_2022_5_y9),
    .Y10(_15_bit_div_11_bit_triple_block_version_b_05_feb_2022_5_y10));  // open: Z0
  Seven_Seg_Hex seven_seg_hex_9 (.d({R7, R6, R5, R4}), .dp(1'b0));
  Seven_Seg_Hex seven_seg_hex_10 (.d({R3, R2, R1, R0}), .dp(1'b0));
  LED led_95 (.in(_15_bit_div_11_bit_triple_block_version_b_05_feb_2022_5_y10));
  LED led_96 (.in(_74181_1_pin3));
  LED led_97 (.in(_74181_3_pin2));
  LED led_98 (.in(_15_bit_div_11_bit_triple_block_version_b_05_feb_2022_5_y9));
  LED led_99 (.in(_15_bit_div_11_bit_triple_block_version_b_05_feb_2022_5_y6));
  LED led_100 (.in(_15_bit_div_11_bit_triple_block_version_b_05_feb_2022_5_y7));
  LED led_101 (.in(_74181_2_pin2));
  LED led_102 (.in(_15_bit_div_11_bit_triple_block_version_b_05_feb_2022_5_y5));
  LED led_103 (.in(_15_bit_div_11_bit_triple_block_version_b_05_feb_2022_5_y2));
  LED led_104 (.in(_15_bit_div_11_bit_triple_block_version_b_05_feb_2022_5_y3));
  LED led_105 (.in(_74181_1_pin2));
  LED led_106 (.in(_15_bit_div_11_bit_triple_block_version_b_05_feb_2022_5_y1));
  LED led_107 (.in(Q14));
  LED led_108 (.in(Q12));
  LED led_109 (.in(Q13));
  LED led_110 (.in(Q10));
  LED led_111 (.in(Q11));
  LED led_112 (.in(Q8));
  LED led_113 (.in(Q9));
  LED led_114 (.in(Q6));
  LED led_115 (.in(Q7));
  LED led_116 (.in(Q4));
  LED led_117 (.in(Q5));
  LED led_118 (.in(Q2));
  LED led_119 (.in(Q3));
  LED led_120 (.in(Q0));
  LED led_121 (.in(Q1));
  Seven_Seg_Hex seven_seg_hex_11 (.d({1'b0, Q14, Q13, Q12}), .dp(1'b0));
  Seven_Seg_Hex seven_seg_hex_12 (.d({Q11, Q10, Q9, Q8}), .dp(1'b0));
  Seven_Seg_Hex seven_seg_hex_13 (.d({Q7, Q6, Q5, Q4}), .dp(1'b0));
  Seven_Seg_Hex seven_seg_hex_14 (.d({Q3, Q2, Q1, Q0}), .dp(1'b0));

  // Notes on the sheet:
  //   N14: default 1
  //   D10: default 1
  //   DIVIDEND N (#15 Q)
  //   DIVIDER (M)
  //   15 bit div 11 bit blocked version E 05 feb 2022.dig
  //   #12 A
  //   #9 A
  //   #6 A
  //   #3 A
  //   REMAINDER
  //   #0 A
  //   QUOTIENT (#0 Q)
endmodule
