// Digital circuit 15 bit div 11 bit triple block version B 05 feb 2022.dig as structural Verilog
// 15 bit div 11 bit triple block version B 05 feb 2022
module _15_bit_div_11_bit_triple_block_version_B_05_feb_2022 (
  input  N0,
  input  N1,
  input  N2,
  input  N3,
  input  N4,
  input  N5,
  input  N6,
  input  N7,
  input  N8,
  input  N9,
  input  N10,
  input  N11,
  input  N12,
  input  N13,
  input  N14,
  input  D0,
  input  D1,
  input  D2,
  input  D3,
  input  D4,
  input  D5,
  input  D6,
  input  D7,
  input  D8,
  input  D9,
  input  D10,
  input  S,
  input  A0,
  input  A1,
  input  A2,
  input  A3,
  input  A4,
  input  A5,
  input  A6,
  input  A7,
  input  A8,
  input  A9,
  input  A10,
  output F,
  output Y0,
  output Y1,
  output Y2,
  output Y3,
  output Y4,
  output Y5,
  output Y6,
  output Y7,
  output Y8,
  output Y9,
  output Y10,
  output Z0,
  output Z1,
  output Z2,
  output Z3,
  output Z4,
  output Z5,
  output Z6,
  output Z7,
  output Z8,
  output Z9,
  output Z10,
  output Z11,
  output Z12,
  output Z13,
  output Z14
);

  wire _7404_1_pin9, _74181_1_pin4, _74181_1_pin9, _74181_1_pin10, _74181_1_pin11, _74181_2_pin7,
       _74181_2_pin9, _74181_2_pin10, _74181_2_pin11, _74181_3_pin7, _74181_3_pin9, _74181_3_pin10,
       _74181_3_pin11, _74181_4_pin3, _74181_4_pin9, _74181_4_pin10, _74181_4_pin11, _74181_5_pin2,
       _74181_5_pin7, _74181_5_pin9, _74181_5_pin10, _74181_5_pin11, _74181_6_pin2, _74181_6_pin7,
       _74181_6_pin9, _74181_6_pin10, _74181_6_pin11, _74181_8_pin2, _74181_8_pin7, _74181_9_pin2,
       _74181_9_pin7, _74182_1_pin1, _74182_1_pin2, _74182_1_pin3, _74182_1_pin4, _74182_1_pin7,
       _74182_1_pin9, _74182_1_pin10, _74182_1_pin14, _74182_1_pin15, _74182_2_pin1, _74182_2_pin2,
       _74182_2_pin3, _74182_2_pin4, _74182_2_pin7, _74182_2_pin9, _74182_2_pin10, _74182_2_pin14,
       _74182_2_pin15, _74182_3_pin1, _74182_3_pin2, _74182_3_pin3, _74182_3_pin4, _74182_3_pin7,
       _74182_3_pin9, _74182_3_pin10, _74182_3_pin14, _74182_3_pin15, _74367_1_y1, _74367_1_y2, _74367_1_y3,
       _74367_1_y4, _74367_1_y5, _74367_1_y6, _74367_2_y1, _74367_2_y2, _74367_2_y3, _74367_2_y4,
       _74367_2_y5, _74367_2_y6, _74367_3_y1, _74367_3_y2, _74367_3_y3, _74367_3_y4, _74367_3_y5,
       _74367_3_y6, _74367_4_y1, _74367_4_y2, _74367_4_y3, _74367_4_y4, _74367_4_y5, _74367_4_y6,
       _74367_5_y1, _74367_5_y2, _74367_5_y3, _74367_5_y4, _74367_5_y5, _74367_5_y6, _74367_6_y1,
       _74367_6_y2, _74367_6_y3, _74367_6_y4, _74367_6_y5, _74367_6_y6, undriven, undriven_2, undriven_3,
       undriven_4, undriven_5, undriven_6, undriven_7, undriven_8, undriven_9, undriven_10, undriven_11,
       undriven_12, undriven_13, undriven_14, undriven_15, undriven_16, undriven_17, undriven_18;

  _74181 _74181_1 (
    .pin1(D0), .pin2(N14), .pin3(S), .pin4(_74181_1_pin4), .pin5(_74181_1_pin4), .pin6(S), .pin7(S),
    .pin8(1'b0), .pin9(_74181_1_pin9), .pin10(_74181_1_pin10), .pin11(_74181_1_pin11), .pin12(1'b0));  // open: pin13, pin14, pin15, pin16, pin17, pin18, pin19, pin20, pin21, pin22, pin23, pin24
  LED led_1 (.in(undriven));
  LED led_2 (.in(undriven_2));
  _74181 _74181_2 (
    .pin1(D4), .pin2(A3), .pin3(S), .pin4(_74181_1_pin4), .pin5(_74181_1_pin4), .pin6(S),
    .pin7(_74181_2_pin7), .pin8(1'b0), .pin9(_74181_2_pin9), .pin10(_74181_2_pin10), .pin11(_74181_2_pin11),
    .pin12(1'b0));  // open: pin13, pin14, pin15, pin16, pin17, pin18, pin19, pin20, pin21, pin22, pin23, pin24
  LED led_3 (.in(undriven_3));
  LED led_4 (.in(undriven_4));
  _74181 _74181_3 (
    .pin1(D8), .pin2(A7), .pin3(S), .pin4(_74181_1_pin4), .pin5(_74181_1_pin4), .pin6(S),
    .pin7(_74181_3_pin7), .pin8(1'b0), .pin9(_74181_3_pin9), .pin10(_74181_3_pin10), .pin11(_74181_3_pin11),
    .pin12(1'b0));  // open: pin13, pin14, pin15, pin16, pin17, pin18, pin19, pin20, pin21, pin22, pin23, pin24
  LED led_5 (.in(undriven_5));
  LED led_6 (.in(undriven_6));
  _74182 _74182_1 (
    .pin1(_74182_1_pin1), .pin2(_74182_1_pin2), .pin3(_74182_1_pin3), .pin4(_74182_1_pin4), .pin5(1'b0),
    .pin6(1'b0), .pin7(_74182_1_pin7), .pin8(1'b0), .pin9(_74182_1_pin9), .pin10(_74182_1_pin10),
    .pin11(_74181_3_pin7), .pin12(_74181_2_pin7), .pin13(S), .pin14(_74182_1_pin14), .pin15(_74182_1_pin15),
    .pin16(1'b1));
  LED led_7 (.in(_74182_1_pin7));
  _74367 _74367_1 (
    .nG1(1'b0), .nG2(1'b0), .A1(_74181_4_pin3), .Y1(_74367_1_y1), .A2(_74181_3_pin11), .Y2(_74367_1_y2),
    .A3(_74181_3_pin10), .Y3(_74367_1_y3), .A4(_74181_3_pin9), .Y4(_74367_1_y4), .A5(_74181_6_pin2),
    .Y5(_74367_1_y5), .A6(_74181_2_pin11), .Y6(_74367_1_y6), .VCC(1'b1), .GND(1'b0));
  LED led_8 (.in(_74182_1_pin10));
  LED led_9 (.in(_74182_1_pin9));
  LED u_A10 (.in(_74367_1_y2));
  LED A11 (.in(_74367_1_y1));
  LED u_A8 (.in(_74367_1_y4));
  LED u_A9 (.in(_74367_1_y3));
  LED u_A6 (.in(_74367_1_y6));
  LED u_A7 (.in(_74367_1_y5));
  LED u_A4 (.in(_74367_2_y2));
  LED u_A5 (.in(_74367_2_y1));
  _74367 _74367_2 (
    .nG1(1'b0), .nG2(1'b0), .A1(_74181_2_pin10), .Y1(_74367_2_y1), .A2(_74181_2_pin9), .Y2(_74367_2_y2),
    .A3(_74181_5_pin2), .Y3(_74367_2_y3), .A4(_74181_1_pin11), .Y4(_74367_2_y4), .A5(_74181_1_pin10),
    .Y5(_74367_2_y5), .A6(_74181_1_pin9), .Y6(_74367_2_y6), .VCC(1'b1), .GND(1'b0));
  LED u_A2 (.in(_74367_2_y4));
  LED u_A3 (.in(_74367_2_y3));
  LED u_A0 (.in(_74367_2_y6));
  LED u_A1 (.in(_74367_2_y5));
  _74181 _74181_4 (
    .pin1(D0), .pin2(N13), .pin3(_74181_4_pin3), .pin4(Z2), .pin5(Z2), .pin6(_74181_4_pin3),
    .pin7(_74181_4_pin3), .pin8(1'b0), .pin9(_74181_4_pin9), .pin10(_74181_4_pin10), .pin11(_74181_4_pin11),
    .pin12(1'b0));  // open: pin13, pin14, pin15, pin16, pin17, pin18, pin19, pin20, pin21, pin22, pin23, pin24
  LED led_10 (.in(undriven_7));
  LED led_11 (.in(undriven_8));
  _74181 _74181_5 (
    .pin1(D4), .pin2(_74181_5_pin2), .pin3(_74181_4_pin3), .pin4(Z2), .pin5(Z2), .pin6(_74181_4_pin3),
    .pin7(_74181_5_pin7), .pin8(1'b0), .pin9(_74181_5_pin9), .pin10(_74181_5_pin10), .pin11(_74181_5_pin11),
    .pin12(1'b0));  // open: pin13, pin14, pin15, pin16, pin17, pin18, pin19, pin20, pin21, pin22, pin23, pin24
  LED led_12 (.in(undriven_9));
  LED led_13 (.in(undriven_10));
  _74181 _74181_6 (
    .pin1(D8), .pin2(_74181_6_pin2), .pin3(_74181_4_pin3), .pin4(Z2), .pin5(Z2), .pin6(_74181_4_pin3),
    .pin7(_74181_6_pin7), .pin8(1'b0), .pin9(_74181_6_pin9), .pin10(_74181_6_pin10), .pin11(_74181_6_pin11),
    .pin12(1'b0));  // open: pin13, pin14, pin15, pin16, pin17, pin18, pin19, pin20, pin21, pin22, pin23, pin24
  LED led_14 (.in(undriven_11));
  LED led_15 (.in(undriven_12));
  _74182 _74182_2 (
    .pin1(_74182_2_pin1), .pin2(_74182_2_pin2), .pin3(_74182_2_pin3), .pin4(_74182_2_pin4), .pin5(1'b0),
    .pin6(1'b0), .pin7(_74182_2_pin7), .pin8(1'b0), .pin9(_74182_2_pin9), .pin10(_74182_2_pin10),
    .pin11(_74181_6_pin7), .pin12(_74181_5_pin7), .pin13(_74181_4_pin3), .pin14(_74182_2_pin14),
    .pin15(_74182_2_pin15), .pin16(1'b1));
  LED led_16 (.in(_74182_2_pin7));
  _74367 _74367_3 (
    .nG1(1'b0), .nG2(1'b0), .A1(_7404_1_pin9), .Y1(_74367_3_y1), .A2(_74181_6_pin11), .Y2(_74367_3_y2),
    .A3(_74181_6_pin10), .Y3(_74367_3_y3), .A4(_74181_6_pin9), .Y4(_74367_3_y4), .A5(_74181_9_pin2),
    .Y5(_74367_3_y5), .A6(_74181_5_pin11), .Y6(_74367_3_y6), .VCC(1'b1), .GND(1'b0));
  LED led_17 (.in(_74182_2_pin10));
  LED led_18 (.in(_74182_2_pin9));
  LED B10 (.in(_74367_3_y2));
  LED B11 (.in(_74367_3_y1));
  _7404 _7404_1 (
    .pin1(S), .pin2(_74181_1_pin4), .pin3(1'b0), .pin5(_74181_4_pin3), .pin6(Z2), .pin7(1'b0), .pin8(Z1),
    .pin9(_7404_1_pin9), .pin11(1'b0), .pin12(Z0), .pin13(F), .pin14(1'b1));  // open: pin4, pin10
  LED B8 (.in(_74367_3_y4));
  LED B9 (.in(_74367_3_y3));
  LED B6 (.in(_74367_3_y6));
  LED B7 (.in(_74367_3_y5));
  LED B4 (.in(_74367_4_y2));
  LED B5 (.in(_74367_4_y1));
  _74367 _74367_4 (
    .nG1(1'b0), .nG2(1'b0), .A1(_74181_5_pin10), .Y1(_74367_4_y1), .A2(_74181_5_pin9), .Y2(_74367_4_y2),
    .A3(_74181_8_pin2), .Y3(_74367_4_y3), .A4(_74181_4_pin11), .Y4(_74367_4_y4), .A5(_74181_4_pin10),
    .Y5(_74367_4_y5), .A6(_74181_4_pin9), .Y6(_74367_4_y6), .VCC(1'b1), .GND(1'b0));
  LED B2 (.in(_74367_4_y4));
  LED B3 (.in(_74367_4_y3));
  LED B0 (.in(_74367_4_y6));
  LED B1 (.in(_74367_4_y5));
  _74181 _74181_7 (
    .pin1(D0), .pin2(N12), .pin3(_7404_1_pin9), .pin4(Z1), .pin5(Z1), .pin6(_7404_1_pin9),
    .pin7(_7404_1_pin9), .pin8(1'b0), .pin9(Y0), .pin10(Y1), .pin11(Y2), .pin12(1'b0));  // open: pin13, pin14, pin15, pin16, pin17, pin18, pin19, pin20, pin21, pin22, pin23, pin24
  LED led_19 (.in(undriven_13));
  LED led_20 (.in(undriven_14));
  _74181 _74181_8 (
    .pin1(D4), .pin2(_74181_8_pin2), .pin3(_7404_1_pin9), .pin4(Z1), .pin5(Z1), .pin6(_7404_1_pin9),
    .pin7(_74181_8_pin7), .pin8(1'b0), .pin9(Y4), .pin10(Y5), .pin11(Y6), .pin12(1'b0));  // open: pin13, pin14, pin15, pin16, pin17, pin18, pin19, pin20, pin21, pin22, pin23, pin24
  LED led_21 (.in(undriven_15));
  LED led_22 (.in(undriven_16));
  _74181 _74181_9 (
    .pin1(D8), .pin2(_74181_9_pin2), .pin3(_7404_1_pin9), .pin4(Z1), .pin5(Z1), .pin6(_7404_1_pin9),
    .pin7(_74181_9_pin7), .pin8(1'b0), .pin9(Y8), .pin10(Y9), .pin11(Y10), .pin12(1'b0));  // open: pin13, pin14, pin15, pin16, pin17, pin18, pin19, pin20, pin21, pin22, pin23, pin24
  LED led_23 (.in(undriven_17));
  LED led_24 (.in(undriven_18));
  _74182 _74182_3 (
    .pin1(_74182_3_pin1), .pin2(_74182_3_pin2), .pin3(_74182_3_pin3), .pin4(_74182_3_pin4), .pin5(1'b0),
    .pin6(1'b0), .pin7(_74182_3_pin7), .pin8(1'b0), .pin9(_74182_3_pin9), .pin10(_74182_3_pin10),
    .pin11(_74181_9_pin7), .pin12(_74181_8_pin7), .pin13(_7404_1_pin9), .pin14(_74182_3_pin14),
    .pin15(_74182_3_pin15), .pin16(1'b1));
  LED led_25 (.in(_74182_3_pin7));
  _74367 _74367_5 (
    .nG1(1'b0), .nG2(1'b0), .A1(F), .Y1(_74367_5_y1), .A2(Y10), .Y2(_74367_5_y2), .A3(Y9), .Y3(_74367_5_y3),
    .A4(Y8), .Y4(_74367_5_y4), .A5(Y7), .Y5(_74367_5_y5), .A6(Y6), .Y6(_74367_5_y6), .VCC(1'b1), .GND(1'b0));
  LED led_26 (.in(_74182_3_pin10));
  LED led_27 (.in(_74182_3_pin9));
  LED C10 (.in(_74367_5_y2));
  LED C11 (.in(_74367_5_y1));
  LED C8 (.in(_74367_5_y4));
  LED C9 (.in(_74367_5_y3));
  LED C6 (.in(_74367_5_y6));
  LED C7 (.in(_74367_5_y5));
  LED C4 (.in(_74367_6_y2));
  LED C5 (.in(_74367_6_y1));
  _74367 _74367_6 (
    .nG1(1'b0), .nG2(1'b0), .A1(Y5), .Y1(_74367_6_y1), .A2(Y4), .Y2(_74367_6_y2), .A3(Y3), .Y3(_74367_6_y3),
    .A4(Y2), .Y4(_74367_6_y4), .A5(Y1), .Y5(_74367_6_y5), .A6(Y0), .Y6(_74367_6_y6), .VCC(1'b1), .GND(1'b0));
  LED C2 (.in(_74367_6_y4));
  LED C3 (.in(_74367_6_y3));
  LED C0 (.in(_74367_6_y6));
  LED C1 (.in(_74367_6_y5));

  assign Z3 = N0;
  assign Z4 = N1;
  assign Z5 = N2;
  assign Z6 = N3;
  assign Z7 = N4;
  assign Z8 = N5;
  assign Z9 = N6;
  assign Z10 = N7;
  assign Z11 = N8;
  assign Z12 = N9;
  assign Z13 = N10;
  assign Z14 = N11;

  // Notes on the sheet:
  //   15 bit div 11 bit triple block version B 05 feb 2022.dig
  //   stage A
  //   stage B
  //   stage C
endmodule
