// Digital circuit 3 x 10 bit multiply version E 19 feb 2022.dig as structural Verilog
// 3 x 10 bit multiply version E 19 feb 2022
module _3_x_10_bit_multiply_version_E_19_feb_2022 (
  input  A0,
  input  A1,
  input  A2,
  input  B0,
  input  B1,
  input  B2,
  input  B3,
  input  B4,
  input  B5,
  input  B6,
  input  B7,
  input  B8,
  input  B9,
  output P0,
  output P1,
  output P2,
  output P3,
  output P4,
  output P5,
  output P6,
  output P7,
  output P8,
  output P9,
  output P10,
  output P11,
  output P12
);

  wire _0_3_pin1, _0_3_pin4, _0_3_pin9, _0_3_pin10, _0_3_pin11, _0_3_pin13, _0_4_pin9, _0_4_pin11,
       _0_4_pin15, _4_7_pin1, _4_7_pin2, _4_7_pin4, _4_7_pin6, _4_7_pin9, _4_7_pin10, _4_7_pin11, _4_7_pin13,
       _4_7_pin15, _4_8_pin2, _4_8_pin6, _4_8_pin9, _4_8_pin11, _4_8_pin15, _8_11_pin1, _8_11_pin2,
       _8_11_pin4, _8_11_pin6, _8_11_pin10, _8_11_pin13, _8_11_pin15, _8_12_pin2, _8_12_pin6, _8_12_pin11,
       _8_12_pin15, _7408_1_pin3, _7408_1_pin6, _7408_1_pin8, _7408_1_pin11, _7408_2_pin3, _7408_2_pin6,
       _7408_2_pin8, _7408_2_pin11, _7408_3_pin3, _7408_3_pin6, _7408_3_pin8, _7408_3_pin11;

  Seven_Seg_Hex seven_seg_hex_1 (.d({3'b000, P12}), .dp(1'b0));
  Seven_Seg_Hex seven_seg_hex_2 (.d({P11, P10, P9, P8}), .dp(1'b0));
  Seven_Seg_Hex seven_seg_hex_3 (.d({1'b0, A2, A1, A0}), .dp(1'b0));
  Seven_Seg_Hex seven_seg_hex_4 (.d({P7, P6, P5, P4}), .dp(1'b0));
  Seven_Seg_Hex seven_seg_hex_5 (.d({P3, P2, P1, P0}), .dp(1'b0));
  Seven_Seg_Hex seven_seg_hex_6 (.d({2'b00, B9, B8}), .dp(1'b0));
  Seven_Seg_Hex seven_seg_hex_7 (.d({B7, B6, B5, B4}), .dp(1'b0));
  Seven_Seg_Hex seven_seg_hex_8 (.d({B3, B2, B1, B0}), .dp(1'b0));
  _7408 _7408_1 (
    .pin1(A0), .pin2(B0), .pin3(_7408_1_pin3), .pin4(A0), .pin5(B1), .pin6(_7408_1_pin6), .pin7(1'b0),
    .pin8(_7408_1_pin8), .pin9(A0), .pin10(B2), .pin11(_7408_1_pin11), .pin12(A0), .pin13(B3), .pin14(1'b1));
  _7408 _7408_2 (
    .pin1(A0), .pin2(B4), .pin3(_7408_2_pin3), .pin4(A0), .pin5(B5), .pin6(_7408_2_pin6), .pin7(1'b0),
    .pin8(_7408_2_pin8), .pin9(A0), .pin10(B6), .pin11(_7408_2_pin11), .pin12(A0), .pin13(B7), .pin14(1'b1));
  _7408 _7408_3 (
    .pin1(A0), .pin2(B8), .pin3(_7408_3_pin3), .pin4(A0), .pin5(B9), .pin6(_7408_3_pin6), .pin7(1'b0),
    .pin8(_7408_3_pin8), .pin9(A1), .pin10(B0), .pin11(_7408_3_pin11), .pin12(A1), .pin13(B1), .pin14(1'b1));
  LED R1 (.in(_0_3_pin1));
  LED R0 (.in(_0_3_pin4));
  LED R5 (.in(_4_7_pin1));
  _74283 _0_3 (
    .pin1(_0_3_pin1), .pin2(_7408_3_pin8), .pin3(_7408_1_pin6), .pin4(_0_3_pin4), .pin5(_7408_1_pin3),
    .pin6(1'b0), .pin7(1'b0), .pin8(1'b0), .pin9(_0_3_pin9), .pin10(_0_3_pin10), .pin11(_0_3_pin11),
    .pin12(_7408_1_pin11), .pin13(_0_3_pin13), .pin14(_7408_1_pin8), .pin15(_7408_3_pin11), .pin16(1'b1));
  _74283 _4_7 (
    .pin1(_4_7_pin1), .pin2(_4_7_pin2), .pin3(_7408_2_pin6), .pin4(_4_7_pin4), .pin5(_7408_2_pin3),
    .pin6(_4_7_pin6), .pin7(_0_3_pin9), .pin8(1'b0), .pin9(_4_7_pin9), .pin10(_4_7_pin10),
    .pin11(_4_7_pin11), .pin12(_7408_2_pin11), .pin13(_4_7_pin13), .pin14(_7408_2_pin8), .pin15(_4_7_pin15),
    .pin16(1'b1));
  LED L1 (.in(_0_3_pin9));
  _74283 _8_11 (
    .pin1(_8_11_pin1), .pin2(_8_11_pin2), .pin3(_7408_3_pin6), .pin4(_8_11_pin4), .pin5(_7408_3_pin3),
    .pin6(_8_11_pin6), .pin7(_4_7_pin9), .pin8(1'b0), .pin10(_8_11_pin10), .pin11(1'b0), .pin12(1'b0),
    .pin13(_8_11_pin13), .pin14(1'b0), .pin15(_8_11_pin15), .pin16(1'b1));  // open: pin9
  LED L2 (.in(_4_7_pin9));
  _7408 _7408_4 (
    .pin1(A1), .pin2(B2), .pin3(_0_3_pin11), .pin4(A1), .pin5(B3), .pin6(_4_7_pin6), .pin7(1'b0),
    .pin8(_4_7_pin2), .pin9(A1), .pin10(B4), .pin11(_4_7_pin15), .pin12(A1), .pin13(B5), .pin14(1'b1));
  LED R2 (.in(_0_3_pin13));
  LED R4 (.in(_4_7_pin4));
  LED U12 (.in(P12));
  LED R3 (.in(_0_3_pin10));
  LED R6 (.in(_4_7_pin13));
  LED U10 (.in(P10));
  LED U11 (.in(P11));
  LED R11 (.in(_8_11_pin10));
  LED R8 (.in(_8_11_pin4));
  LED U8 (.in(P8));
  LED U9 (.in(P9));
  LED R9 (.in(_8_11_pin1));
  LED U6 (.in(P6));
  LED U7 (.in(P7));
  LED R10 (.in(_8_11_pin13));
  LED U4 (.in(P4));
  LED U5 (.in(P5));
  _7408 _7408_5 (
    .pin1(A1), .pin2(B6), .pin3(_4_7_pin11), .pin4(A1), .pin5(B7), .pin6(_8_11_pin6), .pin7(1'b0),
    .pin8(_8_11_pin2), .pin9(A1), .pin10(B8), .pin11(_8_11_pin15), .pin12(A1), .pin13(B9), .pin14(1'b1));
  LED U2 (.in(P2));
  LED U3 (.in(P3));
  LED R7 (.in(_4_7_pin10));
  LED U0 (.in(P0));
  LED U1 (.in(P1));
  LED S10 (.in(_8_12_pin15));
  LED S11 (.in(_8_12_pin11));
  LED S8 (.in(_8_12_pin6));
  LED S9 (.in(_8_12_pin2));
  LED S6 (.in(_4_8_pin15));
  LED S7 (.in(_4_8_pin11));
  LED S4 (.in(_4_8_pin6));
  LED S5 (.in(_4_8_pin2));
  _74283 _0_4 (
    .pin1(P1), .pin2(1'b0), .pin3(_0_3_pin1), .pin4(P0), .pin5(_0_3_pin4), .pin6(1'b0), .pin7(1'b0),
    .pin8(1'b0), .pin9(_0_4_pin9), .pin10(P3), .pin11(_0_4_pin11), .pin12(_0_3_pin10), .pin13(P2),
    .pin14(_0_3_pin13), .pin15(_0_4_pin15), .pin16(1'b1));
  _74283 _4_8 (
    .pin1(P5), .pin2(_4_8_pin2), .pin3(_4_7_pin1), .pin4(P4), .pin5(_4_7_pin4), .pin6(_4_8_pin6),
    .pin7(_0_4_pin9), .pin8(1'b0), .pin9(_4_8_pin9), .pin10(P7), .pin11(_4_8_pin11), .pin12(_4_7_pin10),
    .pin13(P6), .pin14(_4_7_pin13), .pin15(_4_8_pin15), .pin16(1'b1));
  LED S2 (.in(_0_4_pin15));
  LED S3 (.in(_0_4_pin11));
  _74283 _8_12 (
    .pin1(P9), .pin2(_8_12_pin2), .pin3(_8_11_pin1), .pin4(P8), .pin5(_8_11_pin4), .pin6(_8_12_pin6),
    .pin7(_4_8_pin9), .pin8(1'b0), .pin9(P12), .pin10(P11), .pin11(_8_12_pin11), .pin12(_8_11_pin10),
    .pin13(P10), .pin14(_8_11_pin13), .pin15(_8_12_pin15), .pin16(1'b1));
  LED S1 (.in(1'b0));
  LED S0 (.in(1'b0));
  LED L11 (.in(_0_4_pin9));
  LED L12 (.in(_4_8_pin9));
  LED L13 (.in(P12));
  _7408 _7408_6 (
    .pin1(A2), .pin2(B0), .pin3(_0_4_pin15), .pin4(A2), .pin5(B1), .pin6(_0_4_pin11), .pin7(1'b0),
    .pin8(_4_8_pin6), .pin9(A2), .pin10(B2), .pin11(_4_8_pin2), .pin12(A2), .pin13(B3), .pin14(1'b1));
  _7408 _7408_7 (
    .pin1(A2), .pin2(B4), .pin3(_4_8_pin15), .pin4(A2), .pin5(B5), .pin6(_4_8_pin11), .pin7(1'b0),
    .pin8(_8_12_pin6), .pin9(A2), .pin10(B6), .pin11(_8_12_pin2), .pin12(A2), .pin13(B7), .pin14(1'b1));
  _7408 _7408_8 (
    .pin1(A2), .pin2(B8), .pin3(_8_12_pin15), .pin4(A2), .pin5(B9), .pin6(_8_12_pin11), .pin7(1'b0),
    .pin9(1'b0), .pin10(B0), .pin12(1'b0), .pin13(B1), .pin14(1'b1));  // open: pin8, pin11

  // Notes on the sheet:
  //   A0: default 1
  //   A1: default 1
  //   B0: default 1
  //   B1: default 1
  //   B2: default 1
  //   B3: default 1
  //   B4: default 1
  //   B5: default 1
  //   B6: default 1
  //   B7: default 1
  //   B8: default 1
  //   B9: default 1
  //   3 x 10 bit multiply version E 19 feb 2022.dig
  //   LSB
  //   A x B
  //   A
  //   B
  //   A0 partial product
  //   R = PP0 + PP1
  //   PP0 + PP1 = R
  //   U = R + S
  //   A1 partial product
  //   S = PP2 + PP3
  //   R + S = U
  //   A2 partial product
endmodule
