// Digital circuit 6 bit div ten version I 06 feb 2022.dig as structural Verilog
// 6 bit div ten version I 06 feb 2022
module _6_bit_div_ten_version_I_06_feb_2022 (
  input  A0,
  input  A1,
  input  A2,
  input  A3,
  input  A4,
  input  A5,
  output Q0,
  output Q1,
  output Q2,
  output R0,
  output R1,
  output R2,
  output R3
);

  wire _7404_1_pin2, _7404_1_pin4, _7404_1_pin6, _7404_1_pin9, _7404_1_pin10, _7404_1_pin12, _7410_1_pin6,
       _7410_1_pin9, _7410_1_pin12, _7410_2_pin9, _7410_2_pin13, _7411_1_pin6, _7411_1_pin12, _7420_1_pin6,
       _7420_1_pin8, _7420_2_pin6, _7420_2_pin8, _7420_3_pin6, _7420_3_pin8, _7420_4_pin6, _7420_4_pin8,
       _7427_1_pin5, _7427_1_pin11, _7432_1_pin3, _7432_1_pin6, _74260_1_pin5, _74260_1_pin6, _74283_1_pin2,
       _74283_1_pin11, _74283_1_pin15, _74367_1_y1, _74367_1_y2, _74367_1_y3, _74367_1_y4, _74367_1_y5,
       _74367_1_y6, pullup_1_out;

  Seven_Seg_Hex seven_seg_hex_1 (.d({2'b00, A5, A4}), .dp(1'b0));
  Seven_Seg_Hex seven_seg_hex_2 (.d({1'b0, Q2, Q1, Q0}), .dp(1'b0));
  Seven_Seg_Hex seven_seg_hex_3 (.d({A3, A2, A1, A0}), .dp(1'b0));
  Seven_Seg_Hex seven_seg_hex_4 (.d({R3, R2, R1, R0}), .dp(1'b0));
  PullUp pullup_1 (.out(pullup_1_out));
  _74283 _74283_1 (
    .pin1(R1), .pin2(_74283_1_pin2), .pin3(A1), .pin4(R0), .pin5(A0), .pin6(pullup_1_out),
    .pin7(pullup_1_out), .pin8(1'b0), .pin10(R3), .pin11(_74283_1_pin11), .pin12(A3), .pin13(R2), .pin14(A2),
    .pin15(_74283_1_pin15), .pin16(1'b1));  // open: pin9
  _7404 _7404_1 (
    .pin1(A1), .pin2(_7404_1_pin2), .pin3(A2), .pin4(_7404_1_pin4), .pin5(A3), .pin6(_7404_1_pin6),
    .pin7(1'b0), .pin8(Q2), .pin9(_7404_1_pin9), .pin10(_7404_1_pin10), .pin11(A5), .pin12(_7404_1_pin12),
    .pin13(A4), .pin14(1'b1));
  _7420 _7420_1 (
    .pin1(A1), .pin2(A3), .pin4(_7404_1_pin12), .pin5(_7404_1_pin10), .pin6(_7420_1_pin6), .pin7(1'b0),
    .pin8(_7420_1_pin8), .pin9(A4), .pin10(_7404_1_pin10), .pin12(_7404_1_pin6), .pin13(_7404_1_pin4),
    .pin14(1'b1));  // open: pin3, pin11
  _7420 _7420_2 (
    .pin1(A2), .pin2(A3), .pin4(_7404_1_pin12), .pin5(_7404_1_pin10), .pin6(_7420_2_pin6), .pin7(1'b0),
    .pin8(_7420_2_pin8), .pin9(_7404_1_pin10), .pin10(A4), .pin12(A3), .pin13(_7404_1_pin2), .pin14(1'b1));  // open: pin3, pin11
  _7420 _7420_3 (
    .pin1(_7404_1_pin4), .pin2(A3), .pin4(A4), .pin5(_7404_1_pin10), .pin6(_7420_3_pin6), .pin7(1'b0),
    .pin8(_7420_3_pin8), .pin9(_7404_1_pin10), .pin10(A4), .pin12(_7404_1_pin6), .pin13(A2), .pin14(1'b1));  // open: pin3, pin11
  _7410 _7410_1 (
    .pin1(_7420_1_pin8), .pin2(_7420_1_pin6), .pin3(_7420_2_pin8), .pin4(_7420_3_pin6), .pin5(_7420_3_pin8),
    .pin6(_7410_1_pin6), .pin7(1'b0), .pin8(Q0), .pin9(_7410_1_pin9), .pin10(_7410_1_pin9),
    .pin11(_7410_1_pin9), .pin12(_7410_1_pin12), .pin13(_7420_2_pin6), .pin14(1'b1));
  _74260 _74260_1 (
    .pin1(_7404_1_pin2), .pin2(_7404_1_pin4), .pin3(_7404_1_pin6), .pin4(A1), .pin5(_74260_1_pin5),
    .pin6(_74260_1_pin6), .pin7(1'b0), .pin8(_7404_1_pin10), .pin9(_7404_1_pin12), .pin10(A3), .pin11(A2),
    .pin12(A5), .pin13(_7404_1_pin12), .pin14(1'b1));
  LED _10__lt__eq__A__lt__20 (.in(_74367_1_y1));
  LED _20__lt__eq__A__lt__30 (.in(_74367_1_y2));
  LED _30__lt__eq__A__lt__40 (.in(_74367_1_y3));
  _74367 _74367_1 (
    .nG1(1'b0), .nG2(1'b0), .A1(_7410_1_pin12), .Y1(_74367_1_y1), .A2(_7410_1_pin6), .Y2(_74367_1_y2),
    .A3(_7432_1_pin3), .Y3(_74367_1_y3), .A4(_7427_1_pin5), .Y4(_74367_1_y4), .A5(_7427_1_pin11),
    .Y5(_74367_1_y5), .A6(_7432_1_pin6), .Y6(_74367_1_y6), .VCC(1'b1), .GND(1'b0));
  LED _40__lt__eq__A__lt__50 (.in(_74367_1_y6));
  LED _50__lt__eq__A__lt__60 (.in(_74367_1_y5));
  LED _60__lt__eq__A (.in(_74367_1_y4));
  _7411 _7411_1 (
    .pin1(_7404_1_pin6), .pin2(_7404_1_pin12), .pin3(A3), .pin4(_7404_1_pin12), .pin5(A5),
    .pin6(_7411_1_pin6), .pin7(1'b0), .pin9(1'b0), .pin10(1'b0), .pin11(1'b0), .pin12(_7411_1_pin12),
    .pin13(A5), .pin14(1'b1));  // open: pin8
  _7432 _7432_1 (
    .pin1(_74260_1_pin5), .pin2(_7411_1_pin12), .pin3(_7432_1_pin3), .pin4(_74260_1_pin6),
    .pin5(_7411_1_pin6), .pin6(_7432_1_pin6), .pin7(1'b0), .pin9(1'b0), .pin10(1'b0), .pin12(1'b0),
    .pin13(1'b0), .pin14(1'b1));  // open: pin8, pin11
  _7427 _7427_1 (
    .pin1(_7410_1_pin12), .pin2(_7432_1_pin3), .pin3(_7410_1_pin6), .pin4(_7432_1_pin3), .pin5(_7427_1_pin5),
    .pin6(_74283_1_pin15), .pin7(1'b0), .pin8(_7404_1_pin9), .pin9(_7432_1_pin6), .pin10(_7427_1_pin5),
    .pin11(_7427_1_pin11), .pin12(_7410_1_pin9), .pin13(_7427_1_pin11), .pin14(1'b1));
  _7420 _7420_4 (
    .pin1(A1), .pin2(_7404_1_pin6), .pin4(A4), .pin5(A5), .pin6(_7420_4_pin6), .pin7(1'b0),
    .pin8(_7420_4_pin8), .pin9(A5), .pin10(A4), .pin12(A3), .pin13(_7404_1_pin4), .pin14(1'b1));  // open: pin3, pin11
  _7410 _7410_2 (
    .pin1(_7420_4_pin8), .pin2(_7420_4_pin6), .pin3(_74283_1_pin15), .pin4(_74283_1_pin15),
    .pin5(_74283_1_pin15), .pin6(Q1), .pin7(1'b0), .pin8(_7427_1_pin5), .pin9(_7410_2_pin9),
    .pin10(_7410_2_pin9), .pin11(_7410_2_pin9), .pin12(_7427_1_pin11), .pin13(_7410_2_pin13), .pin14(1'b1));
  _7420 _7420_5 (
    .pin1(A2), .pin2(_7404_1_pin6), .pin4(A4), .pin5(A5), .pin6(_7410_2_pin13), .pin7(1'b0),
    .pin8(_7410_2_pin9), .pin9(A5), .pin10(A4), .pin12(A3), .pin13(A2), .pin14(1'b1));  // open: pin3, pin11
  _7425 _7425_1 (
    .pin1(_7432_1_pin6), .pin2(_7427_1_pin5), .pin4(_7410_1_pin12), .pin5(_7432_1_pin3),
    .pin6(_74283_1_pin11), .pin7(1'b0), .pin8(_74283_1_pin2), .pin9(_7410_1_pin12), .pin10(_7432_1_pin3),
    .pin12(_7427_1_pin11), .pin13(_7427_1_pin11), .pin14(1'b1));  // open: pin3, pin11

  // Notes on the sheet:
  //   A0: default 1
  //   A4: default 1
  //   A5: default 1
  //   A
  //   Q
  //   R
  //   6 bit div ten version I 06 feb 2022.dig
endmodule
