// Digital circuit 6 x 10 bit multiply version K 19 feb 2022.dig as structural Verilog
// 6 x 10 bit multiply version K 19 feb 2022
module _6_x_10_bit_multiply_version_K_19_feb_2022 (
  input  A0,
  input  A1,
  input  A2,
  input  A3,
  input  A4,
  input  A5,
  input  B0,
  input  B1,
  input  B2,
  input  B3,
  input  B4,
  input  B5,
  input  B6,
  input  B7,
  input  B8,
  input  B9,
  output P0,
  output P1,
  output P2,
  output P3,
  output P4,
  output P5,
  output P6,
  output P7,
  output P8,
  output P9,
  output P10,
  output P11,
  output P12,
  output P13,
  output P14,
  output P15
);

  wire _0_3_2_pin9, _0_3_2_pin11, _0_3_2_pin15, _0_3_3_pin9, _0_3_3_pin11, _0_3_pin1, _0_3_pin4, _0_3_pin9,
       _0_3_pin10, _0_3_pin11, _0_3_pin13, _4_7_2_pin1, _4_7_2_pin2, _4_7_2_pin4, _4_7_2_pin6, _4_7_2_pin9,
       _4_7_2_pin10, _4_7_2_pin11, _4_7_2_pin13, _4_7_2_pin15, _4_7_3_pin2, _4_7_3_pin9, _4_7_3_pin11,
       _4_7_3_pin15, _4_7_4_pin1, _4_7_4_pin4, _4_7_4_pin9, _4_7_4_pin10, _4_7_4_pin11, _4_7_4_pin13,
       _4_7_5_pin9, _4_7_pin1, _4_7_pin2, _4_7_pin4, _4_7_pin6, _4_7_pin9, _4_7_pin10, _4_7_pin11,
       _4_7_pin13, _4_7_pin15, _8_11_2_pin1, _8_11_2_pin2, _8_11_2_pin4, _8_11_2_pin6, _8_11_2_pin9,
       _8_11_2_pin10, _8_11_2_pin11, _8_11_2_pin13, _8_11_2_pin15, _8_11_3_pin2, _8_11_3_pin6, _8_11_3_pin9,
       _8_11_3_pin11, _8_11_3_pin15, _8_11_4_pin1, _8_11_4_pin2, _8_11_4_pin4, _8_11_4_pin6, _8_11_4_pin9,
       _8_11_4_pin10, _8_11_4_pin11, _8_11_4_pin13, _8_11_4_pin15, _8_11_5_pin9, _8_11_pin1, _8_11_pin2,
       _8_11_pin4, _8_11_pin6, _8_11_pin10, _8_11_pin13, _8_11_pin15, _12_15_2_pin6, _12_15_3_pin1,
       _12_15_3_pin2, _12_15_3_pin4, _12_15_3_pin6, _12_15_3_pin10, _12_15_3_pin13, _12_15_3_pin15,
       _12_15_pin1, _12_15_pin2, _12_15_pin4, _12_15_pin6, _7408_1_pin3, _7408_1_pin6, _7408_1_pin8,
       _7408_1_pin11, _7408_2_pin3, _7408_2_pin6, _7408_2_pin8, _7408_2_pin11, _7408_3_pin3, _7408_3_pin6,
       _7408_3_pin8, _7408_3_pin11, _7408_6_pin3, _7408_6_pin6, _7408_6_pin8, _7408_6_pin11, _7408_7_pin3,
       _7408_7_pin6, _7408_7_pin8, _7408_7_pin11, _7408_8_pin3, _7408_8_pin6, _7408_8_pin11, _7408_11_pin3,
       _7408_11_pin6, _7408_11_pin8, _7408_11_pin11, _7408_12_pin3, _7408_12_pin6, _7408_12_pin8,
       _7408_12_pin11, _7408_13_pin3, _7408_13_pin6, _7408_13_pin8, _7408_13_pin11, _74367_1_y1, _74367_1_y2,
       _74367_1_y3, _74367_1_y4, _74367_1_y5, _74367_1_y6, _74367_2_y1, _74367_2_y2, _74367_2_y3,
       _74367_2_y4, _74367_2_y5, _74367_2_y6, _74367_3_y1, _74367_3_y2, _74367_3_y3, _74367_3_y4,
       _74367_3_y5, _74367_3_y6, _74367_4_y1, _74367_4_y2, _74367_4_y3, _74367_4_y4, _74367_4_y5,
       _74367_4_y6, _74367_5_y1, _74367_5_y2, _74367_5_y3, _74367_5_y4, _74367_5_y5, _74367_5_y6,
       _74367_6_y1, _74367_6_y2, _74367_6_y3, _74367_6_y4, _74367_6_y5, _74367_6_y6;

  Seven_Seg_Hex seven_seg_hex_1 (.d({2'b00, A5, A4}), .dp(1'b0));
  Seven_Seg_Hex seven_seg_hex_2 (.d({A3, A2, A1, A0}), .dp(1'b0));
  Seven_Seg_Hex seven_seg_hex_3 (.d({P15, P14, P13, P12}), .dp(1'b0));
  Seven_Seg_Hex seven_seg_hex_4 (.d({2'b00, B9, B8}), .dp(1'b0));
  Seven_Seg_Hex seven_seg_hex_5 (.d({P11, P10, P9, P8}), .dp(1'b0));
  Seven_Seg_Hex seven_seg_hex_6 (.d({B7, B6, B5, B4}), .dp(1'b0));
  Seven_Seg_Hex seven_seg_hex_7 (.d({P7, P6, P5, P4}), .dp(1'b0));
  Seven_Seg_Hex seven_seg_hex_8 (.d({B3, B2, B1, B0}), .dp(1'b0));
  Seven_Seg_Hex seven_seg_hex_9 (.d({P3, P2, P1, P0}), .dp(1'b0));
  _7408 _7408_1 (
    .pin1(A0), .pin2(B0), .pin3(_7408_1_pin3), .pin4(A0), .pin5(B1), .pin6(_7408_1_pin6), .pin7(1'b0),
    .pin8(_7408_1_pin8), .pin9(A0), .pin10(B2), .pin11(_7408_1_pin11), .pin12(A0), .pin13(B3), .pin14(1'b1));
  _7408 _7408_2 (
    .pin1(A0), .pin2(B4), .pin3(_7408_2_pin3), .pin4(A0), .pin5(B5), .pin6(_7408_2_pin6), .pin7(1'b0),
    .pin8(_7408_2_pin8), .pin9(A0), .pin10(B6), .pin11(_7408_2_pin11), .pin12(A0), .pin13(B7), .pin14(1'b1));
  _7408 _7408_3 (
    .pin1(A0), .pin2(B8), .pin3(_7408_3_pin3), .pin4(A0), .pin5(B9), .pin6(_7408_3_pin6), .pin7(1'b0),
    .pin8(_7408_3_pin8), .pin9(A1), .pin10(B0), .pin11(_7408_3_pin11), .pin12(A1), .pin13(B1), .pin14(1'b1));
  _74283 _0_3 (
    .pin1(_0_3_pin1), .pin2(_7408_3_pin8), .pin3(_7408_1_pin6), .pin4(_0_3_pin4), .pin5(_7408_1_pin3),
    .pin6(1'b0), .pin7(1'b0), .pin8(1'b0), .pin9(_0_3_pin9), .pin10(_0_3_pin10), .pin11(_0_3_pin11),
    .pin12(_7408_1_pin11), .pin13(_0_3_pin13), .pin14(_7408_1_pin8), .pin15(_7408_3_pin11), .pin16(1'b1));
  _74283 _4_7 (
    .pin1(_4_7_pin1), .pin2(_4_7_pin2), .pin3(_7408_2_pin6), .pin4(_4_7_pin4), .pin5(_7408_2_pin3),
    .pin6(_4_7_pin6), .pin7(_0_3_pin9), .pin8(1'b0), .pin9(_4_7_pin9), .pin10(_4_7_pin10),
    .pin11(_4_7_pin11), .pin12(_7408_2_pin11), .pin13(_4_7_pin13), .pin14(_7408_2_pin8), .pin15(_4_7_pin15),
    .pin16(1'b1));
  LED L1 (.in(_0_3_pin9));
  _74283 _8_11 (
    .pin1(_8_11_pin1), .pin2(_8_11_pin2), .pin3(_7408_3_pin6), .pin4(_8_11_pin4), .pin5(_7408_3_pin3),
    .pin6(_8_11_pin6), .pin7(_4_7_pin9), .pin8(1'b0), .pin10(_8_11_pin10), .pin11(1'b0), .pin12(1'b0),
    .pin13(_8_11_pin13), .pin14(1'b0), .pin15(_8_11_pin15), .pin16(1'b1));  // open: pin9
  LED L2 (.in(_4_7_pin9));
  _7408 _7408_4 (
    .pin1(A1), .pin2(B2), .pin3(_0_3_pin11), .pin4(A1), .pin5(B3), .pin6(_4_7_pin6), .pin7(1'b0),
    .pin8(_4_7_pin2), .pin9(A1), .pin10(B4), .pin11(_4_7_pin15), .pin12(A1), .pin13(B5), .pin14(1'b1));
  LED U13 (.in(_12_15_pin1));
  LED U11 (.in(_8_11_2_pin10));
  LED U12 (.in(_12_15_pin4));
  LED U9 (.in(_8_11_2_pin1));
  LED U10 (.in(_8_11_2_pin13));
  LED U7 (.in(_4_7_2_pin10));
  LED U8 (.in(_8_11_2_pin4));
  LED U5 (.in(_4_7_2_pin1));
  LED U6 (.in(_4_7_2_pin13));
  _7408 _7408_5 (
    .pin1(A1), .pin2(B6), .pin3(_4_7_pin11), .pin4(A1), .pin5(B7), .pin6(_8_11_pin6), .pin7(1'b0),
    .pin8(_8_11_pin2), .pin9(A1), .pin10(B8), .pin11(_8_11_pin15), .pin12(A1), .pin13(B9), .pin14(1'b1));
  LED U3 (.in(P3));
  LED U4 (.in(_4_7_2_pin4));
  LED U1 (.in(P1));
  LED U2 (.in(P2));
  LED U0 (.in(P0));
  _74367 _74367_1 (
    .nG1(1'b0), .nG2(1'b0), .A1(_8_11_pin10), .Y1(_74367_1_y1), .A2(_8_11_pin13), .Y2(_74367_1_y2),
    .A3(_8_11_pin1), .Y3(_74367_1_y3), .A4(_8_11_pin4), .Y4(_74367_1_y4), .A5(_4_7_pin10), .Y5(_74367_1_y5),
    .A6(_4_7_pin13), .Y6(_74367_1_y6), .VCC(1'b1), .GND(1'b0));
  LED R11 (.in(_74367_1_y1));
  LED R9 (.in(_74367_1_y3));
  LED R10 (.in(_74367_1_y2));
  _7408 _7408_6 (
    .pin1(A2), .pin2(B0), .pin3(_7408_6_pin3), .pin4(A2), .pin5(B1), .pin6(_7408_6_pin6), .pin7(1'b0),
    .pin8(_7408_6_pin8), .pin9(A2), .pin10(B2), .pin11(_7408_6_pin11), .pin12(A2), .pin13(B3), .pin14(1'b1));
  LED R7 (.in(_74367_1_y5));
  LED R8 (.in(_74367_1_y4));
  LED R5 (.in(_74367_2_y1));
  LED R6 (.in(_74367_1_y6));
  LED R3 (.in(_74367_2_y3));
  LED R4 (.in(_74367_2_y2));
  _74367 _74367_2 (
    .nG1(1'b0), .nG2(1'b0), .A1(_4_7_pin1), .Y1(_74367_2_y1), .A2(_4_7_pin4), .Y2(_74367_2_y2),
    .A3(_0_3_pin10), .Y3(_74367_2_y3), .A4(_0_3_pin13), .Y4(_74367_2_y4), .A5(_0_3_pin1), .Y5(_74367_2_y5),
    .A6(_0_3_pin4), .Y6(_74367_2_y6), .VCC(1'b1), .GND(1'b0));
  LED R1 (.in(_74367_2_y5));
  LED R2 (.in(_74367_2_y4));
  _74283 _0_3_2 (
    .pin1(P1), .pin2(1'b0), .pin3(_0_3_pin1), .pin4(P0), .pin5(_0_3_pin4), .pin6(1'b0), .pin7(1'b0),
    .pin8(1'b0), .pin9(_0_3_2_pin9), .pin10(P3), .pin11(_0_3_2_pin11), .pin12(_0_3_pin10), .pin13(P2),
    .pin14(_0_3_pin13), .pin15(_0_3_2_pin15), .pin16(1'b1));
  _74283 _4_7_2 (
    .pin1(_4_7_2_pin1), .pin2(_4_7_2_pin2), .pin3(_4_7_pin1), .pin4(_4_7_2_pin4), .pin5(_4_7_pin4),
    .pin6(_4_7_2_pin6), .pin7(_0_3_2_pin9), .pin8(1'b0), .pin9(_4_7_2_pin9), .pin10(_4_7_2_pin10),
    .pin11(_4_7_2_pin11), .pin12(_4_7_pin10), .pin13(_4_7_2_pin13), .pin14(_4_7_pin13), .pin15(_4_7_2_pin15),
    .pin16(1'b1));
  LED R0 (.in(_74367_2_y6));
  _74283 _8_11_2 (
    .pin1(_8_11_2_pin1), .pin2(_8_11_2_pin2), .pin3(_8_11_pin1), .pin4(_8_11_2_pin4), .pin5(_8_11_pin4),
    .pin6(_8_11_2_pin6), .pin7(_4_7_2_pin9), .pin8(1'b0), .pin9(_8_11_2_pin9), .pin10(_8_11_2_pin10),
    .pin11(_8_11_2_pin11), .pin12(_8_11_pin10), .pin13(_8_11_2_pin13), .pin14(_8_11_pin13),
    .pin15(_8_11_2_pin15), .pin16(1'b1));
  _7408 _7408_7 (
    .pin1(A2), .pin2(B4), .pin3(_7408_7_pin3), .pin4(A2), .pin5(B5), .pin6(_7408_7_pin6), .pin7(1'b0),
    .pin8(_7408_7_pin8), .pin9(A2), .pin10(B6), .pin11(_7408_7_pin11), .pin12(A2), .pin13(B7), .pin14(1'b1));
  LED L8 (.in(_0_3_2_pin9));
  LED L9 (.in(_4_7_2_pin9));
  LED L10 (.in(_8_11_2_pin9));
  _74283 _12_15 (
    .pin1(_12_15_pin1), .pin2(_12_15_pin2), .pin3(1'b0), .pin4(_12_15_pin4), .pin5(1'b0), .pin6(_12_15_pin6),
    .pin7(_8_11_2_pin9), .pin8(1'b0), .pin11(1'b0), .pin12(1'b0), .pin14(1'b0), .pin15(1'b0), .pin16(1'b1));  // open: pin9, pin10, pin13
  _74283 _0_3_3 (
    .pin2(1'b0), .pin3(1'b0), .pin5(1'b0), .pin6(1'b0), .pin7(1'b0), .pin8(1'b0), .pin9(_0_3_3_pin9),
    .pin10(_0_3_2_pin11), .pin11(_0_3_3_pin11), .pin12(_7408_6_pin6), .pin13(_0_3_2_pin15),
    .pin14(_7408_6_pin3), .pin15(1'b0), .pin16(1'b1));  // open: pin1, pin4
  _7408 _7408_8 (
    .pin1(A2), .pin2(B8), .pin3(_7408_8_pin3), .pin4(A2), .pin5(B9), .pin6(_7408_8_pin6), .pin7(1'b0),
    .pin8(_0_3_3_pin11), .pin9(A3), .pin10(B0), .pin11(_7408_8_pin11), .pin12(A3), .pin13(B1), .pin14(1'b1));
  LED L3 (.in(_0_3_3_pin9));
  _74283 _4_7_3 (
    .pin1(_4_7_2_pin2), .pin2(_4_7_3_pin2), .pin3(_7408_6_pin11), .pin4(_4_7_2_pin6), .pin5(_7408_6_pin8),
    .pin6(_7408_8_pin11), .pin7(_0_3_3_pin9), .pin8(1'b0), .pin9(_4_7_3_pin9), .pin10(_4_7_2_pin11),
    .pin11(_4_7_3_pin11), .pin12(_7408_7_pin6), .pin13(_4_7_2_pin15), .pin14(_7408_7_pin3),
    .pin15(_4_7_3_pin15), .pin16(1'b1));
  _74283 _8_11_3 (
    .pin1(_8_11_2_pin2), .pin2(_8_11_3_pin2), .pin3(_7408_7_pin11), .pin4(_8_11_2_pin6), .pin5(_7408_7_pin8),
    .pin6(_8_11_3_pin6), .pin7(_4_7_3_pin9), .pin8(1'b0), .pin9(_8_11_3_pin9), .pin10(_8_11_2_pin11),
    .pin11(_8_11_3_pin11), .pin12(_7408_8_pin6), .pin13(_8_11_2_pin15), .pin14(_7408_8_pin3),
    .pin15(_8_11_3_pin15), .pin16(1'b1));
  _74283 _12_15_2 (
    .pin1(_12_15_pin2), .pin2(1'b0), .pin3(1'b0), .pin4(_12_15_pin6), .pin5(1'b0), .pin6(_12_15_2_pin6),
    .pin7(_8_11_3_pin9), .pin8(1'b0), .pin11(1'b0), .pin12(1'b0), .pin14(1'b0), .pin15(1'b0), .pin16(1'b1));  // open: pin9, pin10, pin13
  LED L4 (.in(_4_7_3_pin9));
  LED L5 (.in(_8_11_3_pin9));
  _7408 _7408_9 (
    .pin1(A3), .pin2(B2), .pin3(_4_7_3_pin2), .pin4(A3), .pin5(B3), .pin6(_4_7_3_pin15), .pin7(1'b0),
    .pin8(_4_7_3_pin11), .pin9(A3), .pin10(B4), .pin11(_8_11_3_pin6), .pin12(A3), .pin13(B5), .pin14(1'b1));
  _7408 _7408_10 (
    .pin1(A3), .pin2(B6), .pin3(_8_11_3_pin2), .pin4(A3), .pin5(B7), .pin6(_8_11_3_pin15), .pin7(1'b0),
    .pin8(_8_11_3_pin11), .pin9(A3), .pin10(B8), .pin11(_12_15_2_pin6), .pin12(A3), .pin13(B9), .pin14(1'b1));
  _74367 _74367_3 (
    .nG1(1'b0), .nG2(1'b0), .A1(_12_15_pin2), .Y1(_74367_3_y1), .A2(_12_15_pin6), .Y2(_74367_3_y2),
    .A3(_8_11_2_pin11), .Y3(_74367_3_y3), .A4(_8_11_2_pin15), .Y4(_74367_3_y4), .A5(_8_11_2_pin2),
    .Y5(_74367_3_y5), .A6(_8_11_2_pin6), .Y6(_74367_3_y6), .VCC(1'b1), .GND(1'b0));
  _7408 _7408_11 (
    .pin1(A4), .pin2(B0), .pin3(_7408_11_pin3), .pin4(A4), .pin5(B1), .pin6(_7408_11_pin6), .pin7(1'b0),
    .pin8(_7408_11_pin8), .pin9(A4), .pin10(B2), .pin11(_7408_11_pin11), .pin12(A4), .pin13(B3), .pin14(1'b1));
  LED S12 (.in(_74367_3_y2));
  LED S13 (.in(_74367_3_y1));
  LED S10 (.in(_74367_3_y4));
  LED S11 (.in(_74367_3_y3));
  LED S0 (.in(_74367_3_y5));
  LED S8 (.in(_74367_3_y6));
  LED S9 (.in(_74367_3_y5));
  LED S6 (.in(_74367_4_y2));
  LED S7 (.in(_74367_4_y1));
  _74367 _74367_4 (
    .nG1(1'b0), .nG2(1'b0), .A1(_4_7_2_pin11), .Y1(_74367_4_y1), .A2(_4_7_2_pin15), .Y2(_74367_4_y2),
    .A3(_4_7_2_pin2), .Y3(_74367_4_y3), .A4(_4_7_2_pin6), .Y4(_74367_4_y4), .A5(_0_3_2_pin11),
    .Y5(_74367_4_y5), .A6(_0_3_2_pin15), .Y6(_74367_4_y6), .VCC(1'b1), .GND(1'b0));
  LED S4 (.in(_74367_4_y4));
  LED S5 (.in(_74367_4_y3));
  LED S2 (.in(_74367_4_y6));
  LED S3 (.in(_74367_4_y5));
  _7408 _7408_12 (
    .pin1(A4), .pin2(B4), .pin3(_7408_12_pin3), .pin4(A4), .pin5(B5), .pin6(_7408_12_pin6), .pin7(1'b0),
    .pin8(_7408_12_pin8), .pin9(A4), .pin10(B6), .pin11(_7408_12_pin11), .pin12(A4), .pin13(B7), .pin14(1'b1));
  _7408 _7408_13 (
    .pin1(A4), .pin2(B8), .pin3(_7408_13_pin3), .pin4(A4), .pin5(B9), .pin6(_7408_13_pin6), .pin7(1'b0),
    .pin8(_7408_13_pin8), .pin9(A5), .pin10(B0), .pin11(_7408_13_pin11), .pin12(A5), .pin13(B1), .pin14(1'b1));
  _74283 _4_7_4 (
    .pin1(_4_7_4_pin1), .pin2(_7408_13_pin8), .pin3(_7408_11_pin6), .pin4(_4_7_4_pin4), .pin5(_7408_11_pin3),
    .pin6(1'b0), .pin7(1'b0), .pin8(1'b0), .pin9(_4_7_4_pin9), .pin10(_4_7_4_pin10), .pin11(_4_7_4_pin11),
    .pin12(_7408_11_pin11), .pin13(_4_7_4_pin13), .pin14(_7408_11_pin8), .pin15(_7408_13_pin11), .pin16(1'b1));
  _74283 _8_11_4 (
    .pin1(_8_11_4_pin1), .pin2(_8_11_4_pin2), .pin3(_7408_12_pin6), .pin4(_8_11_4_pin4),
    .pin5(_7408_12_pin3), .pin6(_8_11_4_pin6), .pin7(_4_7_4_pin9), .pin8(1'b0), .pin9(_8_11_4_pin9),
    .pin10(_8_11_4_pin10), .pin11(_8_11_4_pin11), .pin12(_7408_12_pin11), .pin13(_8_11_4_pin13),
    .pin14(_7408_12_pin8), .pin15(_8_11_4_pin15), .pin16(1'b1));
  _74283 _12_15_3 (
    .pin1(_12_15_3_pin1), .pin2(_12_15_3_pin2), .pin3(_7408_13_pin6), .pin4(_12_15_3_pin4),
    .pin5(_7408_13_pin3), .pin6(_12_15_3_pin6), .pin7(_8_11_4_pin9), .pin8(1'b0), .pin10(_12_15_3_pin10),
    .pin11(1'b0), .pin12(1'b0), .pin13(_12_15_3_pin13), .pin14(1'b0), .pin15(_12_15_3_pin15), .pin16(1'b1));  // open: pin9
  _74283 _4_7_5 (
    .pin1(P5), .pin2(_4_7_4_pin1), .pin3(_4_7_2_pin1), .pin4(P4), .pin5(_4_7_2_pin4), .pin6(_4_7_4_pin4),
    .pin7(1'b0), .pin8(1'b0), .pin9(_4_7_5_pin9), .pin10(P7), .pin11(_4_7_4_pin10), .pin12(_4_7_2_pin10),
    .pin13(P6), .pin14(_4_7_2_pin13), .pin15(_4_7_4_pin13), .pin16(1'b1));
  _74283 _8_11_5 (
    .pin1(P9), .pin2(_8_11_4_pin1), .pin3(_8_11_2_pin1), .pin4(P8), .pin5(_8_11_2_pin4), .pin6(_8_11_4_pin4),
    .pin7(_4_7_5_pin9), .pin8(1'b0), .pin9(_8_11_5_pin9), .pin10(P11), .pin11(_8_11_4_pin10),
    .pin12(_8_11_2_pin10), .pin13(P10), .pin14(_8_11_2_pin13), .pin15(_8_11_4_pin13), .pin16(1'b1));
  LED L6 (.in(_4_7_4_pin9));
  LED L7 (.in(_8_11_4_pin9));
  _7408 _7408_14 (
    .pin1(A5), .pin2(B2), .pin3(_4_7_4_pin11), .pin4(A5), .pin5(B3), .pin6(_8_11_4_pin6), .pin7(1'b0),
    .pin8(_8_11_4_pin2), .pin9(A5), .pin10(B4), .pin11(_8_11_4_pin15), .pin12(A5), .pin13(B5), .pin14(1'b1));
  LED L11 (.in(_4_7_5_pin9));
  LED L12 (.in(_8_11_5_pin9));
  _74283 _12_15_4 (
    .pin1(P13), .pin2(_12_15_3_pin1), .pin3(_12_15_pin1), .pin4(P12), .pin5(_12_15_pin4),
    .pin6(_12_15_3_pin4), .pin7(_8_11_5_pin9), .pin8(1'b0), .pin10(P15), .pin11(_12_15_3_pin10),
    .pin12(1'b0), .pin13(P14), .pin14(1'b0), .pin15(_12_15_3_pin13), .pin16(1'b1));  // open: pin9
  _7408 _7408_15 (
    .pin1(A5), .pin2(B6), .pin3(_8_11_4_pin11), .pin4(A5), .pin5(B7), .pin6(_12_15_3_pin6), .pin7(1'b0),
    .pin8(_12_15_3_pin2), .pin9(A5), .pin10(B8), .pin11(_12_15_3_pin15), .pin12(A5), .pin13(B9), .pin14(1'b1));
  _74367 _74367_5 (
    .nG1(1'b0), .nG2(1'b0), .A1(_12_15_3_pin10), .Y1(_74367_5_y1), .A2(_12_15_3_pin13), .Y2(_74367_5_y2),
    .A3(_12_15_3_pin1), .Y3(_74367_5_y3), .A4(_12_15_3_pin4), .Y4(_74367_5_y4), .A5(_8_11_4_pin10),
    .Y5(_74367_5_y5), .A6(_8_11_4_pin13), .Y6(_74367_5_y6), .VCC(1'b1), .GND(1'b0));
  LED T14 (.in(_74367_5_y2));
  LED T15 (.in(_74367_5_y1));
  LED T12 (.in(_74367_5_y4));
  LED T13 (.in(_74367_5_y3));
  LED T10 (.in(_74367_5_y6));
  LED T11 (.in(_74367_5_y5));
  LED T8 (.in(_74367_6_y2));
  LED T9 (.in(_74367_6_y1));
  _74367 _74367_6 (
    .nG1(1'b0), .nG2(1'b0), .A1(_8_11_4_pin1), .Y1(_74367_6_y1), .A2(_8_11_4_pin4), .Y2(_74367_6_y2),
    .A3(_4_7_4_pin10), .Y3(_74367_6_y3), .A4(_4_7_4_pin13), .Y4(_74367_6_y4), .A5(_4_7_4_pin1),
    .Y5(_74367_6_y5), .A6(_4_7_4_pin4), .Y6(_74367_6_y6), .VCC(1'b1), .GND(1'b0));
  LED T6 (.in(_74367_6_y4));
  LED T7 (.in(_74367_6_y3));
  LED T4 (.in(_74367_6_y6));
  LED T5 (.in(_74367_6_y5));

  // Notes on the sheet:
  //   A0: default 1
  //   A1: default 1
  //   A2: default 1
  //   A3: default 1
  //   A4: default 1
  //   A5: default 1
  //   B0: default 1
  //   B1: default 1
  //   B2: default 1
  //   B3: default 1
  //   B4: default 1
  //   B5: default 1
  //   B6: default 1
  //   B7: default 1
  //   B8: default 1
  //   B9: default 1
  //   LSB
  //   6 x 10 bit multiply version K 19 feb 2022.dig
  //   A
  //   A x B
  //   B
  //   A0 partial product
  //   PP0 + PP1 = R
  //   U = R + S
  //   A1 partial product
  //   R = PP0 + PP1
  //   R + S = U
  //   A2 partial product
  //   PP2 + PP3 = S
  //   A3 partial product
  //   S = PP2 + PP3
  //   A4 partial product
  //   PP4 + PP5 = T
  //   U + T
  //   A5 partial product
  //   T = PP4 + PP5
endmodule
